// Digital circuit alu-16b-final.dig as structural Verilog
module alu_16b_final (
  input  CLK,
  input  [15:0] A,
  input  [15:0] B,
  input  [15:0] C,
  input  cin,
  input  [15:0] Test,
  input  RST,
  input  hold,
  output [7:0] lutB,
  output [7:0] lutA,
  output [15:0] Out
);

  wire aeff31, and_1_out, beff31, clk_t, counter_1_ovf, COUT, cout0, cout1, cout2, en, final0, final1,
       final2, final3, final4, final5, final6, final7, final8, final9, final10, final11, final12, final13,
       final14, final15, found, not_1_out, not_2_out, ovf, sum31, x0, x1, x2, x3, x4, x5, x6, x7, y0, y1, y2,
       y3, z0, z1;
  wire [7:0] lutAin, lutBin;

  _7486 _7486_1 (
    .pin1(Out[0]), .pin2(Test[0]), .pin3(final0), .pin4(Out[1]), .pin5(Test[1]), .pin6(final1), .pin7(1'b0),
    .pin8(final2), .pin9(Out[2]), .pin10(Test[2]), .pin11(final3), .pin12(Out[3]), .pin13(Test[3]),
    .pin14(1'b1));
  _7486 _7486_2 (
    .pin1(Out[8]), .pin2(Test[8]), .pin3(final8), .pin4(Out[9]), .pin5(Test[9]), .pin6(final9), .pin7(1'b0),
    .pin8(final10), .pin9(Out[10]), .pin10(Test[10]), .pin11(final11), .pin12(Out[11]), .pin13(Test[11]),
    .pin14(1'b1));
  _7432 _7432_1 (
    .pin1(final8), .pin2(final9), .pin3(x4), .pin4(final10), .pin5(final11), .pin6(x5), .pin7(1'b0),
    .pin8(x6), .pin9(final12), .pin10(final13), .pin11(x7), .pin12(final14), .pin13(final15), .pin14(1'b1));
  _7432 _7432_2 (
    .pin1(x0), .pin2(x1), .pin3(y0), .pin4(x2), .pin5(x3), .pin6(y1), .pin7(1'b0), .pin8(y2), .pin9(x4),
    .pin10(x5), .pin11(y3), .pin12(x6), .pin13(x7), .pin14(1'b1));
  _7432 _7432_3 (
    .pin1(final0), .pin2(final1), .pin3(x0), .pin4(final2), .pin5(final3), .pin6(x1), .pin7(1'b0), .pin8(x2),
    .pin9(final4), .pin10(final5), .pin11(x3), .pin12(final6), .pin13(final7), .pin14(1'b1));
  _7432 _7432_4 (
    .pin1(y0), .pin2(y1), .pin3(z0), .pin4(y2), .pin5(y3), .pin6(z1), .pin7(1'b0), .pin8(found), .pin9(z0),
    .pin10(z1), .pin12(1'b0), .pin13(1'b0), .pin14(1'b1));  // open: pin11
  _7486 _7486_3 (
    .pin1(Out[4]), .pin2(Test[4]), .pin3(final4), .pin4(Out[5]), .pin5(Test[5]), .pin6(final5), .pin7(1'b0),
    .pin8(final6), .pin9(Out[6]), .pin10(Test[6]), .pin11(final7), .pin12(Out[7]), .pin13(Test[7]),
    .pin14(1'b1));
  _7486 _7486_4 (
    .pin1(Out[12]), .pin2(Test[12]), .pin3(final12), .pin4(Out[13]), .pin5(Test[13]), .pin6(final13),
    .pin7(1'b0), .pin8(final14), .pin9(Out[14]), .pin10(Test[14]), .pin11(final15), .pin12(Out[15]),
    .pin13(Test[15]), .pin14(1'b1));
  not not_1 (not_1_out, ovf);
  and and_1 (and_1_out, not_1_out, found);
  or or_1 (en, and_1_out, RST);
  not not_2 (not_2_out, hold);
  Counter #(.Bits(8)) counter_1 (.en(found), .C(clk_t), .clr(RST), .out(lutAin), .ovf(counter_1_ovf));
  and and_2 (clk_t, CLK, en, not_2_out);
  Counter #(.Bits(8)) counter_2 (.en(counter_1_ovf), .C(clk_t), .clr(RST), .out(lutBin), .ovf(ovf));
  Register #(.Bits(8)) register_1 (.D(lutAin), .C(clk_t), .en(en), .Q(lutA));
  Register #(.Bits(8)) register_2 (.D(lutBin), .C(clk_t), .en(en), .Q(lutB));
  alu_4b_final alu_4b_final_1 (
    .A(A[3:0]), .B(B[3:0]), .lutA(lutA), .C(C[3:0]), .cin(cin), .lutB(lutB), .Out(Out[3:0]), .cout(cout0));  // open: sum3, aeff3, beff3
  alu_4b_final alu_4b_final_2 (
    .A(A[11:8]), .B(B[11:8]), .lutA(lutA), .C(C[11:8]), .cin(cout1), .lutB(lutB), .Out(Out[11:8]),
    .cout(cout2));  // open: sum3, aeff3, beff3
  alu_4b_final alu_4b_final_3 (
    .A(A[7:4]), .B(B[7:4]), .lutA(lutA), .C(C[7:4]), .cin(cout0), .lutB(lutB), .Out(Out[7:4]), .cout(cout1));  // open: sum3, aeff3, beff3
  alu_4b_final alu_4b_final_4 (
    .A(A[15:12]), .B(B[15:12]), .lutA(lutA), .C(C[15:12]), .cin(cout2), .lutB(lutB), .Out(Out[15:12]),
    .cout(COUT), .sum3(sum31), .aeff3(aeff31), .beff3(beff31));

  // Other names for the same wires on the sheet: a4[3:0] = A[3:0]; a8[3:0] = A[7:4]; a12[3:0] = A[11:8];
  //   a16[3:0] = A[15:12]; b4[3:0] = B[3:0]; b8[3:0] = B[7:4]; b12[3:0] = B[11:8]; b16[3:0] = B[15:12];
  //   c4[3:0] = C[3:0]; c8[3:0] = C[7:4]; c12[3:0] = C[11:8]; c16[3:0] = C[15:12]; OUT4[3:0] = Out[3:0];
  //   out4_t = Out[4]; OUT8[3:0] = Out[7:4]; out8_t = Out[8]; OUT12[3:0] = Out[11:8]; out12_t = Out[12];
  //   OUT16[3:0] = Out[15:12]

  // Notes on the sheet:
  //   CLK: Hz: 100000
  //   A: default 10811
  //   B: default 7245
  //   C: default 20318
  //   Test: default 4112
endmodule
