// Digital circuit alu-1b-final.dig as structural Verilog
module alu_1b_final (
  input  [7:0] OPCODE,
  input  A,
  input  B,
  input  C,
  output MUX_OUT
);

  Multiplexer #(.Selector_Bits(3)) multiplexer_1 (
    .sel({C, B, A}), .in_0(OPCODE[0]), .in_1(OPCODE[1]), .in_2(OPCODE[2]), .in_3(OPCODE[3]),
    .in_4(OPCODE[4]), .in_5(OPCODE[5]), .in_6(OPCODE[6]), .in_7(OPCODE[7]), .out(MUX_OUT));
endmodule

/* Test case Arithmetic Tests:
# Arithmetic Tests (OPCODE 0x96)
OPCODE Asel A_inv Bsel B_inv A B C MUX_OUT P G
150 0 0 0 0 0 0 0 0 0 0
150 0 0 0 0 0 1 0 0 0 0
150 0 0 0 0 1 0 0 0 0 0
150 0 0 0 0 1 1 0 0 0 0
150 0 0 0 0 0 0 1 1 0 0
150 0 0 0 0 0 1 1 1 0 0
150 0 0 0 0 1 0 1 1 0 0
150 0 0 0 0 1 1 1 1 0 0
150 0 0 0 1 0 0 0 1 1 0
150 0 0 0 1 0 1 0 1 1 0
150 0 0 0 1 1 0 0 1 1 0
150 0 0 0 1 1 1 0 1 1 0
150 0 0 0 1 0 0 1 0 1 0
150 0 0 0 1 0 1 1 0 1 0
150 0 0 0 1 1 0 1 0 1 0
150 0 0 0 1 1 1 1 0 1 0
150 0 0 1 0 0 0 0 0 0 0
150 0 0 1 0 0 1 0 1 1 0
150 0 0 1 0 1 0 0 0 0 0
150 0 0 1 0 1 1 0 1 1 0
150 0 0 1 0 0 0 1 1 0 0
150 0 0 1 0 0 1 1 0 1 0
150 0 0 1 0 1 0 1 1 0 0
150 0 0 1 0 1 1 1 0 1 0
150 0 0 1 1 0 0 0 1 1 0
150 0 0 1 1 0 1 0 0 0 0
150 0 0 1 1 1 0 0 1 1 0
150 0 0 1 1 1 1 0 0 0 0
150 0 0 1 1 0 0 1 0 1 0
150 0 0 1 1 0 1 1 1 0 0
150 0 0 1 1 1 0 1 0 1 0
150 0 0 1 1 1 1 1 1 0 0
150 0 1 0 0 0 0 0 1 1 0
150 0 1 0 0 0 1 0 1 1 0
150 0 1 0 0 1 0 0 1 1 0
150 0 1 0 0 1 1 0 1 1 0
150 0 1 0 0 0 0 1 0 1 0
150 0 1 0 0 0 1 1 0 1 0
150 0 1 0 0 1 0 1 0 1 0
150 0 1 0 0 1 1 1 0 1 0
150 0 1 0 1 0 0 0 0 0 1
150 0 1 0 1 0 1 0 0 0 1
150 0 1 0 1 1 0 0 0 0 1
150 0 1 0 1 1 1 0 0 0 1
150 0 1 0 1 0 0 1 1 0 1
150 0 1 0 1 0 1 1 1 0 1
150 0 1 0 1 1 0 1 1 0 1
150 0 1 0 1 1 1 1 1 0 1
150 0 1 1 0 0 0 0 1 1 0
150 0 1 1 0 0 1 0 0 0 1
150 0 1 1 0 1 0 0 1 1 0
150 0 1 1 0 1 1 0 0 0 1
150 0 1 1 0 0 0 1 0 1 0
150 0 1 1 0 0 1 1 1 0 1
150 0 1 1 0 1 0 1 0 1 0
150 0 1 1 0 1 1 1 1 0 1
150 0 1 1 1 0 0 0 0 0 1
150 0 1 1 1 0 1 0 1 1 0
150 0 1 1 1 1 0 0 0 0 1
150 0 1 1 1 1 1 0 1 1 0
150 0 1 1 1 0 0 1 1 0 1
150 0 1 1 1 0 1 1 0 1 0
150 0 1 1 1 1 0 1 1 0 1
150 0 1 1 1 1 1 1 0 1 0
150 1 0 0 0 0 0 0 0 0 0
150 1 0 0 0 0 1 0 0 0 0
150 1 0 0 0 1 0 0 1 1 0
150 1 0 0 0 1 1 0 1 1 0
150 1 0 0 0 0 0 1 1 0 0
150 1 0 0 0 0 1 1 1 0 0
150 1 0 0 0 1 0 1 0 1 0
150 1 0 0 0 1 1 1 0 1 0
150 1 0 0 1 0 0 0 1 1 0
150 1 0 0 1 0 1 0 1 1 0
150 1 0 0 1 1 0 0 0 0 1
150 1 0 0 1 1 1 0 0 0 1
150 1 0 0 1 0 0 1 0 1 0
150 1 0 0 1 0 1 1 0 1 0
150 1 0 0 1 1 0 1 1 0 1
150 1 0 0 1 1 1 1 1 0 1
150 1 0 1 0 0 0 0 0 0 0
150 1 0 1 0 0 1 0 1 1 0
150 1 0 1 0 1 0 0 1 1 0
150 1 0 1 0 1 1 0 0 0 1
150 1 0 1 0 0 0 1 1 0 0
150 1 0 1 0 0 1 1 0 1 0
150 1 0 1 0 1 0 1 0 1 0
150 1 0 1 0 1 1 1 1 0 1
150 1 0 1 1 0 0 0 1 1 0
150 1 0 1 1 0 1 0 0 0 0
150 1 0 1 1 1 0 0 0 0 1
150 1 0 1 1 1 1 0 1 1 0
150 1 0 1 1 0 0 1 0 1 0
150 1 0 1 1 0 1 1 1 0 0
150 1 0 1 1 1 0 1 1 0 1
150 1 0 1 1 1 1 1 0 1 0
150 1 1 0 0 0 0 0 1 1 0
150 1 1 0 0 0 1 0 1 1 0
150 1 1 0 0 1 0 0 0 0 0
150 1 1 0 0 1 1 0 0 0 0
150 1 1 0 0 0 0 1 0 1 0
150 1 1 0 0 0 1 1 0 1 0
150 1 1 0 0 1 0 1 1 0 0
150 1 1 0 0 1 1 1 1 0 0
150 1 1 0 1 0 0 0 0 0 1
150 1 1 0 1 0 1 0 0 0 1
150 1 1 0 1 1 0 0 1 1 0
150 1 1 0 1 1 1 0 1 1 0
150 1 1 0 1 0 0 1 1 0 1
150 1 1 0 1 0 1 1 1 0 1
150 1 1 0 1 1 0 1 0 1 0
150 1 1 0 1 1 1 1 0 1 0
150 1 1 1 0 0 0 0 1 1 0
150 1 1 1 0 0 1 0 0 0 1
150 1 1 1 0 1 0 0 0 0 0
150 1 1 1 0 1 1 0 1 1 0
150 1 1 1 0 0 0 1 0 1 0
150 1 1 1 0 0 1 1 1 0 1
150 1 1 1 0 1 0 1 1 0 0
150 1 1 1 0 1 1 1 0 1 0
150 1 1 1 1 0 0 0 0 0 1
150 1 1 1 1 0 1 0 1 1 0
150 1 1 1 1 1 0 0 1 1 0
150 1 1 1 1 1 1 0 0 0 0
150 1 1 1 1 0 0 1 1 0 1
150 1 1 1 1 0 1 1 0 1 0
150 1 1 1 1 1 0 1 0 1 0
150 1 1 1 1 1 1 1 1 0 0
            
*/

/* Test case Logic Tests:
# Logic Tests (All 256 OpCodes)
OPCODE Asel A_inv Bsel B_inv A B C MUX_OUT P G
0 1 0 1 0 0 0 0 0 0 0
0 1 0 1 0 0 0 1 0 0 0
0 1 0 1 0 0 1 0 0 0 0
0 1 0 1 0 0 1 1 0 0 0
0 1 0 1 0 1 0 0 0 0 0
0 1 0 1 0 1 0 1 0 0 0
0 1 0 1 0 1 1 0 0 0 1
0 1 0 1 0 1 1 1 0 0 1
1 1 0 1 0 0 0 0 1 1 0
1 1 0 1 0 0 0 1 0 1 0
1 1 0 1 0 0 1 0 0 0 0
1 1 0 1 0 0 1 1 0 0 0
1 1 0 1 0 1 0 0 0 0 0
1 1 0 1 0 1 0 1 0 0 0
1 1 0 1 0 1 1 0 0 0 1
1 1 0 1 0 1 1 1 0 0 1
2 1 0 1 0 0 0 0 0 0 0
2 1 0 1 0 0 0 1 0 0 0
2 1 0 1 0 0 1 0 0 0 0
2 1 0 1 0 0 1 1 0 0 0
2 1 0 1 0 1 0 0 1 1 0
2 1 0 1 0 1 0 1 0 1 0
2 1 0 1 0 1 1 0 0 0 1
2 1 0 1 0 1 1 1 0 0 1
3 1 0 1 0 0 0 0 1 1 0
3 1 0 1 0 0 0 1 0 1 0
3 1 0 1 0 0 1 0 0 0 0
3 1 0 1 0 0 1 1 0 0 0
3 1 0 1 0 1 0 0 1 1 0
3 1 0 1 0 1 0 1 0 1 0
3 1 0 1 0 1 1 0 0 0 1
3 1 0 1 0 1 1 1 0 0 1
4 1 0 1 0 0 0 0 0 0 0
4 1 0 1 0 0 0 1 0 0 0
4 1 0 1 0 0 1 0 1 1 0
4 1 0 1 0 0 1 1 0 1 0
4 1 0 1 0 1 0 0 0 0 0
4 1 0 1 0 1 0 1 0 0 0
4 1 0 1 0 1 1 0 0 0 1
4 1 0 1 0 1 1 1 0 0 1
5 1 0 1 0 0 0 0 1 1 0
5 1 0 1 0 0 0 1 0 1 0
5 1 0 1 0 0 1 0 1 1 0
5 1 0 1 0 0 1 1 0 1 0
5 1 0 1 0 1 0 0 0 0 0
5 1 0 1 0 1 0 1 0 0 0
5 1 0 1 0 1 1 0 0 0 1
5 1 0 1 0 1 1 1 0 0 1
6 1 0 1 0 0 0 0 0 0 0
6 1 0 1 0 0 0 1 0 0 0
6 1 0 1 0 0 1 0 1 1 0
6 1 0 1 0 0 1 1 0 1 0
6 1 0 1 0 1 0 0 1 1 0
6 1 0 1 0 1 0 1 0 1 0
6 1 0 1 0 1 1 0 0 0 1
6 1 0 1 0 1 1 1 0 0 1
7 1 0 1 0 0 0 0 1 1 0
7 1 0 1 0 0 0 1 0 1 0
7 1 0 1 0 0 1 0 1 1 0
7 1 0 1 0 0 1 1 0 1 0
7 1 0 1 0 1 0 0 1 1 0
7 1 0 1 0 1 0 1 0 1 0
7 1 0 1 0 1 1 0 0 0 1
7 1 0 1 0 1 1 1 0 0 1
8 1 0 1 0 0 0 0 0 0 0
8 1 0 1 0 0 0 1 0 0 0
8 1 0 1 0 0 1 0 0 0 0
8 1 0 1 0 0 1 1 0 0 0
8 1 0 1 0 1 0 0 0 0 0
8 1 0 1 0 1 0 1 0 0 0
8 1 0 1 0 1 1 0 1 1 1
8 1 0 1 0 1 1 1 0 1 1
9 1 0 1 0 0 0 0 1 1 0
9 1 0 1 0 0 0 1 0 1 0
9 1 0 1 0 0 1 0 0 0 0
9 1 0 1 0 0 1 1 0 0 0
9 1 0 1 0 1 0 0 0 0 0
9 1 0 1 0 1 0 1 0 0 0
9 1 0 1 0 1 1 0 1 1 1
9 1 0 1 0 1 1 1 0 1 1
10 1 0 1 0 0 0 0 0 0 0
10 1 0 1 0 0 0 1 0 0 0
10 1 0 1 0 0 1 0 0 0 0
10 1 0 1 0 0 1 1 0 0 0
10 1 0 1 0 1 0 0 1 1 0
10 1 0 1 0 1 0 1 0 1 0
10 1 0 1 0 1 1 0 1 1 1
10 1 0 1 0 1 1 1 0 1 1
11 1 0 1 0 0 0 0 1 1 0
11 1 0 1 0 0 0 1 0 1 0
11 1 0 1 0 0 1 0 0 0 0
11 1 0 1 0 0 1 1 0 0 0
11 1 0 1 0 1 0 0 1 1 0
11 1 0 1 0 1 0 1 0 1 0
11 1 0 1 0 1 1 0 1 1 1
11 1 0 1 0 1 1 1 0 1 1
12 1 0 1 0 0 0 0 0 0 0
12 1 0 1 0 0 0 1 0 0 0
12 1 0 1 0 0 1 0 1 1 0
12 1 0 1 0 0 1 1 0 1 0
12 1 0 1 0 1 0 0 0 0 0
12 1 0 1 0 1 0 1 0 0 0
12 1 0 1 0 1 1 0 1 1 1
12 1 0 1 0 1 1 1 0 1 1
13 1 0 1 0 0 0 0 1 1 0
13 1 0 1 0 0 0 1 0 1 0
13 1 0 1 0 0 1 0 1 1 0
13 1 0 1 0 0 1 1 0 1 0
13 1 0 1 0 1 0 0 0 0 0
13 1 0 1 0 1 0 1 0 0 0
13 1 0 1 0 1 1 0 1 1 1
13 1 0 1 0 1 1 1 0 1 1
14 1 0 1 0 0 0 0 0 0 0
14 1 0 1 0 0 0 1 0 0 0
14 1 0 1 0 0 1 0 1 1 0
14 1 0 1 0 0 1 1 0 1 0
14 1 0 1 0 1 0 0 1 1 0
14 1 0 1 0 1 0 1 0 1 0
14 1 0 1 0 1 1 0 1 1 1
14 1 0 1 0 1 1 1 0 1 1
15 1 0 1 0 0 0 0 1 1 0
15 1 0 1 0 0 0 1 0 1 0
15 1 0 1 0 0 1 0 1 1 0
15 1 0 1 0 0 1 1 0 1 0
15 1 0 1 0 1 0 0 1 1 0
15 1 0 1 0 1 0 1 0 1 0
15 1 0 1 0 1 1 0 1 1 1
15 1 0 1 0 1 1 1 0 1 1
16 1 0 1 0 0 0 0 0 0 0
16 1 0 1 0 0 0 1 1 0 0
16 1 0 1 0 0 1 0 0 0 0
16 1 0 1 0 0 1 1 0 0 0
16 1 0 1 0 1 0 0 0 0 0
16 1 0 1 0 1 0 1 0 0 0
16 1 0 1 0 1 1 0 0 0 1
16 1 0 1 0 1 1 1 0 0 1
17 1 0 1 0 0 0 0 1 1 0
17 1 0 1 0 0 0 1 1 1 0
17 1 0 1 0 0 1 0 0 0 0
17 1 0 1 0 0 1 1 0 0 0
17 1 0 1 0 1 0 0 0 0 0
17 1 0 1 0 1 0 1 0 0 0
17 1 0 1 0 1 1 0 0 0 1
17 1 0 1 0 1 1 1 0 0 1
18 1 0 1 0 0 0 0 0 0 0
18 1 0 1 0 0 0 1 1 0 0
18 1 0 1 0 0 1 0 0 0 0
18 1 0 1 0 0 1 1 0 0 0
18 1 0 1 0 1 0 0 1 1 0
18 1 0 1 0 1 0 1 0 1 0
18 1 0 1 0 1 1 0 0 0 1
18 1 0 1 0 1 1 1 0 0 1
19 1 0 1 0 0 0 0 1 1 0
19 1 0 1 0 0 0 1 1 1 0
19 1 0 1 0 0 1 0 0 0 0
19 1 0 1 0 0 1 1 0 0 0
19 1 0 1 0 1 0 0 1 1 0
19 1 0 1 0 1 0 1 0 1 0
19 1 0 1 0 1 1 0 0 0 1
19 1 0 1 0 1 1 1 0 0 1
20 1 0 1 0 0 0 0 0 0 0
20 1 0 1 0 0 0 1 1 0 0
20 1 0 1 0 0 1 0 1 1 0
20 1 0 1 0 0 1 1 0 1 0
20 1 0 1 0 1 0 0 0 0 0
20 1 0 1 0 1 0 1 0 0 0
20 1 0 1 0 1 1 0 0 0 1
20 1 0 1 0 1 1 1 0 0 1
21 1 0 1 0 0 0 0 1 1 0
21 1 0 1 0 0 0 1 1 1 0
21 1 0 1 0 0 1 0 1 1 0
21 1 0 1 0 0 1 1 0 1 0
21 1 0 1 0 1 0 0 0 0 0
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*/

/* Test case Prefix Accelerators:
# Prefix-Logic Accelerators
OPCODE Asel A_inv Bsel B_inv A B C MUX_OUT P G
80 1 0 0 1 0 0 0 0 0 0
80 1 0 0 1 0 1 0 0 0 0
80 1 0 0 1 1 0 0 0 0 1
80 1 0 0 1 1 1 0 0 0 1
10 1 0 0 0 0 0 1 0 0 0
10 1 0 0 0 0 1 1 0 0 0
10 1 0 0 0 1 0 1 0 1 0
10 1 0 0 0 1 1 1 0 1 0
250 1 0 0 1 0 0 0 0 0 0
250 1 0 0 1 0 1 0 0 0 0
250 1 0 0 1 1 0 0 1 1 1
250 1 0 0 1 1 1 0 1 1 1
170 1 0 1 0 0 0 0 0 0 0
170 1 0 1 0 0 1 0 0 0 0
170 1 0 1 0 1 0 0 1 1 0
170 1 0 1 0 1 1 0 1 1 1
            
*/
