// Digital circuit alu-32b-final.dig as structural Verilog
module alu_32b_final (
  input  [31:0] A,
  input  [31:0] B,
  input  [7:0] Opcode,
  input  [3:0] control,
  input  [31:0] C,
  input  [1:0] csel,
  input  CLK,
  input  FLAG_WE,
  input  nflag_a_is_zero,
  output [31:0] Out,
  output [12:0] CSR_FLAG
);

  wire _74377_2_pin1, C_out, ceff0, cin_sel, cout1, cout8, cout16, cout24, g0, g8, g16, g24, g_out_0,
       g_out_1, g_out_2, g_out_3, g_out_4, g_out_5, g_out_6, g_out_7, g_out_A, g_out_B, gb0, gb1, gb2, gb3,
       gb4, gb5, gb6, gb7, gb8, gb9, gb10, gb11, gb12, gb13, gb14, gb15, gb16, gb17, gb18, gb19, gb20, gb21,
       gb22, gb23, gb24, gb25, gb26, gb27, gb28, gb29, gb30, gb31, GT_sign, GTE_sign, LT_sign, LTE_sign,
       nC_out, nN_out, not_1_out, nV_out, nZ_out, p0, p8, p16, p24, p_out_0, p_out_1, p_out_2, p_out_3,
       p_out_4, p_out_5, p_out_6, p_out_7, p_out_A, p_out_B, pb0, pb1, pb2, pb3, pb4, pb5, pb6, pb7, pb8,
       pb9, pb10, pb11, pb12, pb13, pb14, pb15, pb16, pb17, pb18, pb19, pb20, pb21, pb22, pb23, pb24, pb25,
       pb26, pb27, pb28, pb29, pb30, pb31, q12, q13, q14, q15, V_out, z0, z1, z2, z3, z4, z5, z6, z7, Z_out;
  wire [6:1] cout1_7;
  wire [7:0] ceff8_15, ceff16_23, ceff24_31;
  wire [7:1] ceff0_7, cout8_15, cout16_23, cout24_31, g0_7, g8_15, g16_23, g24_31, p0_7, p8_15, p16_23,
       p24_31;

  _74540 _74540_1 (
    .pin1(1'b0), .pin2(g0), .pin3(g0_7[1]), .pin4(g0_7[2]), .pin5(g0_7[3]), .pin6(g0_7[4]), .pin7(g0_7[5]),
    .pin8(g0_7[6]), .pin9(g0_7[7]), .pin10(1'b0), .pin11(gb7), .pin12(gb6), .pin13(gb5), .pin14(gb4),
    .pin15(gb3), .pin16(gb2), .pin17(gb1), .pin18(gb0), .pin19(1'b0), .pin20(1'b1));
  _74540 _74540_2 (
    .pin1(1'b0), .pin2(p0), .pin3(p0_7[1]), .pin4(p0_7[2]), .pin5(p0_7[3]), .pin6(p0_7[4]), .pin7(p0_7[5]),
    .pin8(p0_7[6]), .pin9(p0_7[7]), .pin10(1'b0), .pin11(pb7), .pin12(pb6), .pin13(pb5), .pin14(pb4),
    .pin15(pb3), .pin16(pb2), .pin17(pb1), .pin18(pb0), .pin19(1'b0), .pin20(1'b1));
  _74540 _74540_3 (
    .pin1(1'b0), .pin2(g8), .pin3(g8_15[1]), .pin4(g8_15[2]), .pin5(g8_15[3]), .pin6(g8_15[4]),
    .pin7(g8_15[5]), .pin8(g8_15[6]), .pin9(g8_15[7]), .pin10(1'b0), .pin11(gb15), .pin12(gb14),
    .pin13(gb13), .pin14(gb12), .pin15(gb11), .pin16(gb10), .pin17(gb9), .pin18(gb8), .pin19(1'b0),
    .pin20(1'b1));
  _74540 _74540_4 (
    .pin1(1'b0), .pin2(p8), .pin3(p8_15[1]), .pin4(p8_15[2]), .pin5(p8_15[3]), .pin6(p8_15[4]),
    .pin7(p8_15[5]), .pin8(p8_15[6]), .pin9(p8_15[7]), .pin10(1'b0), .pin11(pb15), .pin12(pb14),
    .pin13(pb13), .pin14(pb12), .pin15(pb11), .pin16(pb10), .pin17(pb9), .pin18(pb8), .pin19(1'b0),
    .pin20(1'b1));
  _74540 _74540_5 (
    .pin1(1'b0), .pin2(g16), .pin3(g16_23[1]), .pin4(g16_23[2]), .pin5(g16_23[3]), .pin6(g16_23[4]),
    .pin7(g16_23[5]), .pin8(g16_23[6]), .pin9(g16_23[7]), .pin10(1'b0), .pin11(gb23), .pin12(gb22),
    .pin13(gb21), .pin14(gb20), .pin15(gb19), .pin16(gb18), .pin17(gb17), .pin18(gb16), .pin19(1'b0),
    .pin20(1'b1));
  _74540 _74540_6 (
    .pin1(1'b0), .pin2(p16), .pin3(p16_23[1]), .pin4(p16_23[2]), .pin5(p16_23[3]), .pin6(p16_23[4]),
    .pin7(p16_23[5]), .pin8(p16_23[6]), .pin9(p16_23[7]), .pin10(1'b0), .pin11(pb23), .pin12(pb22),
    .pin13(pb21), .pin14(pb20), .pin15(pb19), .pin16(pb18), .pin17(pb17), .pin18(pb16), .pin19(1'b0),
    .pin20(1'b1));
  and and_1 (cin_sel, csel[0], csel[1]);
  Multiplexer #(.Selector_Bits(2)) multiplexer_1 (
    .sel(csel), .in_0(1'b0), .in_1(1'b1), .in_2(CSR_FLAG[4]), .in_3(C[0]), .out(ceff0));
  Multiplexer #(.Bits(7)) multiplexer_2 (.sel(cin_sel), .in_0({cout1_7, cout1}), .in_1(C[7:1]), .out(ceff0_7));
  Multiplexer #(.Bits(8)) multiplexer_3 (.sel(cin_sel), .in_0({cout8_15, cout8}), .in_1(C[15:8]), .out(ceff8_15));
  Multiplexer #(.Bits(8)) multiplexer_4 (.sel(cin_sel), .in_0({cout16_23, cout16}), .in_1(C[23:16]), .out(ceff16_23));
  Multiplexer #(.Bits(8)) multiplexer_5 (.sel(cin_sel), .in_0({cout24_31, cout24}), .in_1(C[31:24]), .out(ceff24_31));
  _74540 _74540_7 (
    .pin1(1'b0), .pin2(g24), .pin3(g24_31[1]), .pin4(g24_31[2]), .pin5(g24_31[3]), .pin6(g24_31[4]),
    .pin7(g24_31[5]), .pin8(g24_31[6]), .pin9(g24_31[7]), .pin10(1'b0), .pin11(gb31), .pin12(gb30),
    .pin13(gb29), .pin14(gb28), .pin15(gb27), .pin16(gb26), .pin17(gb25), .pin18(gb24), .pin19(1'b0),
    .pin20(1'b1));
  _74540 _74540_8 (
    .pin1(1'b0), .pin2(p24), .pin3(p24_31[1]), .pin4(p24_31[2]), .pin5(p24_31[3]), .pin6(p24_31[4]),
    .pin7(p24_31[5]), .pin8(p24_31[6]), .pin9(p24_31[7]), .pin10(1'b0), .pin11(pb31), .pin12(pb30),
    .pin13(pb29), .pin14(pb28), .pin15(pb27), .pin16(pb26), .pin17(pb25), .pin18(pb24), .pin19(1'b0),
    .pin20(1'b1));
  _74182 _74182_1 (
    .pin1(gb1), .pin2(pb1), .pin3(gb0), .pin4(pb0), .pin5(gb3), .pin6(pb3), .pin7(p_out_0), .pin8(1'b0),
    .pin9(cout1_7[2]), .pin10(g_out_0), .pin11(cout1_7[1]), .pin12(cout1), .pin13(ceff0), .pin14(gb2),
    .pin15(pb2), .pin16(1'b1));
  _74182 _74182_2 (
    .pin1(gb17), .pin2(pb17), .pin3(gb16), .pin4(pb16), .pin5(gb19), .pin6(pb19), .pin7(p_out_4),
    .pin8(1'b0), .pin9(cout16_23[3]), .pin10(g_out_4), .pin11(cout16_23[2]), .pin12(cout16_23[1]),
    .pin13(cout16), .pin14(gb18), .pin15(pb18), .pin16(1'b1));
  _74182 _74182_3 (
    .pin1(gb5), .pin2(pb5), .pin3(gb4), .pin4(pb4), .pin5(gb7), .pin6(pb7), .pin7(p_out_1), .pin8(1'b0),
    .pin9(cout1_7[6]), .pin10(g_out_1), .pin11(cout1_7[5]), .pin12(cout1_7[4]), .pin13(cout1_7[3]),
    .pin14(gb6), .pin15(pb6), .pin16(1'b1));
  _74182 _74182_4 (
    .pin1(gb21), .pin2(pb21), .pin3(gb20), .pin4(pb20), .pin5(gb23), .pin6(pb23), .pin7(p_out_5),
    .pin8(1'b0), .pin9(cout16_23[7]), .pin10(g_out_5), .pin11(cout16_23[6]), .pin12(cout16_23[5]),
    .pin13(cout16_23[4]), .pin14(gb22), .pin15(pb22), .pin16(1'b1));
  _74182 _74182_5 (
    .pin1(gb9), .pin2(pb9), .pin3(gb8), .pin4(pb8), .pin5(gb11), .pin6(pb11), .pin7(p_out_2), .pin8(1'b0),
    .pin9(cout8_15[3]), .pin10(g_out_2), .pin11(cout8_15[2]), .pin12(cout8_15[1]), .pin13(cout8),
    .pin14(gb10), .pin15(pb10), .pin16(1'b1));
  _74182 _74182_6 (
    .pin1(gb25), .pin2(pb25), .pin3(gb24), .pin4(pb24), .pin5(gb27), .pin6(pb27), .pin7(p_out_6),
    .pin8(1'b0), .pin9(cout24_31[3]), .pin10(g_out_6), .pin11(cout24_31[2]), .pin12(cout24_31[1]),
    .pin13(cout24), .pin14(gb26), .pin15(pb26), .pin16(1'b1));
  // alu_8b_final Cell_0: pin names not known; wires that end beside it: Opcode, control[0], A[7:0], B[7:0], {ceff0_7, ceff0}, control[1], control[2], control[3], Out[7:0], {p0_7, p0}, {g0_7, g0}
  // alu_8b_final Cell_1: pin names not known; wires that end beside it: Opcode, control[0], A[15:8], B[15:8], ceff8_15, control[1], control[2], control[3], Out[15:8], {p8_15, p8}, {g8_15, g8}
  _74182 _74182_7 (
    .pin1(gb13), .pin2(pb13), .pin3(gb12), .pin4(pb12), .pin5(gb15), .pin6(pb15), .pin7(p_out_3),
    .pin8(1'b0), .pin9(cout8_15[7]), .pin10(g_out_3), .pin11(cout8_15[6]), .pin12(cout8_15[5]),
    .pin13(cout8_15[4]), .pin14(gb14), .pin15(pb14), .pin16(1'b1));
  _74182 _74182_8 (
    .pin1(gb29), .pin2(pb29), .pin3(gb28), .pin4(pb28), .pin5(gb31), .pin6(pb31), .pin7(p_out_7),
    .pin8(1'b0), .pin9(cout24_31[7]), .pin10(g_out_7), .pin11(cout24_31[6]), .pin12(cout24_31[5]),
    .pin13(cout24_31[4]), .pin14(gb30), .pin15(pb30), .pin16(1'b1));
  // alu_8b_final Cell_2: pin names not known; wires that end beside it: Opcode, control[0], A[23:16], B[23:16], ceff16_23, control[1], control[2], control[3], Out[23:16], {p16_23, p16}, {g16_23, g16}
  // alu_8b_final Cell_3: pin names not known; wires that end beside it: Opcode, control[0], A[31:24], B[31:24], ceff24_31, control[1], control[2], control[3], Out[31:24], {p24_31, p24}, {g24_31, g24}
  _74182 _74182_9 (
    .pin1(g_out_1), .pin2(p_out_1), .pin3(g_out_0), .pin4(p_out_0), .pin5(g_out_3), .pin6(p_out_3),
    .pin7(p_out_A), .pin8(1'b0), .pin9(cout8_15[4]), .pin10(g_out_A), .pin11(cout8), .pin12(cout1_7[3]),
    .pin13(ceff0), .pin14(g_out_2), .pin15(p_out_2), .pin16(1'b1));
  _74182 _74182_10 (
    .pin1(g_out_5), .pin2(p_out_5), .pin3(g_out_4), .pin4(p_out_4), .pin5(g_out_7), .pin6(p_out_7),
    .pin7(p_out_B), .pin8(1'b0), .pin9(cout24_31[4]), .pin10(g_out_B), .pin11(cout24), .pin12(cout16_23[4]),
    .pin13(cout16), .pin14(g_out_6), .pin15(p_out_6), .pin16(1'b1));
  _74182 _74182_11 (
    .pin1(g_out_B), .pin2(p_out_B), .pin3(g_out_A), .pin4(p_out_A), .pin5(1'b0), .pin6(1'b0), .pin8(1'b0),
    .pin11(C_out), .pin12(cout16), .pin13(ceff0), .pin14(1'b0), .pin15(1'b0), .pin16(1'b1));  // open: pin7, pin9, pin10
  _7425 _7425_1 (
    .pin1(Out[0]), .pin2(Out[1]), .pin3(1'b1), .pin4(Out[2]), .pin5(Out[3]), .pin6(z0), .pin7(1'b0),
    .pin8(z1), .pin9(Out[4]), .pin10(Out[5]), .pin11(1'b1), .pin12(Out[6]), .pin13(Out[7]), .pin14(1'b1));
  _7425 _7425_2 (
    .pin1(Out[16]), .pin2(Out[17]), .pin3(1'b1), .pin4(Out[18]), .pin5(Out[19]), .pin6(z4), .pin7(1'b0),
    .pin8(z5), .pin9(Out[20]), .pin10(Out[21]), .pin11(1'b1), .pin12(Out[22]), .pin13(Out[23]), .pin14(1'b1));
  _7425 _7425_3 (
    .pin1(Out[8]), .pin2(Out[9]), .pin3(1'b0), .pin4(1'b1), .pin5(Out[11]), .pin6(z2), .pin7(1'b0),
    .pin8(z3), .pin9(Out[12]), .pin10(Out[13]), .pin11(1'b1), .pin12(Out[14]), .pin13(Out[15]), .pin14(1'b1));
  _7425 _7425_4 (
    .pin1(Out[24]), .pin2(Out[25]), .pin3(1'b1), .pin4(Out[26]), .pin5(Out[27]), .pin6(z6), .pin7(1'b0),
    .pin8(z7), .pin9(Out[28]), .pin10(Out[29]), .pin11(1'b1), .pin12(Out[30]), .pin13(Out[31]), .pin14(1'b1));
  _74133 _74133_1 (
    .pin1(z0), .pin2(z1), .pin3(z2), .pin4(z3), .pin5(z4), .pin6(z5), .pin7(z6), .pin8(1'b0), .pin9(nZ_out),
    .pin10(1'b1), .pin11(1'b1), .pin12(1'b1), .pin13(1'b1), .pin14(z7), .pin15(1'b1), .pin16(1'b1));
  not not_1 (not_1_out, FLAG_WE);
  _74377 _74377_1 (
    .pin1(not_1_out), .pin2(CSR_FLAG[0]), .pin3(Z_out), .pin4(nZ_out), .pin5(CSR_FLAG[1]),
    .pin6(CSR_FLAG[2]), .pin7(Out[31]), .pin8(nN_out), .pin9(CSR_FLAG[3]), .pin10(1'b0), .pin11(CLK),
    .pin12(CSR_FLAG[4]), .pin13(C_out), .pin14(nC_out), .pin15(CSR_FLAG[5]), .pin16(CSR_FLAG[6]),
    .pin17(V_out), .pin18(nV_out), .pin19(CSR_FLAG[7]), .pin20(1'b1));
  not not_2 (nV_out, V_out);
  not not_3 (Z_out, nZ_out);
  xor xor_1 (V_out, cout24_31[7], C_out);
  not not_4 (nC_out, C_out);
  and and_2 (GT_sign, nZ_out, GTE_sign);
  or or_1 (LTE_sign, Z_out, LT_sign);
  _74377 _74377_2 (
    .pin1(_74377_2_pin1), .pin2(CSR_FLAG[8]), .pin3(LT_sign), .pin4(LTE_sign), .pin5(CSR_FLAG[9]),
    .pin6(CSR_FLAG[10]), .pin7(GT_sign), .pin8(GTE_sign), .pin9(CSR_FLAG[11]), .pin10(1'b0), .pin11(CLK),
    .pin12(q12), .pin13(1'b0), .pin14(1'b0), .pin15(q13), .pin16(q14), .pin17(1'b0), .pin18(1'b0),
    .pin19(q15), .pin20(1'b1));
  not not_5 (_74377_2_pin1, FLAG_WE);
  not not_6 (nN_out, Out[31]);
  not not_7 (GTE_sign, LT_sign);
  xor xor_2 (LT_sign, V_out, Out[31]);

  assign CSR_FLAG[12] = nflag_a_is_zero;

  // Other names for the same wires on the sheet: a0_7[7:0] = A[7:0]; a8_15[7:0] = A[15:8]; a16_23[7:0] = A[23:16];
  //   a24_31[7:0] = A[31:24]; b0_7[7:0] = B[7:0]; b8_15[7:0] = B[15:8]; b16_23[7:0] = B[23:16];
  //   b24_31[7:0] = B[31:24]; C_logic[31:0] = C; cin0 = C[0]; c1_7[6:0] = C[7:1]; c8_15[7:0] = C[15:8];
  //   c16_23[7:0] = C[23:16]; c24_31[7:0] = C[31:24]; ceff0_7[0] = ceff0; ceff1_7[6:0] = ceff0_7; asel = control[0];
  //   ainv = control[1]; bsel = control[2]; binv = control[3]; cout1_7[0] = cout1; cout2 = cout1_7[1];
  //   cout3 = cout1_7[2]; cout4 = cout1_7[3]; cout5 = cout1_7[4]; cout6 = cout1_7[5]; cout7 = cout1_7[6];
  //   cout8_15[0] = cout8; cout9 = cout8_15[1]; cout10 = cout8_15[2]; cout11 = cout8_15[3]; cout12 = cout8_15[4];
  //   cout13 = cout8_15[5]; cout14 = cout8_15[6]; cout15 = cout8_15[7]; cout16_23[0] = cout16; cout17 = cout16_23[1];
  //   cout18 = cout16_23[2]; cout19 = cout16_23[3]; cout20 = cout16_23[4]; cout21 = cout16_23[5];
  //   cout22 = cout16_23[6]; cout23 = cout16_23[7]; cout24_31[0] = cout24; cout25 = cout24_31[1];
  //   cout26 = cout24_31[2]; cout27 = cout24_31[3]; cout28 = cout24_31[4]; cout29 = cout24_31[5];
  //   cout30 = cout24_31[6]; cout31 = cout24_31[7]; cout32 = C_out; flag_c = CSR_FLAG[4]; flag_c_b = CSR_FLAG[5];
  //   flag_gt = CSR_FLAG[10]; flag_gte = CSR_FLAG[11]; flag_lt = CSR_FLAG[8]; flag_lte = CSR_FLAG[9];
  //   flag_n = CSR_FLAG[2]; flag_n_b = CSR_FLAG[3]; flag_v = CSR_FLAG[6]; flag_v_b = CSR_FLAG[7];
  //   flag_z = CSR_FLAG[0]; flag_z_b = CSR_FLAG[1]; g0_7[0] = g0; g1 = g0_7[1]; g2 = g0_7[2]; g3 = g0_7[3];
  //   g4 = g0_7[4]; g5 = g0_7[5]; g6 = g0_7[6]; g7 = g0_7[7]; g8_15[0] = g8; g9 = g8_15[1]; g10 = g8_15[2];
  //   g11 = g8_15[3]; g12 = g8_15[4]; g13 = g8_15[5]; g14 = g8_15[6]; g15 = g8_15[7]; g16_23[0] = g16;
  //   g17 = g16_23[1]; g18 = g16_23[2]; g19 = g16_23[3]; g20 = g16_23[4]; g21 = g16_23[5]; g22 = g16_23[6];
  //   g23 = g16_23[7]; g24_31[0] = g24; g25 = g24_31[1]; g26 = g24_31[2]; g27 = g24_31[3]; g28 = g24_31[4];
  //   g29 = g24_31[5]; g30 = g24_31[6]; g31 = g24_31[7]; out0_7[7:0] = Out[7:0]; out32[31:0] = Out;
  //   out8_15[7:0] = Out[15:8]; out16_23[7:0] = Out[23:16]; out24_31[7:0] = Out[31:24]; N_out = Out[31]; p0_7[0] = p0;
  //   p1 = p0_7[1]; p2 = p0_7[2]; p3 = p0_7[3]; p4 = p0_7[4]; p5 = p0_7[5]; p6 = p0_7[6]; p7 = p0_7[7]; p8_15[0] = p8;
  //   p9 = p8_15[1]; p10 = p8_15[2]; p11 = p8_15[3]; p12 = p8_15[4]; p13 = p8_15[5]; p14 = p8_15[6]; p15 = p8_15[7];
  //   p16_23[0] = p16; p17 = p16_23[1]; p18 = p16_23[2]; p19 = p16_23[3]; p20 = p16_23[4]; p21 = p16_23[5];
  //   p22 = p16_23[6]; p23 = p16_23[7]; p24_31[0] = p24; p25 = p24_31[1]; p26 = p24_31[2]; p27 = p24_31[3];
  //   p28 = p24_31[4]; p29 = p24_31[5]; p30 = p24_31[6]; p31 = p24_31[7]

  // Notes on the sheet:
  //   A: default 9
  //   B: default 20
  //   Opcode: default 150
  //   control: default 13
  //   csel: default 1
endmodule

/* Test case Exhaustive 91 Ops Test:
A B C Opcode control csel CLK FLAG_WE Out

0xa783a7a6 0x4db0c2fa 0x44df5242 0x96 5 2 0 0 0xf5346aa0
0x25ab61a9 0x1ecff469 0x96d6ac2b 0x96 5 2 0 0 0x447b5612
0x2308253d 0x6b2f3778 0x13ba47fb 0x96 5 2 0 0 0x8e375cb5
0x24475286 0x90fb871d 0x7a9ca76d 0x96 5 2 0 0 0xb542d9a3
0xb7db4234 0x5a5492cc 0x56b9b64c 0x96 5 2 0 0 0x122fd500
0x39b95cea 0x352df531 0xf8ae3b49 0x96 5 1 0 0 0x6ee7521c
0xb8df2e6e 0xbb86eb67 0xcf0e683a 0x96 5 1 0 0 0x746619d6
0xc63364f0 0xb7e2c1b0 0xd9b33248 0x96 5 1 0 0 0x7e1626a1
0xa31b9b7d 0xf6cd05a7 0x351a85cd 0x96 5 1 0 0 0x99e8a125
0xc7e604ba 0x3d70b751 0xa7cb8fa9 0x96 5 1 0 0 0x556bc0c
0xa4dac17c 0xe49f230f 0xffffffff 0x96 1 1 0 0 0xa4dac17d
0x550711ea 0x32bad3a 0x2be8e94b 0x96 1 1 0 0 0x550711eb
0xcabd96b7 0xf04c7d26 0x56561533 0x96 1 1 0 0 0xcabd96b8
0x824c1bd4 0xe711d246 0xa74cb39e 0x96 1 1 0 0 0x824c1bd5
0x377ae39 0x6c0f7344 0xc06ba4ac 0x96 1 1 0 0 0x377ae3a
0xc987e839 0x4760dca5 0xff26c139 0x96 4 1 0 0 0x4760dca6
0xd5d8579e 0xbfd13081 0xae5b793 0x96 4 1 0 0 0xbfd13082
0x37c67886 0x65a5fe9f 0xf5218f29 0x96 4 1 0 0 0x65a5fea0
0x8827e1a7 0x3180fae4 0x4c8087cc 0x96 4 1 0 0 0x3180fae5
0x3e2abc6 0x2215c5db 0x792ef900 0x96 4 1 0 0 0x2215c5dc
0x99dc27d5 0x8a2423b9 0x56c53e7f 0x96 9 0 0 0 0x99dc27d4
0x36d535b3 0xcfb6a74 0xe5c5e92b 0x96 9 0 0 0 0x36d535b2
0x98958417 0xa314599b 0x157fe84e 0x96 9 0 0 0 0x98958416
0xd007aec0 0x65258fab 0x2de3bca1 0x96 9 0 0 0 0xd007aebf
0x1940dde4 0x563f4f9c 0x987d53eb 0x96 9 0 0 0 0x1940dde3
0x52feb4fa 0xb1fd66bd 0xffffffff 0x96 6 0 0 0 0xb1fd66bc
0x44450552 0x1c2cf134 0xa1f922ef 0x96 6 0 0 0 0x1c2cf133
0xc66310fc 0xc5d19144 0x7301ec83 0x96 6 0 0 0 0xc5d19143
0xd46532c0 0x56d3e6f0 0x6b80d09f 0x96 6 0 0 0 0x56d3e6ef
0xcc7eecfd 0x5bc433e1 0x57f4750e 0x96 6 0 0 0 0x5bc433e0
0x7ab17b5a 0x5f17e18 0x71f763ad 0x96 3 1 0 0 0x854e84a6
0x56ec227 0x1176692b 0xc31830c 0x96 3 1 0 0 0xfa913dd9
0x18ba8927 0xf1594232 0x975daa8f 0x96 3 1 0 0 0xe74576d9
0x581f137 0x1babe0a7 0x98a5d3f7 0x96 3 1 0 0 0xfa7e0ec9
0x646fb9b4 0xcd5acf2c 0x9209419f 0x96 3 1 0 0 0x9b90464c
0x456ee48c 0x87debd7 0xbc3e175a 0x96 12 1 0 0 0xf7821429
0xe0a161ec 0xed5df8e3 0xacd208cf 0x96 12 1 0 0 0x12a2071d
0x5f48a116 0xe7c3d85b 0xfc79147 0x96 12 1 0 0 0x183c27a5
0xad051dd3 0xa8f93c87 0xae3bf329 0x96 12 1 0 0 0x5706c379
0xf6d2003b 0x3b144782 0x1aeb41a4 0x96 12 1 0 0 0xc4ebb87e
0x71ec31e2 0xf2bb2b8f 0xffffffff 0x96 3 0 0 0 0x8e13ce1d
0xa63ceda6 0xf711f4b5 0x91b69386 0x96 3 0 0 0 0x59c31259
0xe80cab2b 0x151bc3c9 0x5ec2accf 0x96 3 0 0 0 0x17f354d4
0x579f15df 0xc2810325 0xae22f089 0x96 3 0 0 0 0xa860ea20
0x8d164400 0xf62449b 0x57f5ef10 0x96 3 0 0 0 0x72e9bbff
0xa673f3d8 0xf7f0b71e 0x852c536d 0x96 12 0 0 0 0x80f48e1
0xdcdd1146 0x2a6720e5 0xed4fe86c 0x96 12 0 0 0 0xd598df1a
0xa64faa35 0x82d59321 0xf28eecbb 0x96 12 0 0 0 0x7d2a6cde
0xa9b36b5b 0xcb94b49a 0x501363d9 0x96 12 0 0 0 0x346b4b65
0xdf807222 0xdb5f08d 0x93376de6 0x96 12 0 0 0 0xf24a0f72
0xdb122d71 0x27324783 0x7496e322 0x96 1 0 0 0 0xdb122d71
0x667798e2 0xb6e1cf3 0x2d99cfb5 0x96 1 0 0 0 0x667798e2
0xb74acff6 0x8ba22f7a 0x3656221b 0x96 1 0 0 0 0xb74acff6
0x8e50efd1 0xb53e3eaf 0x20650729 0x96 1 0 0 0 0x8e50efd1
0x3f3a36ab 0x58041bb4 0xc039084c 0x96 1 0 0 0 0x3f3a36ab
0xe711665c 0xe2848f73 0xffffffff 0x96 4 0 0 0 0xe2848f73
0x4f44daf6 0x73db8e4e 0x2271c831 0x96 4 0 0 0 0x73db8e4e
0xa4f34821 0x9fc8cd98 0x35351d36 0x96 4 0 0 0 0x9fc8cd98
0x53c02f74 0x9c0bf2e9 0x2b844ff5 0x96 4 0 0 0 0x9c0bf2e9
0x7c36e2ef 0x880ed993 0x92cd1af7 0x96 4 0 0 0 0x880ed993
0x83a2e889 0xc84fbcfd 0x33cc91ee 0x96 0 0 0 0 0x0
0x52bf9b53 0xc5977586 0x9a3592f0 0x96 0 0 0 0 0x0
0xad7257e1 0x3f317ec1 0x8e697f1a 0x96 0 0 0 0 0x0
0xc756a361 0xc8633116 0x777bafa8 0x96 0 0 0 0 0x0
0x5c8fe74b 0x6a625d02 0x1309dd04 0x96 0 0 0 0 0x0
0x34c56b92 0x195795a8 0xd9003d13 0x96 0 1 0 0 0x1
0x3bdb56f5 0xa55477e0 0xb292c036 0x96 0 1 0 0 0x1
0xe2054c5a 0xa969969e 0xabab4967 0x96 0 1 0 0 0x1
0x90252e30 0x8a9f4d03 0xffa321e 0x96 0 1 0 0 0x1
0xb7db5f0a 0x2b56228 0x930f1ac5 0x96 0 1 0 0 0x1
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*/

/* Test case alu-comb-flags:
A B C Opcode control csel CLK FLAG_WE Out


0x0 0x0 0x0 0x96 0 0 0 0 0x0
0xffffffff 0xffffffff 0x0 0x96 13 1 0 0 0x0
0x0 0x1 0x0 0x96 13 1 0 0 0xffffffff
0x7fffffff 0x1 0x0 0x96 1 1 0 0 0x80000000
0x80000000 0x80000000 0x0 0x96 5 2 0 0 0x0
0x1 0xffffffff 0x0 0x96 5 0 0 0 0x0
0xffffffff 0x1 0x0 0x96 5 0 0 0 0x0
0x12345678 0x12345678 0x0 0x96 13 1 0 0 0x0
0x0 0x1 0x0 0x96 13 1 0 0 0xffffffff
0x2 0x1 0x0 0x96 13 1 0 0 0x1
0x80000000 0x1 0x0 0x96 13 1 0 0 0x7fffffff
0x7fffffff 0xffffffff 0x0 0x96 13 1 0 0 0x80000000
*/

/* Test case alu-flagc-carry:
A B C Opcode control csel CLK FLAG_WE Out


0x5 0x3 0x0 0x96 13 1 0 1 0x2
0x5 0x3 0x0 0x96 13 1 C 1 0x2
0x5 0x3 0x0 0x96 5 2 0 0 0x9
0x0 0xffffffff 0x0 0x96 13 1 0 1 0x1
0x0 0xffffffff 0x0 0x96 13 1 C 1 0x1
0x0 0xffffffff 0x0 0x96 5 2 0 0 0xffffffff
0x12345678 0x9abcdef0 0x0 0x96 13 1 0 1 0x77777788
0x12345678 0x9abcdef0 0x0 0x96 13 1 C 1 0x77777788
0x12345678 0x9abcdef0 0x0 0x96 5 2 0 0 0xacf13568
*/
