// Digital circuit alu-4b-final.dig as structural Verilog
module alu_4b_final (
  input  [3:0] A,
  input  [3:0] B,
  input  [7:0] OPCODE,
  input  [3:0] C,
  input  [1:0] alu_ctrl,
  input  cin,
  output [3:0] Out,
  output cout,
  output sum3,
  output aeff3,
  output beff3
);

  wire beff0, beff1, beff2, log0, log1, log2, nand_1_out, nand_2_out, nand_3_out, nand_4_out;

  nand nand_1 (nand_1_out, B[0], alu_ctrl[1]);
  nand nand_2 (nand_2_out, B[1], alu_ctrl[1]);
  nand nand_3 (nand_3_out, B[2], alu_ctrl[1]);
  nand nand_4 (nand_4_out, B[3], alu_ctrl[1]);
  xor xor_1 (beff0, nand_1_out, alu_ctrl[0]);
  xor xor_2 (beff1, nand_2_out, alu_ctrl[0]);
  xor xor_3 (beff2, nand_3_out, alu_ctrl[0]);
  xor xor_4 (beff3, nand_4_out, alu_ctrl[0]);
  alu_1b_final alu_1b_final_1 (.OPCODE(OPCODE), .A(A[0]), .B(B[0]), .C(C[0]), .MUX_OUT(log0));
  alu_1b_final alu_1b_final_2 (.OPCODE(OPCODE), .A(A[1]), .B(B[1]), .C(C[1]), .MUX_OUT(log1));
  alu_1b_final alu_1b_final_3 (.OPCODE(OPCODE), .A(A[2]), .B(B[2]), .C(C[2]), .MUX_OUT(log2));
  alu_1b_final alu_1b_final_4 (.OPCODE(OPCODE), .A(A[3]), .B(B[3]), .C(C[3]), .MUX_OUT(aeff3));
  _74283 _74283_1 (
    .pin1(Out[1]), .pin2(beff1), .pin3(log1), .pin4(Out[0]), .pin5(log0), .pin6(beff0), .pin7(cin),
    .pin8(1'b0), .pin9(cout), .pin10(Out[3]), .pin11(beff3), .pin12(aeff3), .pin13(Out[2]), .pin14(log2),
    .pin15(beff2), .pin16(1'b1));

  assign sum3 = Out[3];

  // Other names for the same wires on the sheet: binv = alu_ctrl[0]; bsel = alu_ctrl[1]; log3 = aeff3

  // Notes on the sheet:
  //   A: default 5
  //   B: default 3
endmodule
