// Digital circuit alu-8b-final.dig as structural Verilog
module alu_8b_final (
  input  [7:0] opcode,
  input  [4:0] control,
  input  [7:0] A,
  input  [7:0] B,
  input  [7:0] C,
  input  nz_in,
  input  cin,
  output [7:0] out,
  output vout,
  output zout,
  output nz_out,
  output n,
  output cout
);

  wire _7432_1_pin2, _7432_1_pin5, c0xp0, c4xp1, ceff0, ceff1, ceff2, ceff3, ceff4, ceff5, ceff6, ceff7,
       cin1, cin2, cin3, cin4, cin5, cin6, cin7, g0, g0_b, g1, g1_b, g2, g2_b, g3, g3_b, g4, g4_b, g5, g5_b,
       g6, g6_b, g7, g7_b, g_out_0, g_out_1, nor_1_out, nor_2_out, not_1_out, not_2_out, not_3_out, p0, p0_b,
       p1, p1_b, p2, p2_b, p3, p3_b, p4, p4_b, p5, p5_b, p6, p6_b, p7, p7_b, p_out_0, p_out_1;

  xor xor_1 (vout, cin7, cout);
  nor nor_1 (nor_1_out, out[0], out[1], out[2], out[3]);
  nor nor_2 (nor_2_out, out[4], out[5], out[6], n);
  and and_1 (zout, nor_1_out, nor_2_out);
  not not_1 (not_1_out, zout);
  or or_1 (nz_out, not_1_out, nz_in);
  alu_1b_final alu_1b_final_1 (
    .OPCODE(opcode), .A(A[0]), .B(B[0]), .C(ceff0), .Asel(control[0]), .Bsel(control[2]), .A_inv(control[1]),
    .B_inv(control[3]), .MUX_OUT(out[0]), .G(g0), .P(p0));
  alu_1b_final alu_1b_final_2 (
    .OPCODE(opcode), .A(A[1]), .B(B[1]), .C(ceff1), .Asel(control[0]), .Bsel(control[2]), .A_inv(control[1]),
    .B_inv(control[3]), .MUX_OUT(out[1]), .G(g1), .P(p1));
  alu_1b_final alu_1b_final_3 (
    .OPCODE(opcode), .A(A[2]), .B(B[2]), .C(ceff2), .Asel(control[0]), .Bsel(control[2]), .A_inv(control[1]),
    .B_inv(control[3]), .MUX_OUT(out[2]), .G(g2), .P(p2));
  alu_1b_final alu_1b_final_4 (
    .OPCODE(opcode), .A(A[3]), .B(B[3]), .C(ceff3), .Asel(control[0]), .Bsel(control[2]), .A_inv(control[1]),
    .B_inv(control[3]), .MUX_OUT(out[3]), .G(g3), .P(p3));
  alu_1b_final alu_1b_final_5 (
    .OPCODE(opcode), .A(A[4]), .B(B[4]), .C(ceff4), .Asel(control[0]), .Bsel(control[2]), .A_inv(control[1]),
    .B_inv(control[3]), .MUX_OUT(out[4]), .G(g4), .P(p4));
  alu_1b_final alu_1b_final_6 (
    .OPCODE(opcode), .A(A[5]), .B(B[5]), .C(ceff5), .Asel(control[0]), .Bsel(control[2]), .A_inv(control[1]),
    .B_inv(control[3]), .MUX_OUT(out[5]), .G(g5), .P(p5));
  alu_1b_final alu_1b_final_7 (
    .OPCODE(opcode), .A(A[6]), .B(B[6]), .C(ceff6), .Asel(control[0]), .Bsel(control[2]), .A_inv(control[1]),
    .B_inv(control[3]), .MUX_OUT(out[6]), .G(g6), .P(p6));
  alu_1b_final alu_1b_final_8 (
    .OPCODE(opcode), .A(A[7]), .B(B[7]), .C(ceff7), .Asel(control[0]), .Bsel(control[2]), .A_inv(control[1]),
    .B_inv(control[3]), .MUX_OUT(n), .G(g7), .P(p7));
  _74540 _74540_1 (
    .pin1(1'b0), .pin2(p0), .pin3(p1), .pin4(p2), .pin5(p3), .pin6(g0), .pin7(g1), .pin8(g2), .pin9(g3),
    .pin10(1'b0), .pin11(g3_b), .pin12(g2_b), .pin13(g1_b), .pin14(g0_b), .pin15(p3_b), .pin16(p2_b),
    .pin17(p1_b), .pin18(p0_b), .pin19(1'b0), .pin20(1'b1));
  _74182 _74182_1 (
    .pin1(g1_b), .pin2(p1_b), .pin3(g0_b), .pin4(p0_b), .pin5(g3_b), .pin6(p3_b), .pin7(p_out_0),
    .pin8(1'b0), .pin9(cin3), .pin10(g_out_0), .pin11(cin2), .pin12(cin1), .pin13(cin), .pin14(g2_b),
    .pin15(p2_b), .pin16(1'b1));
  _74157 _74157_1 (
    .pin1(control[4]), .pin2(cin), .pin3(C[0]), .pin4(ceff0), .pin5(cin1), .pin6(C[1]), .pin7(ceff1),
    .pin8(1'b0), .pin9(ceff2), .pin10(C[2]), .pin11(cin2), .pin12(ceff3), .pin13(C[3]), .pin14(cin3),
    .pin15(1'b0), .pin16(1'b1));
  _74157 _74157_2 (
    .pin1(control[4]), .pin2(cin4), .pin3(C[4]), .pin4(ceff4), .pin5(cin5), .pin6(C[5]), .pin7(ceff5),
    .pin8(1'b0), .pin9(ceff6), .pin10(C[6]), .pin11(cin6), .pin12(ceff7), .pin13(C[7]), .pin14(cin7),
    .pin15(1'b0), .pin16(1'b1));
  _74540 _74540_2 (
    .pin1(1'b0), .pin2(p4), .pin3(p5), .pin4(p6), .pin5(p7), .pin6(g4), .pin7(g5), .pin8(g6), .pin9(g7),
    .pin10(1'b0), .pin11(g7_b), .pin12(g6_b), .pin13(g5_b), .pin14(g4_b), .pin15(p7_b), .pin16(p6_b),
    .pin17(p5_b), .pin18(p4_b), .pin19(1'b0), .pin20(1'b1));
  _74182 _74182_2 (
    .pin1(g5_b), .pin2(p5_b), .pin3(g4_b), .pin4(p4_b), .pin5(g7_b), .pin6(p7_b), .pin7(p_out_1),
    .pin8(1'b0), .pin9(cin7), .pin10(g_out_1), .pin11(cin6), .pin12(cin5), .pin13(cin4), .pin14(g6_b),
    .pin15(p6_b), .pin16(1'b1));
  not not_2 (not_2_out, p_out_0);
  not not_3 (not_3_out, p_out_1);
  _7408 _7408_1 (
    .pin1(not_2_out), .pin2(cin), .pin3(c0xp0), .pin4(not_3_out), .pin5(cin4), .pin6(c4xp1), .pin7(1'b0),
    .pin9(1'b0), .pin10(1'b0), .pin12(1'b0), .pin13(1'b0), .pin14(1'b1));  // open: pin8, pin11
  _7432 _7432_1 (
    .pin1(c0xp0), .pin2(_7432_1_pin2), .pin3(cin4), .pin4(c4xp1), .pin5(_7432_1_pin5), .pin6(cout),
    .pin7(1'b0), .pin9(1'b0), .pin10(1'b0), .pin12(1'b0), .pin13(1'b0), .pin14(1'b1));  // open: pin8, pin11
  not not_4 (_7432_1_pin2, g_out_0);
  not not_5 (_7432_1_pin5, g_out_1);

  assign out[7] = n;

  // Other names for the same wires on the sheet: cin0 = cin; cin8 = cout; asel = control[0]; ainv = control[1];
  //   bsel = control[2]; binv = control[3]; csel = control[4]; out7 = n

  // Notes on the sheet:
  //   opcode: default 150
  //   control: default 21
  //   A: default 6
  //   B: default 1
  //   C: default 1
endmodule

/* Test case Logic Tests:
              opcode control A B C nz-in out vout zout nz-out n
              # XOR
              0x3C 21 0xAA 0xCC 0 0 0x66 x 0 x 0
              # AND
              0xC0 21 0xFF 0xAA 0 0 0xAA x 0 x 1
            
*/

/* Test case Arithmetic Tests:
              opcode control A B C nz-in out vout zout nz-out n
              # ADD
              0x96 21 15 25 0 0 40 0 0 x 0
              # SUB
              0x96 29 50 20 1 0 30 0 0 x 0
            
*/

/* Test case Hardware Accelerators:
              opcode control A B C nz-in out vout zout nz-out n
              # FF1 (Find First 1)
              0x50 25 0xB8 0 0 0 0x08 0 0 x 0
            
*/
