// Digital circuit alu-control.dig as structural Verilog
module alu_control (
  input  [9:0] op,
  output [7:0] lutA,
  output [2:0] csel,
  output flag_we,
  output [7:0] lutB,
  output [1:0] shift_op,
  output mul_div_en,
  output pc_enc
);

  ROM #(.bigEndian("true"), .AddrBits(10), .Bits(8)) alu_control (.A(op), .sel(1'b1), .D(lutA));
  ROM #(.bigEndian("true"), .AddrBits(10), .Bits(8)) alu_control_2 (.A(op), .sel(1'b1), .D(lutB));
  ROM #(.bigEndian("true"), .AddrBits(10), .Bits(8)) alu_shift_control (
    .A(op), .sel(1'b1), .D({pc_enc, mul_div_en, shift_op, flag_we, csel}));

  // Other names for the same wires on the sheet: ir_opcode[9:0] = op

  // Notes on the sheet:
  //   op: default 48
  //   alu_control loads alu_control_1.hex
  //   alu_control_2 loads alu_control_1.hex
  //   alu_shift_control loads alu_control_2.hex
endmodule
