// Digital circuit alu-display-control.dig as structural Verilog
module alu_display_control (
  input  [31:0] Data_A,
  input  [31:0] Data_B,
  input  [31:0] Data_C,
  input  [31:0] Data_W,
  input  clk
);

  wire count0, count1, count2, count3, count4, d0, d1, d2, d3, d4, d5, d6, d7, decoder_1_out_8, q0, q1, q2,
       q3, q4, q5, q6, q7, regA0, regA1, regA2, regA3, regA4, regA5, regA6, regA7, regB0, regB1, regB2,
       regB3, regB4, regB5, regB6, regB7, regC0, regC1, regC2, regC3, regC4, regC5, regC6, regC7, regW0,
       regW1, regW2, regW3, regW4, regW5, regW6, regW7;
  wire [2:2] sel1, sel2, sel3;
  wire [3:0] mux, register_1_q, register_2_q, register_3_q, register_4_q, register_5_q, register_6_q,
       register_7_q, register_8_q, register_9_q, register_10_q, register_11_q, register_12_q, register_13_q,
       register_14_q, register_15_q, register_16_q, register_17_q, register_18_q, register_19_q,
       register_20_q, register_21_q, register_22_q, register_23_q, register_24_q, register_25_q,
       register_26_q, register_27_q, register_28_q, register_29_q, register_30_q, register_31_q;
  wire [7:4] register_1_q_2, register_2_q_2, register_3_q_2, register_4_q_2, register_5_q_2, register_6_q_2,
       register_7_q_2, register_8_q_2, register_9_q_2, register_10_q_2, register_11_q_2, register_12_q_2,
       register_13_q_2, register_14_q_2, register_15_q_2, register_16_q_2, register_17_q_2, register_18_q_2,
       register_19_q_2, register_20_q_2, register_21_q_2, register_22_q_2, register_23_q_2, register_24_q_2,
       register_25_q_2, register_26_q_2, register_27_q_2, register_28_q_2, register_29_q_2, register_30_q_2,
       register_31_q_2;

  not not_1 (sel1[2], count2);
  not not_2 (sel2[2], count3);
  not not_3 (sel3[2], count4);
  Counter #(.Bits(5)) counter_1 (
    .en(1'b1), .C(clk), .clr(1'b0), .out({count4, count3, count2, count1, count0}));  // open: ovf
  Decoder #(.Selector_Bits(5)) decoder_1 (
    .sel({count4, count3, count2, count1, count0}), .out_0(regA0), .out_1(regA1), .out_2(regA2),
    .out_3(regA3), .out_4(regA4), .out_5(regA5), .out_6(regA6), .out_7(regA7), .out_8(decoder_1_out_8),
    .out_9(regB1), .out_10(regB2), .out_11(regB3), .out_12(regB4), .out_13(regB5), .out_14(regB6),
    .out_15(regB7), .out_16(regC0), .out_17(regC1), .out_18(regC2), .out_19(regC3), .out_20(regC4),
    .out_21(regC5), .out_22(regC6), .out_23(regC7), .out_24(regW0), .out_25(regW1), .out_26(regW2),
    .out_27(regW3), .out_28(regW4), .out_29(regW5), .out_30(regW6), .out_31(regW7));
  not not_4 (regB0, decoder_1_out_8);
  Multiplexer #(.Bits(4), .Selector_Bits(3)) multiplexer_1 (
    .sel({count2, count1, count0}), .in_0(Data_A[3:0]), .in_1(Data_A[7:4]), .in_2(Data_A[11:8]),
    .in_3(Data_A[15:12]), .in_4(Data_A[19:16]), .in_5(Data_A[23:20]), .in_6(Data_A[27:24]),
    .in_7(Data_A[31:28]), .out(mux));
  Multiplexer #(.Selector_Bits(3), .Bits(4)) multiplexer_2 (
    .sel({sel1[2], count1, count0}), .in_0(Data_B[3:0]), .in_1(Data_B[7:4]), .in_2(Data_B[11:8]),
    .in_3(Data_B[15:12]), .in_4(Data_B[19:16]), .in_5(Data_B[23:20]), .in_6(Data_B[27:24]),
    .in_7(Data_B[31:28]), .out(mux));
  Multiplexer #(.Selector_Bits(3), .Bits(4)) multiplexer_3 (
    .sel({sel2[2], count1, count0}), .in_0(Data_C[3:0]), .in_1(Data_C[7:4]), .in_2(Data_C[11:8]),
    .in_3(Data_C[15:12]), .in_4(Data_C[19:16]), .in_5(Data_C[23:20]), .in_6(Data_C[27:24]),
    .in_7(Data_C[31:28]), .out(mux));
  Multiplexer #(.Selector_Bits(3), .Bits(4)) multiplexer_4 (
    .sel({sel3[2], count1, count0}), .in_0(Data_W[3:0]), .in_1(Data_W[7:4]), .in_2(Data_W[11:8]),
    .in_3(Data_W[15:12]), .in_4(Data_W[19:16]), .in_5(Data_W[23:20]), .in_6(Data_W[27:24]),
    .in_7(Data_W[31:28]), .out(mux));
  Register #(.Bits(8)) register_1 (
    .D({d7, d6, d5, d4, d3, d2, d1, d0}), .C(clk), .en(regA7), .Q({register_1_q_2, register_1_q}));
  Seven_Seg seven_seg_1 (
    .a(register_2_q[0]), .b(register_2_q[1]), .c(register_2_q[2]), .d(register_2_q[3]),
    .e(register_2_q_2[4]), .f(register_2_q_2[5]), .g(register_2_q_2[6]), .dp(register_2_q_2[7]));
  Register #(.Bits(8)) register_2 (
    .D({d7, d6, d5, d4, d3, d2, d1, d0}), .C(clk), .en(regB7), .Q({register_2_q_2, register_2_q}));
  Seven_Seg seven_seg_2 (
    .a(register_1_q[0]), .b(register_1_q[1]), .c(register_1_q[2]), .d(register_1_q[3]),
    .e(register_1_q_2[4]), .f(register_1_q_2[5]), .g(register_1_q_2[6]), .dp(register_1_q_2[7]));
  Register #(.Bits(8)) register_3 (
    .D({d7, d6, d5, d4, d3, d2, d1, d0}), .C(clk), .en(regB6), .Q({register_3_q_2, register_3_q}));
  Seven_Seg seven_seg_3 (
    .a(register_4_q[0]), .b(register_4_q[1]), .c(register_4_q[2]), .d(register_4_q[3]),
    .e(register_4_q_2[4]), .f(register_4_q_2[5]), .g(register_4_q_2[6]), .dp(register_4_q_2[7]));
  Register #(.Bits(8)) register_4 (
    .D({d7, d6, d5, d4, d3, d2, d1, d0}), .C(clk), .en(regA6), .Q({register_4_q_2, register_4_q}));
  Seven_Seg seven_seg_4 (
    .a(register_3_q[0]), .b(register_3_q[1]), .c(register_3_q[2]), .d(register_3_q[3]),
    .e(register_3_q_2[4]), .f(register_3_q_2[5]), .g(register_3_q_2[6]), .dp(register_3_q_2[7]));
  ROM #(.bigEndian("true"), .AddrBits(13), .Bits(8)) display_rom_1 (
    .A({{9{1'b0}}, mux}), .sel(1'b1), .D({d7, d6, d5, d4, d3, d2, d1, d0}));
  Register #(.Bits(8)) register_5 (
    .D({d7, d6, d5, d4, d3, d2, d1, d0}), .C(clk), .en(regA5), .Q({register_5_q_2, register_5_q}));
  Seven_Seg seven_seg_5 (
    .a(register_6_q[0]), .b(register_6_q[1]), .c(register_6_q[2]), .d(register_6_q[3]),
    .e(register_6_q_2[4]), .f(register_6_q_2[5]), .g(register_6_q_2[6]), .dp(register_6_q_2[7]));
  Register #(.Bits(8)) register_6 (
    .D({d7, d6, d5, d4, d3, d2, d1, d0}), .C(clk), .en(regB5), .Q({register_6_q_2, register_6_q}));
  Seven_Seg seven_seg_6 (
    .a(register_5_q[0]), .b(register_5_q[1]), .c(register_5_q[2]), .d(register_5_q[3]),
    .e(register_5_q_2[4]), .f(register_5_q_2[5]), .g(register_5_q_2[6]), .dp(register_5_q_2[7]));
  Register #(.Bits(8)) register_7 (
    .D({d7, d6, d5, d4, d3, d2, d1, d0}), .C(clk), .en(regB4), .Q({register_7_q_2, register_7_q}));
  Seven_Seg seven_seg_7 (
    .a(register_8_q[0]), .b(register_8_q[1]), .c(register_8_q[2]), .d(register_8_q[3]),
    .e(register_8_q_2[4]), .f(register_8_q_2[5]), .g(register_8_q_2[6]), .dp(register_8_q_2[7]));
  Register #(.Bits(8)) register_8 (
    .D({d7, d6, d5, d4, d3, d2, d1, d0}), .C(clk), .en(regA4), .Q({register_8_q_2, register_8_q}));
  Seven_Seg seven_seg_8 (
    .a(register_7_q[0]), .b(register_7_q[1]), .c(register_7_q[2]), .d(register_7_q[3]),
    .e(register_7_q_2[4]), .f(register_7_q_2[5]), .g(register_7_q_2[6]), .dp(register_7_q_2[7]));
  Register #(.Bits(8)) register_9 (
    .D({d7, d6, d5, d4, d3, d2, d1, d0}), .C(clk), .en(regA3), .Q({register_9_q_2, register_9_q}));
  Seven_Seg seven_seg_9 (
    .a(register_10_q[0]), .b(register_10_q[1]), .c(register_10_q[2]), .d(register_10_q[3]),
    .e(register_10_q_2[4]), .f(register_10_q_2[5]), .g(register_10_q_2[6]), .dp(register_10_q_2[7]));
  Register #(.Bits(8)) register_10 (
    .D({d7, d6, d5, d4, d3, d2, d1, d0}), .C(clk), .en(regB3), .Q({register_10_q_2, register_10_q}));
  Seven_Seg seven_seg_10 (
    .a(register_9_q[0]), .b(register_9_q[1]), .c(register_9_q[2]), .d(register_9_q[3]),
    .e(register_9_q_2[4]), .f(register_9_q_2[5]), .g(register_9_q_2[6]), .dp(register_9_q_2[7]));
  Register #(.Bits(8)) register_11 (
    .D({d7, d6, d5, d4, d3, d2, d1, d0}), .C(clk), .en(regB2), .Q({register_11_q_2, register_11_q}));
  Seven_Seg seven_seg_11 (
    .a(register_12_q[0]), .b(register_12_q[1]), .c(register_12_q[2]), .d(register_12_q[3]),
    .e(register_12_q_2[4]), .f(register_12_q_2[5]), .g(register_12_q_2[6]), .dp(register_12_q_2[7]));
  Register #(.Bits(8)) register_12 (
    .D({d7, d6, d5, d4, d3, d2, d1, d0}), .C(clk), .en(regA2), .Q({register_12_q_2, register_12_q}));
  Seven_Seg seven_seg_12 (
    .a(register_11_q[0]), .b(register_11_q[1]), .c(register_11_q[2]), .d(register_11_q[3]),
    .e(register_11_q_2[4]), .f(register_11_q_2[5]), .g(register_11_q_2[6]), .dp(register_11_q_2[7]));
  Register #(.Bits(8)) register_13 (
    .D({d7, d6, d5, d4, d3, d2, d1, d0}), .C(clk), .en(regA1), .Q({register_13_q_2, register_13_q}));
  Seven_Seg seven_seg_13 (
    .a(register_14_q[0]), .b(register_14_q[1]), .c(register_14_q[2]), .d(register_14_q[3]),
    .e(register_14_q_2[4]), .f(register_14_q_2[5]), .g(register_14_q_2[6]), .dp(register_14_q_2[7]));
  Register #(.Bits(8)) register_14 (
    .D({d7, d6, d5, d4, d3, d2, d1, d0}), .C(clk), .en(regB1), .Q({register_14_q_2, register_14_q}));
  Seven_Seg seven_seg_14 (
    .a(register_13_q[0]), .b(register_13_q[1]), .c(register_13_q[2]), .d(register_13_q[3]),
    .e(register_13_q_2[4]), .f(register_13_q_2[5]), .g(register_13_q_2[6]), .dp(register_13_q_2[7]));
  Seven_Seg seven_seg_15 (
    .a(register_15_q[0]), .b(register_15_q[1]), .c(register_15_q[2]), .d(register_15_q[3]),
    .e(register_15_q_2[4]), .f(register_15_q_2[5]), .g(register_15_q_2[6]), .dp(register_15_q_2[7]));
  Register #(.Bits(8)) register_15 (
    .D({d7, d6, d5, d4, d3, d2, d1, d0}), .C(clk), .en(regA0), .Q({register_15_q_2, register_15_q}));
  Seven_Seg seven_seg_16 (.a(q0), .b(q1), .c(q2), .d(q3), .e(q4), .f(q5), .g(q6), .dp(q7));
  _74377 _74377_1 (
    .pin1(regB0), .pin2(q0), .pin3(d0), .pin4(d1), .pin5(q1), .pin6(q2), .pin7(d2), .pin8(d3), .pin9(q3),
    .pin10(1'b0), .pin11(clk), .pin12(q4), .pin13(d4), .pin14(d5), .pin15(q5), .pin16(q6), .pin17(d6),
    .pin18(d7), .pin19(q7), .pin20(1'b1));
  Register #(.Bits(8)) register_16 (
    .D({d7, d6, d5, d4, d3, d2, d1, d0}), .C(clk), .en(regC7), .Q({register_16_q_2, register_16_q}));
  Seven_Seg seven_seg_17 (
    .a(register_17_q[0]), .b(register_17_q[1]), .c(register_17_q[2]), .d(register_17_q[3]),
    .e(register_17_q_2[4]), .f(register_17_q_2[5]), .g(register_17_q_2[6]), .dp(register_17_q_2[7]));
  Register #(.Bits(8)) register_17 (
    .D({d7, d6, d5, d4, d3, d2, d1, d0}), .C(clk), .en(regW7), .Q({register_17_q_2, register_17_q}));
  Seven_Seg seven_seg_18 (
    .a(register_16_q[0]), .b(register_16_q[1]), .c(register_16_q[2]), .d(register_16_q[3]),
    .e(register_16_q_2[4]), .f(register_16_q_2[5]), .g(register_16_q_2[6]), .dp(register_16_q_2[7]));
  Register #(.Bits(8)) register_18 (
    .D({d7, d6, d5, d4, d3, d2, d1, d0}), .C(clk), .en(regW6), .Q({register_18_q_2, register_18_q}));
  Seven_Seg seven_seg_19 (
    .a(register_19_q[0]), .b(register_19_q[1]), .c(register_19_q[2]), .d(register_19_q[3]),
    .e(register_19_q_2[4]), .f(register_19_q_2[5]), .g(register_19_q_2[6]), .dp(register_19_q_2[7]));
  Register #(.Bits(8)) register_19 (
    .D({d7, d6, d5, d4, d3, d2, d1, d0}), .C(clk), .en(regC6), .Q({register_19_q_2, register_19_q}));
  Seven_Seg seven_seg_20 (
    .a(register_18_q[0]), .b(register_18_q[1]), .c(register_18_q[2]), .d(register_18_q[3]),
    .e(register_18_q_2[4]), .f(register_18_q_2[5]), .g(register_18_q_2[6]), .dp(register_18_q_2[7]));
  Register #(.Bits(8)) register_20 (
    .D({d7, d6, d5, d4, d3, d2, d1, d0}), .C(clk), .en(regC5), .Q({register_20_q_2, register_20_q}));
  Seven_Seg seven_seg_21 (
    .a(register_21_q[0]), .b(register_21_q[1]), .c(register_21_q[2]), .d(register_21_q[3]),
    .e(register_21_q_2[4]), .f(register_21_q_2[5]), .g(register_21_q_2[6]), .dp(register_21_q_2[7]));
  Register #(.Bits(8)) register_21 (
    .D({d7, d6, d5, d4, d3, d2, d1, d0}), .C(clk), .en(regW5), .Q({register_21_q_2, register_21_q}));
  Seven_Seg seven_seg_22 (
    .a(register_20_q[0]), .b(register_20_q[1]), .c(register_20_q[2]), .d(register_20_q[3]),
    .e(register_20_q_2[4]), .f(register_20_q_2[5]), .g(register_20_q_2[6]), .dp(register_20_q_2[7]));
  Register #(.Bits(8)) register_22 (
    .D({d7, d6, d5, d4, d3, d2, d1, d0}), .C(clk), .en(regW4), .Q({register_22_q_2, register_22_q}));
  Seven_Seg seven_seg_23 (
    .a(register_23_q[0]), .b(register_23_q[1]), .c(register_23_q[2]), .d(register_23_q[3]),
    .e(register_23_q_2[4]), .f(register_23_q_2[5]), .g(register_23_q_2[6]), .dp(register_23_q_2[7]));
  Register #(.Bits(8)) register_23 (
    .D({d7, d6, d5, d4, d3, d2, d1, d0}), .C(clk), .en(regC4), .Q({register_23_q_2, register_23_q}));
  Seven_Seg seven_seg_24 (
    .a(register_22_q[0]), .b(register_22_q[1]), .c(register_22_q[2]), .d(register_22_q[3]),
    .e(register_22_q_2[4]), .f(register_22_q_2[5]), .g(register_22_q_2[6]), .dp(register_22_q_2[7]));
  Register #(.Bits(8)) register_24 (
    .D({d7, d6, d5, d4, d3, d2, d1, d0}), .C(clk), .en(regC3), .Q({register_24_q_2, register_24_q}));
  Seven_Seg seven_seg_25 (
    .a(register_25_q[0]), .b(register_25_q[1]), .c(register_25_q[2]), .d(register_25_q[3]),
    .e(register_25_q_2[4]), .f(register_25_q_2[5]), .g(register_25_q_2[6]), .dp(register_25_q_2[7]));
  Register #(.Bits(8)) register_25 (
    .D({d7, d6, d5, d4, d3, d2, d1, d0}), .C(clk), .en(regW3), .Q({register_25_q_2, register_25_q}));
  Seven_Seg seven_seg_26 (
    .a(register_24_q[0]), .b(register_24_q[1]), .c(register_24_q[2]), .d(register_24_q[3]),
    .e(register_24_q_2[4]), .f(register_24_q_2[5]), .g(register_24_q_2[6]), .dp(register_24_q_2[7]));
  Register #(.Bits(8)) register_26 (
    .D({d7, d6, d5, d4, d3, d2, d1, d0}), .C(clk), .en(regW2), .Q({register_26_q_2, register_26_q}));
  Seven_Seg seven_seg_27 (
    .a(register_27_q[0]), .b(register_27_q[1]), .c(register_27_q[2]), .d(register_27_q[3]),
    .e(register_27_q_2[4]), .f(register_27_q_2[5]), .g(register_27_q_2[6]), .dp(register_27_q_2[7]));
  Register #(.Bits(8)) register_27 (
    .D({d7, d6, d5, d4, d3, d2, d1, d0}), .C(clk), .en(regC2), .Q({register_27_q_2, register_27_q}));
  Seven_Seg seven_seg_28 (
    .a(register_26_q[0]), .b(register_26_q[1]), .c(register_26_q[2]), .d(register_26_q[3]),
    .e(register_26_q_2[4]), .f(register_26_q_2[5]), .g(register_26_q_2[6]), .dp(register_26_q_2[7]));
  Register #(.Bits(8)) register_28 (
    .D({d7, d6, d5, d4, d3, d2, d1, d0}), .C(clk), .en(regC1), .Q({register_28_q_2, register_28_q}));
  Seven_Seg seven_seg_29 (
    .a(register_29_q[0]), .b(register_29_q[1]), .c(register_29_q[2]), .d(register_29_q[3]),
    .e(register_29_q_2[4]), .f(register_29_q_2[5]), .g(register_29_q_2[6]), .dp(register_29_q_2[7]));
  Register #(.Bits(8)) register_29 (
    .D({d7, d6, d5, d4, d3, d2, d1, d0}), .C(clk), .en(regW1), .Q({register_29_q_2, register_29_q}));
  Seven_Seg seven_seg_30 (
    .a(register_28_q[0]), .b(register_28_q[1]), .c(register_28_q[2]), .d(register_28_q[3]),
    .e(register_28_q_2[4]), .f(register_28_q_2[5]), .g(register_28_q_2[6]), .dp(register_28_q_2[7]));
  Register #(.Bits(8)) register_30 (
    .D({d7, d6, d5, d4, d3, d2, d1, d0}), .C(clk), .en(regW0), .Q({register_30_q_2, register_30_q}));
  Seven_Seg seven_seg_31 (
    .a(register_31_q[0]), .b(register_31_q[1]), .c(register_31_q[2]), .d(register_31_q[3]),
    .e(register_31_q_2[4]), .f(register_31_q_2[5]), .g(register_31_q_2[6]), .dp(register_31_q_2[7]));
  Register #(.Bits(8)) register_31 (
    .D({d7, d6, d5, d4, d3, d2, d1, d0}), .C(clk), .en(regC0), .Q({register_31_q_2, register_31_q}));
  Seven_Seg seven_seg_32 (
    .a(register_30_q[0]), .b(register_30_q[1]), .c(register_30_q[2]), .d(register_30_q[3]),
    .e(register_30_q_2[4]), .f(register_30_q_2[5]), .g(register_30_q_2[6]), .dp(register_30_q_2[7]));

  // Other names for the same wires on the sheet: count_n[4:0] = {count4, count3, count2, count1, count0};
  //   sel0[2:0] = {count2, count1, count0}; sel1[1:0] = {count1, count0}; sel2[1:0] = {count1, count0};
  //   sel3[1:0] = {count1, count0}; din[7:0] = {d7, d6, d5, d4, d3, d2, d1, d0}

  // Notes on the sheet:
  //   Data_A: default 3735928559
  //   Data_B: default 3134268229
  //   Data_C: default 305419896
  //   Data_W: default 2554539437
  //   clk: Hz: 600
  //   contents of display_rom_1 (hex, n*v repeats v):
  //   11
endmodule
