// Digital circuit bus-arbitration.dig as structural Verilog
module bus_arbitration (
  input  FETCH,
  input  [21:0] IR_ADDR,
  input  MEM_RD_IN,
  input  [2:0] addr_sel,
  input  [31:0] Reg_b,
  input  [23:0] Pc_out,
  input  [23:0] SP_out,
  input  [31:0] Alu_in,
  output [23:0] ADDR_BUS,
  output MEM_RD_OUT
);

  wire [23:0] addr_mux_out;

  or or_1 (MEM_RD_OUT, MEM_RD_IN, FETCH);
  Multiplexer #(.Selector_Bits(3), .Bits(24)) multiplexer_1 (
    .sel(addr_sel), .in_0({2'b00, IR_ADDR}), .in_1(Alu_in[23:0]), .in_2(Reg_b[23:0]), .in_3(Pc_out),
    .in_4({24{1'b0}}), .in_5({24{1'b0}}), .in_6({24{1'b0}}), .in_7(SP_out), .out(addr_mux_out));
  Multiplexer #(.Selector_Bits(1), .Bits(24)) multiplexer_2 (
    .sel(FETCH), .in_0(addr_mux_out), .in_1(Pc_out), .out(ADDR_BUS));

  // Other names for the same wires on the sheet: alu_out[23:0] = Alu_in[23:0]; ir_addr_t[21:0] = IR_ADDR;
  //   reg_b_t[23:0] = Reg_b[23:0]
endmodule

/* Test case bus-arbitration-exhaustive:
FETCH MEM_RD_IN addr_sel IR_ADDR Alu-in Reg_b Pc-out SP-out ADDR_BUS MEM_RD_OUT

# 1. Test ADDR_BUS routing based on addr_sel (0-7)
0 0 0 0x111111 0x22222222 0x33333333 0x444444 0x777777 0x111111 0
0 0 1 0x111111 0x22222222 0x33333333 0x444444 0x777777 0x222222 0
0 0 2 0x111111 0x22222222 0x33333333 0x444444 0x777777 0x333333 0
0 0 3 0x111111 0x22222222 0x33333333 0x444444 0x777777 0x444444 0
0 0 4 0x111111 0x22222222 0x33333333 0x444444 0x777777 0x000000 0
0 0 5 0x111111 0x22222222 0x33333333 0x444444 0x777777 0x000000 0
0 0 6 0x111111 0x22222222 0x33333333 0x444444 0x777777 0x000000 0
0 0 7 0x111111 0x22222222 0x33333333 0x444444 0x777777 0x777777 0

# 2. Test MEM_RD_OUT logic (MEM_RD_OUT = MEM_RD_IN | FETCH)
0 0 0 0 0 0 0 0 0 0
0 1 0 0 0 0 0 0 0 1
1 0 0 0 0 0 0 0 0 1
1 1 0 0 0 0 0 0 0 1

# 3. FETCH forces Pc-out on ADDR_BUS (instruction fetch must track PC)
1 0 0 0xDEADBE 0x11111111 0x22222222 0x000004 0x777777 0x000004 1
1 0 3 0x111111 0x22222222 0x33333333 0x000010 0x777777 0x000010 1
1 1 1 0x111111 0x22222222 0x33333333 0x000020 0x777777 0x000020 1
*/
