// Digital circuit ir-reg-control.dig as structural Verilog
module ir_reg_control (
  input  [9:0] op,
  output [3:0] ir_imm_sel,
  output [2:0] wb_sel,
  output reg_we
);

  ROM #(.bigEndian("true"), .AddrBits(10), .Bits(8)) ir_reg_control (
    .A(op), .sel(1'b1), .D({reg_we, wb_sel, ir_imm_sel}));

  // Other names for the same wires on the sheet: ir_opcode[9:0] = op

  // Notes on the sheet:
  //   op: default 48
  //   ir_reg_control loads ir_reg_control.hex
endmodule
