// Digital circuit main.dig as structural Verilog
module main (
  input  clk,
  input  reset,
  output [23:0] pc_out,
  output [31:0] mem_din,
  output [31:0] ir_bus,
  output [21:0] ir_offset,
  output [21:0] ir_addr,
  output [5:0] ir_addr_w,
  output [5:0] ir_addr_b,
  output [2:0] wb_sel,
  output [9:0] ir_opcode,
  output [7:0] ctrl_alu_op,
  output [31:0] alu_out,
  output [31:0] reg_w_data,
  output [31:0] p,
  output [15:0] term_data,
  output [15:0] vram_addr,
  output term_we,
  output [23:0] pc_save,
  output [31:0] m_out,
  output [23:0] mem_addr,
  output [2:0] ctrl_w_sel,
  output [31:0] reg_b,
  output [31:0] reg_a,
  output ctrl_reg_we,
  output [5:0] ir_addr_a,
  output [3:0] ir_sel
);

  wire alu_cout, alu_nout, alu_nzout, alu_vout, alu_zout, and_1_out, bank_en, comparator_1_eq,
       comparator_2_eq, ctrl_branch_en, ctrl_bus_sel, ctrl_byte_sel, ctrl_cin_sel, ctrl_cycles,
       ctrl_flags_we, ctrl_jump_type, ctrl_mem_rd, ctrl_mem_wr, ctrl_pc_link_WE, ctrl_pc_src, ctrl_sp_out,
       flag_c, flag_n, flag_v, flag_z, HALT_IN, is_mmio, mem_rd_out, ram_cs, seq_exec, seq_fetch, sp_out,
       vram_we;
  wire [1:0] c_addr_msb2, ctrl_mem_sel, ctrl_shift_op;
  wire [2:0] cond;
  wire [3:0] BANK_SEL;
  wire [4:0] ctrl_alu_pre;
  wire [15:0] vram_data;
  wire [23:0] CPU_ADDR_OUT, mmio_addr;
  wire [31:0] io_data_in, mem_in, mul_out, reg_c, shift_out;

  // program_counter program_counter_1: pin names not known; wires that end beside it: mem_din, alu_out, ctrl_pc_src, ir_offset, reset, ctrl_cycles, clk, flag_n, flag_c, flag_z, flag_v, cond, ctrl_jump_type, ctrl_branch_en, 1'b0, HALT_IN, 1'b0, 1'b0, 1'b0, 1'b0, ctrl_pc_link_WE, pc_out, pc_save, seq_fetch, seq_exec
  register register_1 (
    .WE(ctrl_reg_we), .DATA_W(reg_w_data), .ADDR_A(ir_addr_a), .ADDR_B(ir_addr_b), .ADDR_W(ir_addr_w),
    .EXEC(seq_exec), .clk(clk), .BANK_SEL(BANK_SEL), .Bank_en(bank_en), .DATA_A(reg_a), .DATA_B(reg_b),
    .DATA_C(reg_c));
  store_mux store_mux_1 (
    .reg_a(reg_a), .alu_out(alu_out), .pc_save(pc_save), .reg_b(reg_b), .mem_sel(ctrl_mem_sel),
    .mem_mux(mem_in));
  ir ir_1 (
    .DATA_IN(mem_din), .LOAD(seq_fetch), .CLK(clk), .ir_sel(ir_sel), .RegB(reg_b), .OPCODE(ir_opcode),
    .ADDR_A(ir_addr_a), .ADDR_B(ir_addr_b), .ADDR_W(ir_addr_w), .ADDR_ABS(ir_addr), .OFFSET(ir_offset),
    .COND(cond), .ir_imm_out(ir_bus), .BANK_SEL(BANK_SEL));  // open: MUX1_SEL, MUX2_SEL
  // bus_arbitration bus_arbitration_1: pin names not known; wires that end beside it: seq_fetch, ir_addr, ctrl_mem_rd, ctrl_bus_sel, reg_b, pc_out, sp_out, alu_out, mem_addr, mem_rd_out
  io_controller io_controller_1 (
    .mem_addr(mmio_addr), .c_wr(ctrl_mem_wr), .kb_data(16'h1), .mem_data_out(mem_in),
    .io_data_in(io_data_in), .ram_cs(ram_cs), .vram_we(vram_we), .vram_addr(vram_addr),
    .vram_data(vram_data), .term_we(term_we), .term_data(term_data));
  EEPROMDualPort #(.AddrBits(24), .Bits(32)) eepromdualport_1 (
    .A(CPU_ADDR_OUT), .Din(mem_in), .str(ctrl_mem_wr), .C(clk), .ld(mem_rd_out), .D(m_out));
  // microcode microcode_1: pin names not known; wires that end beside it: ir_opcode, ctrl_alu_op, ctrl_alu_pre, ctrl_cin_sel, ctrl_shift_op, ir_sel, bank_en, ctrl_w_sel, ctrl_reg_we, ctrl_flags_we, ctrl_mem_rd, ctrl_mem_wr, ctrl_byte_sel, ctrl_branch_en, ctrl_jump_type, ctrl_pc_src, ctrl_sp_out, ctrl_cycles, ctrl_bus_sel, ctrl_pc_link_WE, ctrl_mem_sel
  mmio_bus mmio_bus_1 (
    .ADDR(mem_addr), .CPU_ADDR_OUT(CPU_ADDR_OUT), .mmio_addr(mmio_addr), .is_mmio(is_mmio),
    .cpu_addr_msb2(c_addr_msb2));
  Comparator #(.Bits(6)) comparator_1 (.a(6'b000010), .b(ir_addr_w), .eq(comparator_1_eq));  // open: gt, lt
  // mul_div mul_div_1: pin names not known; wires that end beside it: reg_a, ir_bus, mul_out
  // byte_lane_decoder byte_lane_decoder_1: pin names not known; wires that end beside it: m_out, ctrl_byte_sel, io_data_in, c_addr_msb2, mem_din
  and and_1 (and_1_out, seq_exec, ctrl_reg_we, comparator_1_eq);
  shift shift_1 (.A(reg_a), .mode(ctrl_shift_op), .B(ir_bus), .Out(shift_out));
  alu_32b_final alu_32b_final_1 (
    .A(reg_a), .nz0(1'b0), .B(ir_bus), .Opcode(ctrl_alu_op), .control(ctrl_alu_pre), .REG_C(reg_c),
    .cin_sel(ctrl_cin_sel), .FLAG_C(flag_c), .vout(alu_vout), .zout(alu_zout), .nzout(alu_nzout),
    .nout(alu_nout), .Out(alu_out), .cout(alu_cout));
  flag_reg flag_reg_1 (
    .ZERO_IN(alu_zout), .CARRY_IN(alu_cout), .NEGATIVE_IN(alu_nout), .OVERFLOW_IN(alu_vout),
    .FLAG_WE(ctrl_flags_we), .CLK(clk), .EXEC(seq_exec), .FLAG_Z(flag_z), .FLAG_C(flag_c), .FLAG_N(flag_n),
    .FLAG_O(flag_v));
  wb_mux wb_mux_1 (
    .wb_sel(ctrl_w_sel), .alu_out(alu_out), .shift_out(shift_out), .pc_save(pc_save), .mem_din(io_data_in),
    .io_datain(reg_a), .reg_a(ir_bus), .ir_bus(mul_out), .reg_w_data(reg_w_data));
  // sp sp_1: pin names not known; wires that end beside it: mem_din, ctrl_sp_out, clk, reset, alu_out, seq_exec, sp_out
  Register #(.Bits(32)) register_2 (.D(reg_w_data), .C(clk), .en(and_1_out), .Q(p));
  and and_2 (HALT_IN, comparator_2_eq, seq_exec);
  Comparator #(.Bits(10)) comparator_2 (.a(10'hff), .b(ir_opcode), .eq(comparator_2_eq));  // open: gt, lt

  assign wb_sel = ctrl_w_sel;

  // Other names for the same wires on the sheet: ctrl_wb_sel[2:0] = ctrl_w_sel; mem_ram_out[31:0] = m_out

  // Notes on the sheet:
  //   contents of eepromdualport_1 (hex, n*v repeats v):
  //   10203,1010203,2010203,3010203,4010203,5010203,6010203,7010203
  //   ,8010203,9010203,a010203,b010203,c010203,d010203,e010203,f010203
  //   ,10011003,11011003,120100ff,130100ff,140100ff,150100ff,16015003
  //   ,170100ff,18011003,19001233,19001233,1b2af343,1c015003,1d0100ff
  //   ,1e010203,1f010203,20010203,21010203,22010203,23010203,24010003
  //   ,25010003,26010003,27010003,30011003,31011003,32011003,33011003
  //   ,34011003,35010203,40011003,41011003,42011003,43010203,50010300
  //   ,51010300,52010300,53010300,54010300,55010300,56010300,57010300
  //   ,60011000,61011003,62000200,63010203,64010203,70010203,71010203
  //   ,72011000,73010203,80010203,81010203,82010203,83010203,84010203
  //   ,850100ff,90010203,91010203,92010203,93010203,a0010203,a1010203
  //   ,a2010203,ff010203
endmodule

/* Test case mc-branch:
reset clk alu-out ir-opcode ctrl-alu-op ctrl-reg-we
# auto-generated mc-branch — microcode dispatch via main.dig
# Assert ir-opcode + ctrl-alu-op + ctrl-reg-we on EXECUTE for each native op
# NOP (0x00)
1 0 x x x x
1 1 x x x x
1 0 x x x x
1 1 x x x x
# ADD (0x01)
1 0 x x x x
1 1 x x x x
1 0 x x x x
1 1 x x x x
# SUB (0x02)
1 0 x x x x
1 1 x x x x
1 0 x x x x
1 1 x x x x
# AND (0x03)
1 0 x x x x
1 1 x x x x
1 0 x x x x
1 1 x x x x
# OR (0x04)
1 0 x x x x
1 1 x x x x
1 0 x x x x
1 1 x x x x
# XOR (0x05)
1 0 x x x x
1 1 x x x x
1 0 x x x x
1 1 x x x x
# NOT (0x06)
1 0 x x x x
1 1 x x x x
1 0 x x x x
1 1 x x x x
# NEG (0x07)
1 0 x x x x
1 1 x x x x
1 0 x x x x
1 1 x x x x
# ADC (0x08)
1 0 x x x x
1 1 x x x x
1 0 x x x x
1 1 x x x x
# SBC (0x09)
1 0 x x x x
1 1 x x x x
1 0 x x x x
1 1 x x x x
# ANDN (0x0A)
1 0 x x x x
1 1 x x x x
1 0 x x x x
1 1 x x x x
# ORN (0x0B)
1 0 x x x x
1 1 x x x x
1 0 x x x x
1 1 x x x x
# INC (0x0C)
1 0 x x x x
1 1 x x x x
1 0 x x x x
1 1 x x x x
# DEC (0x0D)
1 0 x x x x
1 1 x x x x
1 0 x x x x
1 1 x x x x
# MOV (0x0E)
1 0 x x x x
1 1 x x x x
1 0 x x x x
1 1 x x x x
# CMP (0x0F)
1 0 x x x x
1 1 x x x x
1 0 x x x x
1 1 x x x x
# ADDI (0x10)
1 0 x x x x
1 1 x x x x
1 0 x x x x
1 1 x x x x
# SUBI (0x11)
1 0 x x x x
1 1 x x x x
1 0 x x x x
1 1 x x x x
# ANDI (0x12)
1 0 x x x x
1 1 x x x x
1 0 x x x x
1 1 x x x x
# ORI (0x13)
1 0 x x x x
1 1 x x x x
1 0 x x x x
1 1 x x x x
# XORI (0x14)
1 0 x x x x
1 1 x x x x
1 0 x x x x
1 1 x x x x
# ADDI16 (0x15)
1 0 x x x x
1 1 x x x x
1 0 x x x x
1 1 x x x x
# ADDI8 (0x16)
1 0 x x x x
1 1 x x x x
1 0 x x x x
1 1 x x x x
# TST (0x17)
1 0 x x x x
1 1 x x x x
1 0 x x x x
1 1 x x x x
# CMPI (0x18)
1 0 x x x x
1 1 x x x x
1 0 x x x x
1 1 x x x x
# LUI (0x19)
1 0 x x x x
1 1 x x x x
1 0 x x x x
1 1 x x x x
# AUIPC (0x1A)
1 0 x x x x
1 1 x x x x
1 0 x x x x
1 1 x x x x
# MOVT (0x1B)
1 0 x x x x
1 1 x x x x
1 0 x x x x
1 1 x x x x
# MOVI8 (0x1C)
1 0 x x x x
1 1 x x x x
1 0 x x x x
1 1 x x x x
# MOVI16 (0x1D)
1 0 x x x x
1 1 x x x x
1 0 x x x x
1 1 x x x x
# SLT (0x1E)
1 0 x x x x
1 1 x x x x
1 0 x x x x
1 1 x x x x
# SLTU (0x1F)
1 0 x x x x
1 1 x x x x
1 0 x x x x
1 1 x x x x
# LSL (0x20)
1 0 x x x x
1 1 x x x x
1 0 x x x x
1 1 x x x x
# LSR (0x21)
1 0 x x x x
1 1 x x x x
1 0 x x x x
1 1 x x x x
# ASR (0x22)
1 0 x x x x
1 1 x x x x
1 0 x x x x
1 1 x x x x
# ROR (0x23)
1 0 x x x x
1 1 x x x x
1 0 x x x x
1 1 x x x x
# LSLI (0x24)
1 0 x x x x
1 1 x x x x
1 0 x x x x
1 1 x x x x
# LSRI (0x25)
1 0 x x x x
1 1 x x x x
1 0 x x x x
1 1 x x x x
# ASRI (0x26)
1 0 x x x x
1 1 x x x x
1 0 x x x x
1 1 x x x x
# RORI (0x27)
1 0 x x x x
1 1 x x x x
1 0 x x x x
1 1 x x x x
# LW (0x30)
1 0 x x x x
1 1 x x x x
1 0 x x x x
1 1 x x x x
1 0 x x x x
1 1 x x x x
# LH (0x31)
1 0 x x x x
1 1 x x x x
1 0 x x x x
1 1 x x x x
1 0 x x x x
1 1 x x x x
# LHU (0x32)
1 0 x x x x
1 1 x x x x
1 0 x x x x
1 1 x x x x
1 0 x x x x
1 1 x x x x
# LB (0x33)
1 0 x x x x
1 1 x x x x
1 0 x x x x
1 1 x x x x
1 0 x x x x
1 1 x x x x
# LBU (0x34)
1 0 x x x x
1 1 x x x x
1 0 x x x x
1 1 x x x x
1 0 x x x x
1 1 x x x x
# LW0 (0x35)
1 0 x x x x
1 1 x x x x
1 0 x x x x
1 1 x x x x
# SW (0x40)
1 0 x x x x
1 1 x x x x
1 0 x x x x
1 1 x x x x
1 0 x x x x
1 1 x x x x
# SH (0x41)
1 0 x x x x
1 1 x x x x
1 0 x x x x
1 1 x x x x
1 0 x x x x
1 1 x x x x
# SB (0x42)
1 0 x x x x
1 1 x x x x
1 0 x x x x
1 1 x x x x
1 0 x x x x
1 1 x x x x
# SW0 (0x43)
1 0 x x x x
1 1 x x x x
1 0 x x x x
1 1 x x x x
# BEQ (0x50)
1 0 x x x x
1 1 x x x x
1 0 x x x x
1 1 x 0 0x50 0x00
# BNE (0x51)
1 0 x x x x
1 1 x x x x
1 0 x x x x
1 1 x 0 0x51 0x00
# BLT (0x52)
1 0 x x x x
1 1 x x x x
1 0 x x x x
1 1 x 0 0x52 0x00
# BGE (0x53)
1 0 x x x x
1 1 x x x x
1 0 x x x x
1 1 x 0 0x53 0x00
# BLTU (0x54)
1 0 x x x x
1 1 x x x x
1 0 x x x x
1 1 x 0 0x54 0x00
# BGEU (0x55)
1 0 x x x x
1 1 x x x x
1 0 x x x x
1 1 x 0 0x55 0x00
# BLEZ (0x56)
1 0 x x x x
1 1 x x x x
1 0 x x x x
1 1 x 0 0x56 0x00
# BGTZ (0x57)
1 0 x x x x
1 1 x x x x
1 0 x x x x
1 1 x 0 0x57 0x00
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*/

/* Test case add-arithmetic-only:
reset clk alu-out ir-opcode ctrl-alu-op
1 0 x x x
1 1 x x x
1 0 x x x
# EXECUTE ADDI R0=0: microcode dispatches alu-op=0x96 (XOR3/ADD)
1 1 0 0x10 0x96
1 0 x x x
1 1 x x x
1 0 x x x
# EXECUTE ADDI R1=10: R0+imm=0+10=10
1 1 10 0x10 0x96
1 0 x x x
1 1 x x x
1 0 x x x
# EXECUTE ADDI R2=10: R0+imm=0+10=10
1 1 10 0x10 0x96
1 0 x x x
1 1 x x x
1 0 x x x
# EXECUTE ADD R2+=R1: post-writeback alu-out=R2_new+R1=20+10=30
1 1 30 0x01 0x96
1 0 x x x
1 1 x x x
1 0 x x x
# EXECUTE JMP: ALU unused, ctrl-alu-op=0x00
1 1 x 0x62 0x00
*/

/* Test case load-store-chain:
reset clk alu-out ctrl-reg-we ir-opcode
# Counter loop (picks up mid-run, R2 already at 40 after lw-pipeline test above)
# This is an independent run — 3 more ADD iterations: 20, 30, 40
1 0 x x x
1 1 x x x
1 0 x x x
1 1 x x x
1 0 x x x
1 1 x x x
1 0 x x x
1 1 x x x
1 0 x x x
1 1 x x x
1 0 x x x
1 1 x x x
1 0 x x x
# ADD first iteration: R2=20
1 1 20 1 0x01
1 0 x x x
1 1 x x x
1 0 x x x
1 1 x 0 0x62
1 0 x x x
1 1 x x x
1 0 x x x
# ADD second iteration: R2=30
1 1 30 1 0x01
*/

/* Test case mc-jump-stack:
reset clk alu-out ir-opcode ctrl-alu-op ctrl-reg-we
# auto-generated mc-jump-stack — microcode dispatch via main.dig
# Assert ir-opcode + ctrl-alu-op + ctrl-reg-we on EXECUTE for each native op
# NOP (0x00)
1 0 x x x x
1 1 x x x x
1 0 x x x x
1 1 x x x x
# ADD (0x01)
1 0 x x x x
1 1 x x x x
1 0 x x x x
1 1 x x x x
# SUB (0x02)
1 0 x x x x
1 1 x x x x
1 0 x x x x
1 1 x x x x
# AND (0x03)
1 0 x x x x
1 1 x x x x
1 0 x x x x
1 1 x x x x
# OR (0x04)
1 0 x x x x
1 1 x x x x
1 0 x x x x
1 1 x x x x
# XOR (0x05)
1 0 x x x x
1 1 x x x x
1 0 x x x x
1 1 x x x x
# NOT (0x06)
1 0 x x x x
1 1 x x x x
1 0 x x x x
1 1 x x x x
# NEG (0x07)
1 0 x x x x
1 1 x x x x
1 0 x x x x
1 1 x x x x
# ADC (0x08)
1 0 x x x x
1 1 x x x x
1 0 x x x x
1 1 x x x x
# SBC (0x09)
1 0 x x x x
1 1 x x x x
1 0 x x x x
1 1 x x x x
# ANDN (0x0A)
1 0 x x x x
1 1 x x x x
1 0 x x x x
1 1 x x x x
# ORN (0x0B)
1 0 x x x x
1 1 x x x x
1 0 x x x x
1 1 x x x x
# INC (0x0C)
1 0 x x x x
1 1 x x x x
1 0 x x x x
1 1 x x x x
# DEC (0x0D)
1 0 x x x x
1 1 x x x x
1 0 x x x x
1 1 x x x x
# MOV (0x0E)
1 0 x x x x
1 1 x x x x
1 0 x x x x
1 1 x x x x
# CMP (0x0F)
1 0 x x x x
1 1 x x x x
1 0 x x x x
1 1 x x x x
# ADDI (0x10)
1 0 x x x x
1 1 x x x x
1 0 x x x x
1 1 x x x x
# SUBI (0x11)
1 0 x x x x
1 1 x x x x
1 0 x x x x
1 1 x x x x
# ANDI (0x12)
1 0 x x x x
1 1 x x x x
1 0 x x x x
1 1 x x x x
# ORI (0x13)
1 0 x x x x
1 1 x x x x
1 0 x x x x
1 1 x x x x
# XORI (0x14)
1 0 x x x x
1 1 x x x x
1 0 x x x x
1 1 x x x x
# ADDI16 (0x15)
1 0 x x x x
1 1 x x x x
1 0 x x x x
1 1 x x x x
# ADDI8 (0x16)
1 0 x x x x
1 1 x x x x
1 0 x x x x
1 1 x x x x
# TST (0x17)
1 0 x x x x
1 1 x x x x
1 0 x x x x
1 1 x x x x
# CMPI (0x18)
1 0 x x x x
1 1 x x x x
1 0 x x x x
1 1 x x x x
# LUI (0x19)
1 0 x x x x
1 1 x x x x
1 0 x x x x
1 1 x x x x
# AUIPC (0x1A)
1 0 x x x x
1 1 x x x x
1 0 x x x x
1 1 x x x x
# MOVT (0x1B)
1 0 x x x x
1 1 x x x x
1 0 x x x x
1 1 x x x x
# MOVI8 (0x1C)
1 0 x x x x
1 1 x x x x
1 0 x x x x
1 1 x x x x
# MOVI16 (0x1D)
1 0 x x x x
1 1 x x x x
1 0 x x x x
1 1 x x x x
# SLT (0x1E)
1 0 x x x x
1 1 x x x x
1 0 x x x x
1 1 x x x x
# SLTU (0x1F)
1 0 x x x x
1 1 x x x x
1 0 x x x x
1 1 x x x x
# LSL (0x20)
1 0 x x x x
1 1 x x x x
1 0 x x x x
1 1 x x x x
# LSR (0x21)
1 0 x x x x
1 1 x x x x
1 0 x x x x
1 1 x x x x
# ASR (0x22)
1 0 x x x x
1 1 x x x x
1 0 x x x x
1 1 x x x x
# ROR (0x23)
1 0 x x x x
1 1 x x x x
1 0 x x x x
1 1 x x x x
# LSLI (0x24)
1 0 x x x x
1 1 x x x x
1 0 x x x x
1 1 x x x x
# LSRI (0x25)
1 0 x x x x
1 1 x x x x
1 0 x x x x
1 1 x x x x
# ASRI (0x26)
1 0 x x x x
1 1 x x x x
1 0 x x x x
1 1 x x x x
# RORI (0x27)
1 0 x x x x
1 1 x x x x
1 0 x x x x
1 1 x x x x
# LW (0x30)
1 0 x x x x
1 1 x x x x
1 0 x x x x
1 1 x x x x
1 0 x x x x
1 1 x x x x
# LH (0x31)
1 0 x x x x
1 1 x x x x
1 0 x x x x
1 1 x x x x
1 0 x x x x
1 1 x x x x
# LHU (0x32)
1 0 x x x x
1 1 x x x x
1 0 x x x x
1 1 x x x x
1 0 x x x x
1 1 x x x x
# LB (0x33)
1 0 x x x x
1 1 x x x x
1 0 x x x x
1 1 x x x x
1 0 x x x x
1 1 x x x x
# LBU (0x34)
1 0 x x x x
1 1 x x x x
1 0 x x x x
1 1 x x x x
1 0 x x x x
1 1 x x x x
# LW0 (0x35)
1 0 x x x x
1 1 x x x x
1 0 x x x x
1 1 x x x x
# SW (0x40)
1 0 x x x x
1 1 x x x x
1 0 x x x x
1 1 x x x x
1 0 x x x x
1 1 x x x x
# SH (0x41)
1 0 x x x x
1 1 x x x x
1 0 x x x x
1 1 x x x x
1 0 x x x x
1 1 x x x x
# SB (0x42)
1 0 x x x x
1 1 x x x x
1 0 x x x x
1 1 x x x x
1 0 x x x x
1 1 x x x x
# SW0 (0x43)
1 0 x x x x
1 1 x x x x
1 0 x x x x
1 1 x x x x
# BEQ (0x50)
1 0 x x x x
1 1 x x x x
1 0 x x x x
1 1 x x x x
# BNE (0x51)
1 0 x x x x
1 1 x x x x
1 0 x x x x
1 1 x x x x
# BLT (0x52)
1 0 x x x x
1 1 x x x x
1 0 x x x x
1 1 x x x x
# BGE (0x53)
1 0 x x x x
1 1 x x x x
1 0 x x x x
1 1 x x x x
# BLTU (0x54)
1 0 x x x x
1 1 x x x x
1 0 x x x x
1 1 x x x x
# BGEU (0x55)
1 0 x x x x
1 1 x x x x
1 0 x x x x
1 1 x x x x
# BLEZ (0x56)
1 0 x x x x
1 1 x x x x
1 0 x x x x
1 1 x x x x
# BGTZ (0x57)
1 0 x x x x
1 1 x x x x
1 0 x x x x
1 1 x x x x
# JAL (0x60)
1 0 x x x x
1 1 x x x x
1 0 x x x x
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*/

/* Test case lw-pipeline:
reset clk alu-out ctrl-reg-we ir-opcode pc-out
# EEPROM: ADDI R0=0 -> ADDI R1=10 -> ADDI R2=10 -> ADD R2+=R1 -> JMP 3 (loop)
# Counter: R2 increments by 10 each iteration (10+10=20, 20+10=30, ...)
1 0 x x x x
1 1 x x x x
1 0 x x x x
# EXECUTE ADDI R0=r0+0=0
1 1 0 1 0x10 1
1 0 x x x x
1 1 x x x x
1 0 x x x x
# EXECUTE ADDI R1=r0+10=10
1 1 10 1 0x10 2
1 0 x x x x
1 1 x x x x
1 0 x x x x
# EXECUTE ADDI R2=r0+10=10
1 1 10 1 0x10 3
1 0 x x x x
1 1 x x x x
1 0 x x x x
# EXECUTE ADD iter1: R2 written=20, write-through re-reads R2=20, shows 20+10=30
1 1 30 1 0x01 4
1 0 x x x x
1 1 x x x x
1 0 x x x x
# EXECUTE JMP 3 — PC reloads to word 3
1 1 x 0 0x62 3
1 0 x x x x
1 1 x x x x
1 0 x x x x
# EXECUTE ADD iter2: R2 written=30, shows 30+10=40
1 1 40 1 0x01 4
1 0 x x x x
1 1 x x x x
1 0 x x x x
# EXECUTE JMP — PC back to 3
1 1 x 0 0x62 3
1 0 x x x x
1 1 x x x x
1 0 x x x x
# EXECUTE ADD iter3: R2 written=40, shows 40+10=50
1 1 50 1 0x01 4
*/

/* Test case mc-store:
reset clk alu-out ir-opcode ctrl-alu-op ctrl-reg-we
# auto-generated mc-store — microcode dispatch via main.dig
# Assert ir-opcode + ctrl-alu-op + ctrl-reg-we on EXECUTE for each native op
# NOP (0x00)
1 0 x x x x
1 1 x x x x
1 0 x x x x
1 1 x x x x
# ADD (0x01)
1 0 x x x x
1 1 x x x x
1 0 x x x x
1 1 x x x x
# SUB (0x02)
1 0 x x x x
1 1 x x x x
1 0 x x x x
1 1 x x x x
# AND (0x03)
1 0 x x x x
1 1 x x x x
1 0 x x x x
1 1 x x x x
# OR (0x04)
1 0 x x x x
1 1 x x x x
1 0 x x x x
1 1 x x x x
# XOR (0x05)
1 0 x x x x
1 1 x x x x
1 0 x x x x
1 1 x x x x
# NOT (0x06)
1 0 x x x x
1 1 x x x x
1 0 x x x x
1 1 x x x x
# NEG (0x07)
1 0 x x x x
1 1 x x x x
1 0 x x x x
1 1 x x x x
# ADC (0x08)
1 0 x x x x
1 1 x x x x
1 0 x x x x
1 1 x x x x
# SBC (0x09)
1 0 x x x x
1 1 x x x x
1 0 x x x x
1 1 x x x x
# ANDN (0x0A)
1 0 x x x x
1 1 x x x x
1 0 x x x x
1 1 x x x x
# ORN (0x0B)
1 0 x x x x
1 1 x x x x
1 0 x x x x
1 1 x x x x
# INC (0x0C)
1 0 x x x x
1 1 x x x x
1 0 x x x x
1 1 x x x x
# DEC (0x0D)
1 0 x x x x
1 1 x x x x
1 0 x x x x
1 1 x x x x
# MOV (0x0E)
1 0 x x x x
1 1 x x x x
1 0 x x x x
1 1 x x x x
# CMP (0x0F)
1 0 x x x x
1 1 x x x x
1 0 x x x x
1 1 x x x x
# ADDI (0x10)
1 0 x x x x
1 1 x x x x
1 0 x x x x
1 1 x x x x
# SUBI (0x11)
1 0 x x x x
1 1 x x x x
1 0 x x x x
1 1 x x x x
# ANDI (0x12)
1 0 x x x x
1 1 x x x x
1 0 x x x x
1 1 x x x x
# ORI (0x13)
1 0 x x x x
1 1 x x x x
1 0 x x x x
1 1 x x x x
# XORI (0x14)
1 0 x x x x
1 1 x x x x
1 0 x x x x
1 1 x x x x
# ADDI16 (0x15)
1 0 x x x x
1 1 x x x x
1 0 x x x x
1 1 x x x x
# ADDI8 (0x16)
1 0 x x x x
1 1 x x x x
1 0 x x x x
1 1 x x x x
# TST (0x17)
1 0 x x x x
1 1 x x x x
1 0 x x x x
1 1 x x x x
# CMPI (0x18)
1 0 x x x x
1 1 x x x x
1 0 x x x x
1 1 x x x x
# LUI (0x19)
1 0 x x x x
1 1 x x x x
1 0 x x x x
1 1 x x x x
# AUIPC (0x1A)
1 0 x x x x
1 1 x x x x
1 0 x x x x
1 1 x x x x
# MOVT (0x1B)
1 0 x x x x
1 1 x x x x
1 0 x x x x
1 1 x x x x
# MOVI8 (0x1C)
1 0 x x x x
1 1 x x x x
1 0 x x x x
1 1 x x x x
# MOVI16 (0x1D)
1 0 x x x x
1 1 x x x x
1 0 x x x x
1 1 x x x x
# SLT (0x1E)
1 0 x x x x
1 1 x x x x
1 0 x x x x
1 1 x x x x
# SLTU (0x1F)
1 0 x x x x
1 1 x x x x
1 0 x x x x
1 1 x x x x
# LSL (0x20)
1 0 x x x x
1 1 x x x x
1 0 x x x x
1 1 x x x x
# LSR (0x21)
1 0 x x x x
1 1 x x x x
1 0 x x x x
1 1 x x x x
# ASR (0x22)
1 0 x x x x
1 1 x x x x
1 0 x x x x
1 1 x x x x
# ROR (0x23)
1 0 x x x x
1 1 x x x x
1 0 x x x x
1 1 x x x x
# LSLI (0x24)
1 0 x x x x
1 1 x x x x
1 0 x x x x
1 1 x x x x
# LSRI (0x25)
1 0 x x x x
1 1 x x x x
1 0 x x x x
1 1 x x x x
# ASRI (0x26)
1 0 x x x x
1 1 x x x x
1 0 x x x x
1 1 x x x x
# RORI (0x27)
1 0 x x x x
1 1 x x x x
1 0 x x x x
1 1 x x x x
# LW (0x30)
1 0 x x x x
1 1 x x x x
1 0 x x x x
1 1 x x x x
1 0 x x x x
1 1 x x x x
# LH (0x31)
1 0 x x x x
1 1 x x x x
1 0 x x x x
1 1 x x x x
1 0 x x x x
1 1 x x x x
# LHU (0x32)
1 0 x x x x
1 1 x x x x
1 0 x x x x
1 1 x x x x
1 0 x x x x
1 1 x x x x
# LB (0x33)
1 0 x x x x
1 1 x x x x
1 0 x x x x
1 1 x x x x
1 0 x x x x
1 1 x x x x
# LBU (0x34)
1 0 x x x x
1 1 x x x x
1 0 x x x x
1 1 x x x x
1 0 x x x x
1 1 x x x x
# LW0 (0x35)
1 0 x x x x
1 1 x x x x
1 0 x x x x
1 1 x x x x
# SW (0x40)
1 0 x x x x
1 1 x x x x
1 0 x x x x
1 1 x x x x
1 0 x x x x
1 1 x 0 0x40 0x00
# SH (0x41)
1 0 x x x x
1 1 x x x x
1 0 x x x x
1 1 x x x x
1 0 x x x x
1 1 x 0 0x41 0x00
# SB (0x42)
1 0 x x x x
1 1 x x x x
1 0 x x x x
1 1 x x x x
1 0 x x x x
1 1 x 0 0x42 0x00
# SW0 (0x43)
1 0 x x x x
1 1 x x x x
1 0 x x x x
1 1 x 0 0x43 0x00
# BEQ (0x50)
1 0 x x x x
1 1 x x x x
1 0 x x x x
1 1 x x x x
# BNE (0x51)
1 0 x x x x
1 1 x x x x
1 0 x x x x
1 1 x x x x
# BLT (0x52)
1 0 x x x x
1 1 x x x x
1 0 x x x x
1 1 x x x x
# BGE (0x53)
1 0 x x x x
1 1 x x x x
1 0 x x x x
1 1 x x x x
# BLTU (0x54)
1 0 x x x x
1 1 x x x x
1 0 x x x x
1 1 x x x x
# BGEU (0x55)
1 0 x x x x
1 1 x x x x
1 0 x x x x
1 1 x x x x
# BLEZ (0x56)
1 0 x x x x
1 1 x x x x
1 0 x x x x
1 1 x x x x
# BGTZ (0x57)
1 0 x x x x
1 1 x x x x
1 0 x x x x
1 1 x x x x
# JAL (0x60)
1 0 x x x x
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*/

/* Test case mc-system-alu-rr:
reset clk alu-out ir-opcode ctrl-alu-op ctrl-reg-we
# auto-generated mc-system-alu-rr — microcode dispatch via main.dig
# Assert ir-opcode + ctrl-alu-op + ctrl-reg-we on EXECUTE for each native op
# NOP (0x00)
1 0 x x x x
1 1 x x x x
1 0 x x x x
1 1 x 0 0x00 0x00
# ADD (0x01)
1 0 x x x x
1 1 x x x x
1 0 x x x x
1 1 x 1 0x01 0x96
# SUB (0x02)
1 0 x x x x
1 1 x x x x
1 0 x x x x
1 1 x 1 0x02 0x96
# AND (0x03)
1 0 x x x x
1 1 x x x x
1 0 x x x x
1 1 x 1 0x03 0x88
# OR (0x04)
1 0 x x x x
1 1 x x x x
1 0 x x x x
1 1 x 1 0x04 0xEE
# XOR (0x05)
1 0 x x x x
1 1 x x x x
1 0 x x x x
1 1 x 1 0x05 0x66
# NOT (0x06)
1 0 x x x x
1 1 x x x x
1 0 x x x x
1 1 x 1 0x06 0x33
# NEG (0x07)
1 0 x x x x
1 1 x x x x
1 0 x x x x
1 1 x 1 0x07 0x96
# ADC (0x08)
1 0 x x x x
1 1 x x x x
1 0 x x x x
1 1 x 1 0x08 0x96
# SBC (0x09)
1 0 x x x x
1 1 x x x x
1 0 x x x x
1 1 x 1 0x09 0x69
# ANDN (0x0A)
1 0 x x x x
1 1 x x x x
1 0 x x x x
1 1 x 1 0x0A 0xC0
# ORN (0x0B)
1 0 x x x x
1 1 x x x x
1 0 x x x x
1 1 x 1 0x0B 0xEE
# INC (0x0C)
1 0 x x x x
1 1 x x x x
1 0 x x x x
1 1 x 1 0x0C 0x96
# DEC (0x0D)
1 0 x x x x
1 1 x x x x
1 0 x x x x
1 1 x 1 0x0D 0x96
# MOV (0x0E)
1 0 x x x x
1 1 x x x x
1 0 x x x x
1 1 x 1 0x0E 0xCC
# CMP (0x0F)
1 0 x x x x
1 1 x x x x
1 0 x x x x
1 1 x 0 0x0F 0x69
# ADDI (0x10)
1 0 x x x x
1 1 x x x x
1 0 x x x x
1 1 x x x x
# SUBI (0x11)
1 0 x x x x
1 1 x x x x
1 0 x x x x
1 1 x x x x
# ANDI (0x12)
1 0 x x x x
1 1 x x x x
1 0 x x x x
1 1 x x x x
# ORI (0x13)
1 0 x x x x
1 1 x x x x
1 0 x x x x
1 1 x x x x
# XORI (0x14)
1 0 x x x x
1 1 x x x x
1 0 x x x x
1 1 x x x x
# ADDI16 (0x15)
1 0 x x x x
1 1 x x x x
1 0 x x x x
1 1 x x x x
# ADDI8 (0x16)
1 0 x x x x
1 1 x x x x
1 0 x x x x
1 1 x x x x
# TST (0x17)
1 0 x x x x
1 1 x x x x
1 0 x x x x
1 1 x x x x
# CMPI (0x18)
1 0 x x x x
1 1 x x x x
1 0 x x x x
1 1 x x x x
# LUI (0x19)
1 0 x x x x
1 1 x x x x
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*/

/* Test case program counter:
reset clk pc-out ir-opcode
# EEPROM loop: ADDI x3, ADD, JMP rel 3 (0x62000003, IR[0]=1)
1 0 x x
1 1 x x
1 0 x x
1 1 1 0x10
1 0 x x
1 1 x x
1 0 x x
1 1 2 0x10
1 0 x x
1 1 x x
1 0 x x
1 1 3 0x10
1 0 x x
1 1 x x
1 0 x x
1 1 4 0x01
1 0 x x
1 1 x x
1 0 x x
1 1 3 0x62
*/

/* Test case mc-load:
reset clk alu-out ir-opcode ctrl-alu-op ctrl-reg-we
# auto-generated mc-load — microcode dispatch via main.dig
# Assert ir-opcode + ctrl-alu-op + ctrl-reg-we on EXECUTE for each native op
# NOP (0x00)
1 0 x x x x
1 1 x x x x
1 0 x x x x
1 1 x x x x
# ADD (0x01)
1 0 x x x x
1 1 x x x x
1 0 x x x x
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*/

/* Test case mc-alu-imm-b:
reset clk alu-out ir-opcode ctrl-alu-op ctrl-reg-we
# auto-generated mc-alu-imm-b — microcode dispatch via main.dig
# Assert ir-opcode + ctrl-alu-op + ctrl-reg-we on EXECUTE for each native op
# NOP (0x00)
1 0 x x x x
1 1 x x x x
1 0 x x x x
1 1 x x x x
# ADD (0x01)
1 0 x x x x
1 1 x x x x
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*/

/* Test case mc-alu-imm-a:
reset clk alu-out ir-opcode ctrl-alu-op ctrl-reg-we
# auto-generated mc-alu-imm-a — microcode dispatch via main.dig
# Assert ir-opcode + ctrl-alu-op + ctrl-reg-we on EXECUTE for each native op
# NOP (0x00)
1 0 x x x x
1 1 x x x x
1 0 x x x x
1 1 x x x x
# ADD (0x01)
1 0 x x x x
1 1 x x x x
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*/

/* Test case mc-shift:
reset clk alu-out ir-opcode ctrl-alu-op ctrl-reg-we
# auto-generated mc-shift — microcode dispatch via main.dig
# Assert ir-opcode + ctrl-alu-op + ctrl-reg-we on EXECUTE for each native op
# NOP (0x00)
1 0 x x x x
1 1 x x x x
1 0 x x x x
1 1 x x x x
# ADD (0x01)
1 0 x x x x
1 1 x x x x
1 0 x x x x
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*/

/* Test case mc-muldiv-flags:
reset clk alu-out ir-opcode ctrl-alu-op ctrl-reg-we
# auto-generated mc-muldiv-flags — microcode dispatch via main.dig
# Assert ir-opcode + ctrl-alu-op + ctrl-reg-we on EXECUTE for each native op
# NOP (0x00)
1 0 x x x x
1 1 x x x x
1 0 x x x x
1 1 x x x x
# ADD (0x01)
1 0 x x x x
1 1 x x x x
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*/
