// Digital circuit mem-bus-control.dig as structural Verilog
module mem_bus_control (
  input  [11:0] op,
  output [2:0] ctrl_bussel
);

  wire [7:3] mem_bus_control_d;

  ROM #(.bigEndian("true"), .AddrBits(12), .isProgramMemory("true"), .Bits(8)) mem_bus_control (
    .A(op), .sel(1'b1), .D({mem_bus_control_d, ctrl_bussel}));

  // Other names for the same wires on the sheet: ir_opcode[11:0] = op

  // Notes on the sheet:
  //   op: default 48
  //   mem_bus_control loads mem_bus_control.hex
endmodule
