// Digital circuit mem-io-control.dig as structural Verilog
module mem_io_control (
  input  [11:0] op,
  input  seq_fetch,
  output bank_en,
  output mem_rd,
  output mem_wr,
  output [3:0] byte_sel
);

  wire nand_1_out, nand_2_out;
  wire [7:2] mem_io_control_d;

  ROM #(.bigEndian("true"), .AddrBits(12), .isProgramMemory("true"), .Bits(8)) mem_io_control (
    .A(op), .sel(1'b1), .D({mem_io_control_d[7], byte_sel, mem_io_control_d[2], mem_rd, bank_en}));
  nand nand_1 (nand_1_out, seq_fetch, seq_fetch);
  nand nand_2 (nand_2_out, mem_io_control_d[2], nand_1_out);
  nand nand_3 (mem_wr, nand_2_out, nand_2_out);

  // Other names for the same wires on the sheet: ir_opcode[11:0] = op

  // Notes on the sheet:
  //   op: default 48
  //   mem_io_control loads mem_io_control.hex
endmodule
