// Digital circuit microcode.dig as structural Verilog
module microcode (
  input  [7:0] op,
  output [7:0] alu_op,
  output [4:0] alu_pre,
  output cin_sel,
  output [2:0] wb_sel,
  output [1:0] shift_op,
  output flags_we,
  output reg_we,
  output mem_rd,
  output mem_wr,
  output addr_csel,
  output branch_en,
  output jump_type,
  output [1:0] sp_op,
  output [1:0] cycles,
  output [2:0] ctrl_bus_sel,
  output [2:0] b_main_sel,
  output pc_rel,
  output [3:0] ir_imm_sel
);

  wire [47:41] microcode_eeprom_d;

  ROM #(.bigEndian("true"), .AddrBits(8), .Bits(48)) microcode_eeprom (
    .A(op), .sel(1'b1),
    .D({microcode_eeprom_d, ir_imm_sel, pc_rel, ctrl_bus_sel, b_main_sel, cycles, sp_op, jump_type, branch_en, addr_csel, mem_wr, mem_rd, reg_we, flags_we, shift_op, wb_sel, cin_sel, alu_pre, alu_op}));

  // Notes on the sheet:
  //   op: default 48
  //   microcode_eeprom loads microopcode_rom.hex
endmodule

/* Test case:
op alu-op alu-pre cin-sel wb-sel shift-op flags-we reg-we mem-rd mem-wr addr-csel branch-en jump-type sp-op cycles b-main-sel ctrl_bus_sel pc-rel

# SECTION 1: all 256 ROM indices (sole address input = op)
0x00 0x00 0x00 0 0 0 0 0 0 0 0 0 0 0 1 0 0 0
0x01 0x96 0x05 0 0 0 1 1 0 0 0 0 0 0 2 0 0 0
0x02 0x96 0x0D 1 0 0 1 1 0 0 0 0 0 0 2 0 0 0
0x03 0x88 0x05 0 0 0 1 1 0 0 0 0 0 0 2 0 0 0
0x04 0xEE 0x05 0 0 0 1 1 0 0 0 0 0 0 2 0 0 0
0x05 0x66 0x05 0 0 0 1 1 0 0 0 0 0 0 2 0 0 0
0x06 0x33 0x01 0 0 0 1 1 0 0 0 0 0 0 2 0 0 0
0x07 0x96 0x07 0 0 0 1 1 0 0 0 0 0 0 2 0 0 0
0x08 0x96 0x1D 0 0 0 1 1 0 0 0 0 0 0 2 0 0 0
0x09 0x96 0x17 0 0 0 1 1 0 0 0 0 0 0 2 0 0 0
0x0A 0x96 0x1D 0 0 0 1 1 0 0 0 0 0 0 2 0 0 0
0x0B 0x96 0x10 0 0 0 1 1 0 0 0 0 0 0 2 0 0 0
0x0C 0x96 0x05 1 0 0 1 1 0 0 0 0 0 0 2 0 0 0
0x0D 0x96 0x02 1 0 0 1 1 0 0 0 0 0 0 2 0 0 0
0x0E 0x96 0x0A 1 0 0 1 1 0 0 0 0 0 0 2 0 0 0
0x0F 0x96 0x0F 0 0 0 1 1 0 0 0 0 0 0 2 0 0 0
0x10 0x00 0x00 0 1 0 1 1 0 0 0 0 0 0 2 0 0 0
0x11 0x00 0x00 0 1 1 1 1 0 0 0 0 0 0 2 0 0 0
0x12 0x00 0x00 0 1 2 1 1 0 0 0 0 0 0 2 0 0 0
0x13 0x00 0x00 0 1 3 1 1 0 0 0 0 0 0 2 0 0 0
0x14 0x00 0x00 0 1 0 1 1 0 0 0 0 0 0 2 0 0 0
0x15 0x00 0x15 0 0 0 1 1 0 0 1 0 0 0 2 0 0 0
0x16 0x02 0x15 0 0 0 1 1 0 0 1 0 0 0 2 0 0 0
0x17 0x03 0x15 0 0 0 1 1 0 0 1 0 0 0 2 0 0 0
0x18 0x04 0x15 0 0 0 1 1 0 0 1 0 0 0 2 0 0 0
0x19 0x05 0x15 0 0 0 1 1 0 0 1 0 0 0 2 0 0 0
0x1A 0x06 0x15 0 0 0 1 1 0 0 1 0 0 0 2 0 0 0
0x1B 0x08 0x15 0 0 0 1 1 0 0 1 0 0 0 2 0 0 0
0x1C 0x09 0x15 0 0 0 1 1 0 0 1 0 0 0 2 0 0 0
0x1D 0x0B 0x15 0 0 0 1 1 0 0 1 0 0 0 2 0 0 0
0x1E 0x0C 0x15 0 0 0 1 1 0 0 1 0 0 0 2 0 0 0
0x1F 0x0D 0x15 0 0 0 1 1 0 0 1 0 0 0 2 0 0 0
0x20 0x00 0x00 0 3 0 0 1 1 0 0 0 0 0 3 0 0 0
0x21 0x00 0x00 0 0 0 0 0 0 1 0 0 0 0 3 0 0 0
0x22 0xCC 0x04 0 0 0 0 1 0 0 0 0 0 0 2 0 0 0
0x23 0x00 0x00 0 3 0 0 1 1 0 0 0 0 0 3 0 1 0
0x24 0x00 0x00 0 0 0 0 0 0 1 0 0 0 0 3 0 1 0
0x25 0x0E 0x15 0 0 0 1 1 0 0 1 0 0 0 2 0 0 0
0x26 0x0F 0x15 0 0 0 1 1 0 0 1 0 0 0 2 0 0 0
0x27 0x10 0x15 0 0 0 1 1 0 0 1 0 0 0 2 0 0 0
0x28 0x11 0x15 0 0 0 1 1 0 0 1 0 0 0 2 0 0 0
0x29 0x12 0x15 0 0 0 1 1 0 0 1 0 0 0 2 0 0 0
0x2A 0x13 0x15 0 0 0 1 1 0 0 1 0 0 0 2 0 0 0
0x2B 0x14 0x15 0 0 0 1 1 0 0 1 0 0 0 2 0 0 0
0x2C 0x15 0x15 0 0 0 1 1 0 0 1 0 0 0 2 0 0 0
0x2D 0x18 0x15 0 0 0 1 1 0 0 1 0 0 0 2 0 0 0
0x2E 0x19 0x15 0 0 0 1 1 0 0 1 0 0 0 2 0 0 0
0x2F 0x1A 0x15 0 0 0 1 1 0 0 1 0 0 0 2 0 0 0
0x30 0x00 0x00 0 0 0 0 0 0 0 0 1 1 0 2 0 0 0
0x31 0x00 0x00 0 0 0 0 0 0 0 0 1 0 0 2 0 0 0
0x32 0x00 0x00 0 2 0 0 1 0 0 0 1 1 1 2 0 0 0
0x33 0x00 0x00 0 0 0 0 0 0 0 0 1 1 0 2 0 0 0
0x34 0x96 0x05 0 0 0 1 1 0 0 0 0 0 0 2 0 0 0
0x35 0x96 0x0D 1 0 0 1 1 0 0 0 0 0 0 2 0 0 0
0x36 0x96 0x0B 1 0 0 1 1 0 0 0 0 0 0 2 0 0 0
0x37 0x96 0x0C 0 0 0 1 1 0 0 0 0 0 0 2 0 0 0
0x38 0x96 0x0E 0 0 0 1 1 0 0 0 0 0 0 2 0 0 0
0x39 0x96 0x0F 1 0 0 1 1 0 0 0 0 0 0 2 0 0 0
0x3A 0x96 0x08 0 0 0 1 1 0 0 0 0 0 0 2 0 0 0
0x3B 0x96 0x06 1 0 0 1 1 0 0 0 0 0 0 2 0 0 0
0x3C 0x96 0x01 0 0 0 1 1 0 0 0 0 0 0 2 0 0 0
0x3D 0x96 0x04 0 0 0 1 1 0 0 0 0 0 0 2 0 0 0
0x3E 0x1C 0x15 0 0 0 1 1 0 0 1 0 0 0 2 0 0 0
0x3F 0x1D 0x15 0 0 0 1 1 0 0 1 0 0 0 2 0 0 0
0x40 0x40 0x15 0 0 0 1 1 0 0 1 0 0 0 2 0 0 0
0x41 0x41 0x15 0 0 0 1 1 0 0 1 0 0 0 2 0 0 0
0x42 0x42 0x15 0 0 0 1 1 0 0 1 0 0 0 2 0 0 0
0x43 0x43 0x15 0 0 0 1 1 0 0 1 0 0 0 2 0 0 0
0x44 0x44 0x15 0 0 0 1 1 0 0 1 0 0 0 2 0 0 0
0x45 0x45 0x15 0 0 0 1 1 0 0 1 0 0 0 2 0 0 0
0x46 0x46 0x15 0 0 0 1 1 0 0 1 0 0 0 2 0 0 0
0x47 0x47 0x15 0 0 0 1 1 0 0 1 0 0 0 2 0 0 0
0x48 0x48 0x15 0 0 0 1 1 0 0 1 0 0 0 2 0 0 0
0x49 0x49 0x15 0 0 0 1 1 0 0 1 0 0 0 2 0 0 0
0x4A 0x4A 0x15 0 0 0 1 1 0 0 1 0 0 0 2 0 0 0
0x4B 0x4B 0x15 0 0 0 1 1 0 0 1 0 0 0 2 0 0 0
0x4C 0x4C 0x15 0 0 0 1 1 0 0 1 0 0 0 2 0 0 0
0x4D 0x4D 0x15 0 0 0 1 1 0 0 1 0 0 0 2 0 0 0
0x4E 0x4E 0x15 0 0 0 1 1 0 0 1 0 0 0 2 0 0 0
0x4F 0x4F 0x15 0 0 0 1 1 0 0 1 0 0 0 2 0 0 0
0x50 0x50 0x15 0 0 0 1 1 0 0 1 0 0 0 2 0 0 0
0x51 0x51 0x15 0 0 0 1 1 0 0 1 0 0 0 2 0 0 0
0x52 0x52 0x15 0 0 0 1 1 0 0 1 0 0 0 2 0 0 0
0x53 0x53 0x15 0 0 0 1 1 0 0 1 0 0 0 2 0 0 0
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*/
