// Digital circuit mul-div.dig as structural Verilog
module mul_div (
  input  [31:0] B,
  input  [1:0] mode,
  input  mul_div,
  input  [31:0] A,
  input  p_enc,
  output [31:0] Out,
  output nflag_A_is_Z,
  output [15:0] mul_nxt_enc
);

  wire and_2_out, decoder_1_out_0, decoder_1_out_1, decoder_1_out_2, decoder_1_out_3, decoder_1_out_4,
       decoder_1_out_5, decoder_1_out_6, decoder_1_out_7, decoder_1_out_8, decoder_1_out_9, decoder_1_out_10,
       decoder_1_out_11, decoder_1_out_12, decoder_1_out_13, decoder_1_out_14, decoder_1_out_15, not_17_out;
  wire [3:0] enc_out;
  wire [4:0] bitextender_1_out, multiplexer_2_out, nor_1_out, p_enc_A;
  wire [15:0] new_enc;
  wire [31:0] multiplexer_1_out;

  PriorityEncoder #(.Selector_Bits(5)) priorityencoder_1 (
    .in0(A[0]), .in1(A[1]), .in2(A[2]), .in3(A[3]), .in4(A[4]), .in5(A[5]), .in6(A[6]), .in7(A[7]),
    .in8(A[8]), .in9(A[9]), .in10(A[10]), .in11(A[11]), .in12(A[12]), .in13(A[13]), .in14(A[14]),
    .in15(A[15]), .in16(A[16]), .in17(A[17]), .in18(A[18]), .in19(A[19]), .in20(A[20]), .in21(A[21]),
    .in22(A[22]), .in23(A[23]), .in24(A[24]), .in25(A[25]), .in26(A[26]), .in27(A[27]), .in28(A[28]),
    .in29(A[29]), .in30(A[30]), .in31(A[31]), .num(p_enc_A), .any(nflag_A_is_Z));
  PriorityEncoder #(.Selector_Bits(4)) priorityencoder_2 (
    .in0(B[0]), .in1(B[1]), .in2(B[2]), .in3(B[3]), .in4(B[4]), .in5(B[5]), .in6(B[6]), .in7(B[7]),
    .in8(B[8]), .in9(B[9]), .in10(B[10]), .in11(B[11]), .in12(B[12]), .in13(B[13]), .in14(B[14]),
    .in15(B[15]), .num(enc_out));  // open: any
  BitExtender #(.inputBits(1), .outputBits(5)) bitextender_1 (.in(p_enc), .out(bitextender_1_out));
  Decoder #(.Selector_Bits(4)) decoder_1 (
    .sel(enc_out), .out_0(decoder_1_out_0), .out_1(decoder_1_out_1), .out_2(decoder_1_out_2),
    .out_3(decoder_1_out_3), .out_4(decoder_1_out_4), .out_5(decoder_1_out_5), .out_6(decoder_1_out_6),
    .out_7(decoder_1_out_7), .out_8(decoder_1_out_8), .out_9(decoder_1_out_9), .out_10(decoder_1_out_10),
    .out_11(decoder_1_out_11), .out_12(decoder_1_out_12), .out_13(decoder_1_out_13),
    .out_14(decoder_1_out_14), .out_15(decoder_1_out_15));
  assign nor_1_out = ~(B[4:0] | bitextender_1_out);  // NOr nor_1, 5 bits wide
  not not_1 (new_enc[0], decoder_1_out_0);
  not not_2 (new_enc[1], decoder_1_out_1);
  not not_3 (new_enc[2], decoder_1_out_2);
  not not_4 (new_enc[3], decoder_1_out_3);
  not not_5 (new_enc[4], decoder_1_out_4);
  not not_6 (new_enc[5], decoder_1_out_5);
  not not_7 (new_enc[6], decoder_1_out_6);
  not not_8 (new_enc[7], decoder_1_out_7);
  not not_9 (new_enc[8], decoder_1_out_8);
  not not_10 (new_enc[9], decoder_1_out_9);
  not not_11 (new_enc[10], decoder_1_out_10);
  not not_12 (new_enc[11], decoder_1_out_11);
  not not_13 (new_enc[12], decoder_1_out_12);
  not not_14 (new_enc[13], decoder_1_out_13);
  not not_15 (new_enc[14], decoder_1_out_14);
  not not_16 (new_enc[15], decoder_1_out_15);
  assign mul_nxt_enc = new_enc & B[15:0];  // And and_1, 16 bits wide
  Multiplexer #(.Bits(32)) multiplexer_1 (.sel(p_enc), .in_0(A), .in_1({{27{1'b0}}, p_enc_A}), .out(multiplexer_1_out));
  Multiplexer #(.Bits(5)) multiplexer_2 (
    .sel(and_2_out), .in_0(nor_1_out), .in_1({1'b0, enc_out}), .out(multiplexer_2_out));
  shift shift_1 (.A(multiplexer_1_out), .mode(mode), .B(multiplexer_2_out), .Out(Out));
  and and_2 (and_2_out, not_17_out, mul_div);
  not not_17 (not_17_out, p_enc);

  // Other names for the same wires on the sheet: mul_div_en = mul_div; nflag_a_is_zero = nflag_A_is_Z

  // Notes on the sheet:
  //   B: default 50000
  //   mode: default 1
  //   A: default 100000
endmodule

/* Test case:
A B mode mul-div p-enc-out clk Shift-Out nxt-enc ~A_is_Zero\n0xAAAAAAAA 0x0 0 0 0 0 0xAAAAAAAA 0x0 1\n0xAAAAAAAA 0x1 0 0 0 0 0x55555554 0x0 1\n0xAAAAAAAA 0x2 0 0 0 0 0xAAAAAAA8 0x0 1\n0xAAAAAAAA 0x3 0 0 0 0 0x55555550 0x0 1\n0xAAAAAAAA 0x4 0 0 0 0 0xAAAAAAA0 0x0 1\n0xAAAAAAAA 0x5 0 0 0 0 0x55555540 0x0 1\n0xAAAAAAAA 0x6 0 0 0 0 0xAAAAAA80 0x0 1\n0xAAAAAAAA 0x7 0 0 0 0 0x55555500 0x0 1\n0xAAAAAAAA 0x8 0 0 0 0 0xAAAAAA00 0x0 1\n0xAAAAAAAA 0x9 0 0 0 0 0x55555400 0x0 1\n0xAAAAAAAA 0xA 0 0 0 0 0xAAAAA800 0x0 1\n0xAAAAAAAA 0xB 0 0 0 0 0x55555000 0x0 1\n0xAAAAAAAA 0xC 0 0 0 0 0xAAAAA000 0x0 1\n0xAAAAAAAA 0xD 0 0 0 0 0x55554000 0x0 1\n0xAAAAAAAA 0xE 0 0 0 0 0xAAAA8000 0x0 1\n0xAAAAAAAA 0xF 0 0 0 0 0x55550000 0x0 1\n0xAAAAAAAA 0x10 0 0 0 0 0xAAAA0000 0x0 1\n0xAAAAAAAA 0x11 0 0 0 0 0x55540000 0x0 1\n0xAAAAAAAA 0x12 0 0 0 0 0xAAA80000 0x0 1\n0xAAAAAAAA 0x13 0 0 0 0 0x55500000 0x0 1\n0xAAAAAAAA 0x14 0 0 0 0 0xAAA00000 0x0 1\n0xAAAAAAAA 0x15 0 0 0 0 0x55400000 0x0 1\n0xAAAAAAAA 0x16 0 0 0 0 0xAA800000 0x0 1\n0xAAAAAAAA 0x17 0 0 0 0 0x55000000 0x0 1\n0xAAAAAAAA 0x18 0 0 0 0 0xAA000000 0x0 1\n0xAAAAAAAA 0x19 0 0 0 0 0x54000000 0x0 1\n0xAAAAAAAA 0x1A 0 0 0 0 0xA8000000 0x0 1\n0xAAAAAAAA 0x1B 0 0 0 0 0x50000000 0x0 1\n0xAAAAAAAA 0x1C 0 0 0 0 0xA0000000 0x0 1\n0xAAAAAAAA 0x1D 0 0 0 0 0x40000000 0x0 1\n0xAAAAAAAA 0x1E 0 0 0 0 0x80000000 0x0 1\n0xAAAAAAAA 0x1F 0 0 0 0 0x0 0x0 1\n0x55555555 0x0 0 0 0 0 0x55555555 0x0 1\n0x55555555 0x1 0 0 0 0 0xAAAAAAAA 0x0 1\n0x55555555 0x2 0 0 0 0 0x55555554 0x0 1\n0x55555555 0x3 0 0 0 0 0xAAAAAAA8 0x0 1\n0x55555555 0x4 0 0 0 0 0x55555550 0x0 1\n0x55555555 0x5 0 0 0 0 0xAAAAAAA0 0x0 1\n0x55555555 0x6 0 0 0 0 0x55555540 0x0 1\n0x55555555 0x7 0 0 0 0 0xAAAAAA80 0x0 1\n0x55555555 0x8 0 0 0 0 0x55555500 0x0 1\n0x55555555 0x9 0 0 0 0 0xAAAAAA00 0x0 1\n0x55555555 0xA 0 0 0 0 0x55555400 0x0 1\n0x55555555 0xB 0 0 0 0 0xAAAAA800 0x0 1\n0x55555555 0xC 0 0 0 0 0x55555000 0x0 1\n0x55555555 0xD 0 0 0 0 0xAAAAA000 0x0 1\n0x55555555 0xE 0 0 0 0 0x55554000 0x0 1\n0x55555555 0xF 0 0 0 0 0xAAAA8000 0x0 1\n0x55555555 0x10 0 0 0 0 0x55550000 0x0 1\n0x55555555 0x11 0 0 0 0 0xAAAA0000 0x0 1\n0x55555555 0x12 0 0 0 0 0x55540000 0x0 1\n0x55555555 0x13 0 0 0 0 0xAAA80000 0x0 1\n0x55555555 0x14 0 0 0 0 0x55500000 0x0 1\n0x55555555 0x15 0 0 0 0 0xAAA00000 0x0 1\n0x55555555 0x16 0 0 0 0 0x55400000 0x0 1\n0x55555555 0x17 0 0 0 0 0xAA800000 0x0 1\n0x55555555 0x18 0 0 0 0 0x55000000 0x0 1\n0x55555555 0x19 0 0 0 0 0xAA000000 0x0 1\n0x55555555 0x1A 0 0 0 0 0x54000000 0x0 1\n0x55555555 0x1B 0 0 0 0 0xA8000000 0x0 1\n0x55555555 0x1C 0 0 0 0 0x50000000 0x0 1\n0x55555555 0x1D 0 0 0 0 0xA0000000 0x0 1\n0x55555555 0x1E 0 0 0 0 0x40000000 0x0 1\n0x55555555 0x1F 0 0 0 0 0x80000000 0x0 1\n0x12345678 0x0 0 0 0 0 0x12345678 0x0 1\n0x12345678 0x1 0 0 0 0 0x2468ACF0 0x0 1\n0x12345678 0x2 0 0 0 0 0x48D159E0 0x0 1\n0x12345678 0x3 0 0 0 0 0x91A2B3C0 0x0 1\n0x12345678 0x4 0 0 0 0 0x23456780 0x0 1\n0x12345678 0x5 0 0 0 0 0x468ACF00 0x0 1\n0x12345678 0x6 0 0 0 0 0x8D159E00 0x0 1\n0x12345678 0x7 0 0 0 0 0x1A2B3C00 0x0 1\n0x12345678 0x8 0 0 0 0 0x34567800 0x0 1\n0x12345678 0x9 0 0 0 0 0x68ACF000 0x0 1\n0x12345678 0xA 0 0 0 0 0xD159E000 0x0 1\n0x12345678 0xB 0 0 0 0 0xA2B3C000 0x0 1\n0x12345678 0xC 0 0 0 0 0x45678000 0x0 1\n0x12345678 0xD 0 0 0 0 0x8ACF0000 0x0 1\n0x12345678 0xE 0 0 0 0 0x159E0000 0x0 1\n0x12345678 0xF 0 0 0 0 0x2B3C0000 0x0 1\n0x12345678 0x10 0 0 0 0 0x56780000 0x0 1\n0x12345678 0x11 0 0 0 0 0xACF00000 0x0 1\n0x12345678 0x12 0 0 0 0 0x59E00000 0x0 1\n0x12345678 0x13 0 0 0 0 0xB3C00000 0x0 1\n0x12345678 0x14 0 0 0 0 0x67800000 0x0 1\n0x12345678 0x15 0 0 0 0 0xCF000000 0x0 1\n0x12345678 0x16 0 0 0 0 0x9E000000 0x0 1\n0x12345678 0x17 0 0 0 0 0x3C000000 0x0 1\n0x12345678 0x18 0 0 0 0 0x78000000 0x0 1\n0x12345678 0x19 0 0 0 0 0xF0000000 0x0 1\n0x12345678 0x1A 0 0 0 0 0xE0000000 0x0 1\n0x12345678 0x1B 0 0 0 0 0xC0000000 0x0 1\n0x12345678 0x1C 0 0 0 0 0x80000000 0x0 1\n0x12345678 0x1D 0 0 0 0 0x0 0x0 1\n0x12345678 0x1E 0 0 0 0 0x0 0x0 1\n0x12345678 0x1F 0 
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*/
