// Digital circuit pc-control.dig as structural Verilog
module pc_control (
  input  exec,
  input  [8:0] op,
  output branch_en,
  output jump_type,
  output [2:0] pc_src,
  output pc_link_we,
  output [1:0] cycles,
  output [2:0] pc_cond,
  output [1:0] sp_out,
  output HALT_IN
);

  wire comparator_1_eq;
  wire [7:5] pc_sp_mul_control_d;

  and and_1 (HALT_IN, comparator_1_eq, exec);
  Comparator #(.Bits(9)) comparator_1 (.a(9'hff), .b(op), .eq(comparator_1_eq));  // open: gt, lt
  ROM #(.bigEndian("true"), .AddrBits(9), .Bits(8)) pc_control (
    .A(op), .sel(1'b1), .D({cycles, pc_link_we, pc_src, jump_type, branch_en}));
  ROM #(.bigEndian("true"), .AddrBits(9), .Bits(8)) pc_sp_mul_control (
    .A(op), .sel(1'b1), .D({pc_sp_mul_control_d, sp_out, pc_cond}));

  // Other names for the same wires on the sheet: ir_opcode[8:0] = op; seq_exec = exec

  // Notes on the sheet:
  //   op: default 48
  //   contents of pc_control (hex, n*v repeats v):
  //   40,40,40,40,40,40,40,40,40,40,40,40,40,40,40,40,40,40,40,40,40,40,40,40,40,40,40,40,40,40,40,
  //   40,40,40,40,40,40,40,40,40,40,40,40,40,40,40,40,40,40,40,40,40,40,40,40,40,40,40,40,40,40,40,
  //   40,40,40,40,40,40,40,40,40,40,40,40,40,40,40,40,40,40,40,40,40,40,40,40,40,40,40,40,40,40,40,
  //   40,40,40,80,80,40,40,40,40,40,40,80,80,40,40,40,40,40,40,40,40,40,40,40,40,40,40,40,40,40,40,
  //   40,40,40,40,41,41,41,40,40,40,40,40,40,40,40,40,40,40,40,40,40,40,40,40,40,40,40,40,40,40,40,
  //   40,40,40,40,40,42,62,4a,4a,40,40,40,40,40,40,40,40,40,40,40,40,40,40,40,40,40,40,40,40,40,40,
  //   40,40,40,40,40,40,40,40,40,40,40,40,40,40,40,40,40,40,40,40,40,40,40,40,40,40,40,40,40,40,40,
  //   40,40,40,40,40,40,40,40,40,40,40,40,40,40,40,40,40,40,40,40,40,40,40,40,40,40,40,40,40,40,40,
  //   40,40,40,40,40,40,40,40,40,40,40,40,40,40,40,40,40,40,40,40,40,40,40,40,40,40,40,40,40,40,40,
  //   40,40,40,40,40,40,40,40,40,40,40,40,40,40,40,40,40,40,40,40,40,40,40,40,40,40,40,40,40,40,40,
  //   40,40,40,40,40,40,40,40,40,40,40,40,40,40,40,40,40,40,40,40,40,40,40,40,40,40,40,40,40,40,40,
  //   40,40,40,40,40,40,40,40,40,40,40,40,40,40,40,40,40,40,40,40,40,40,40,40,40,40,40,40,40,40,40,
  //   40,40,40,40,40,40,40,40,40,40,40,40,40,40,40,40,40,40,40,40,40,40,40,40,40,40,40,40,40,40,40,
  //   40,40,40,40,40,40,40,40,40,40,40,40,40,40,40,40,40,40,40,40,40,40,40,40,40,40,40,40,40,40,40,
  //   40,40,40,40,40,40,40,40,40,40,40,40,40,40,40,40,40,40,40,40,40,40,40,40,40,40,40,40,40,40,40,
  //   40,40,40,40,40,40,40,40,40,40,40,40,40,40,40,40,40,40,40,40,40,40,40,40,40,40,40,40,40,40,40,
  //   40,40,40,40,40,40,40,40,40,40,40,40,40,40,40,40
  //   contents of pc_sp_mul_control (hex, n*v repeats v):
  //   0,0,0,0,0,0,0,0,0,0,0,0,0,0,0,0,0,0,0,0,0,0,0,0,0,0,0,0,0,0,0,0,0,0,0,0,0,0,0,0,0,0,0,0,0,0,
  //   0,0,0,0,0,0,0,0,0,0,0,0,0,0,0,0,0,0,0,0,0,0,0,0,0,0,0,0,0,0,0,0,0,0,0,0,0,0,0,0,0,0,0,0,0,0,
  //   0,0,0,0,0,0,0,0,0,0,0,0,0,0,0,0,0,0,0,0,0,0,0,0,0,0,0,0,0,0,0,0,0,0,0,0,0,4,2,0,0,0,0,0,0,0,
  //   0,0,0,0,0,0,0,0,0,0,0,0,0,0,0,0,0,0,0,0,0,0,0,0,0,0,0,0,0,0,0,0,0,0,0,0,0,0,0,0,0,0,0,0,0,0,
  //   0,0,0,0,0,0,0,0,0,0,0,0,0,0,0,0,0,0,0,0,0,0,0,0,0,0,0,0,0,0,0,0,0,0,0,0,0,0,0,0,0,0,0,0,0,0,
  //   0,0,0,0,0,0,0,0,0,0,0,0,0,0,0,0,0,0,0,0,0,0,0,0,0,0,0,0,0,0,0,0,0,0,0,0,0,0,0,0,0,0,0,0,0,0,
  //   0,0,0,0,0,0,0,0,0,0,0,0,0,0,0,0,0,0,0,0,0,0,0,0,0,0,0,0,0,0,0,0,0,0,0,0,0,0,0,0,0,0,0,0,0,0,
  //   0,0,0,0,0,0,0,0,0,0,0,0,0,0,0,0,0,0,0,0,0,0,0,0,0,0,0,0,0,0,0,0,0,0,0,0,0,0,0,0,0,0,0,0,0,0,
  //   0,0,0,0,0,0,0,0,0,0,0,0,0,0,0,0,0,0,0,0,0,0,0,0,0,0,0,0,0,0,0,0,0,0,0,0,0,0,0,0,0,0,0,0,0,0,
  //   0,0,0,0,0,0,0,0,0,0,0,0,0,0,0,0,0,0,0,0,0,0,0,0,0,0,0,0,0,0,0,0,0,0,0,0,0,0,0,0,0,0,0,0,0,0,
  //   0,0,0,0,0,0,0,0,0,0,0,0,0,0,0,0,0,0,0,0,0,0,0,0,0,0,0,0,0,0,0,0,0,0,0,0,0,0,0,0,0,0,0,0,0,0,
  //   0,0,0,0,0,0
endmodule

/* Test case tomato-v1-burn:
op exec branch-en jump-type pc-src pc-link-we cycles pc-cond sp-out HALT_IN
# NOP
0 0 0 0 0 0 1 0 0 0
# NOP exec
0 1 0 0 0 0 1 0 0 0
# ADD
1 0 0 0 0 0 1 0 0 0
# ADD exec
1 1 0 0 0 0 1 0 0 0
# SUB
2 0 0 0 0 0 1 0 0 0
# SUB exec
2 1 0 0 0 0 1 0 0 0
# AND
3 0 0 0 0 0 1 0 0 0
# AND exec
3 1 0 0 0 0 1 0 0 0
# OR
4 0 0 0 0 0 1 0 0 0
# OR exec
4 1 0 0 0 0 1 0 0 0
# XOR
5 0 0 0 0 0 1 0 0 0
# XOR exec
5 1 0 0 0 0 1 0 0 0
# MOV
6 0 0 0 0 0 1 0 0 0
# MOV exec
6 1 0 0 0 0 1 0 0 0
# CMP
7 0 0 0 0 0 1 0 0 0
# CMP exec
7 1 0 0 0 0 1 0 0 0
# ADDI
32 0 0 0 0 0 1 0 0 0
# ADDI exec
32 1 0 0 0 0 1 0 0 0
# ANDI
33 0 0 0 0 0 1 0 0 0
# ANDI exec
33 1 0 0 0 0 1 0 0 0
# ORI
34 0 0 0 0 0 1 0 0 0
# ORI exec
34 1 0 0 0 0 1 0 0 0
# XORI
35 0 0 0 0 0 1 0 0 0
# XORI exec
35 1 0 0 0 0 1 0 0 0
# LUI
36 0 0 0 0 0 1 0 0 0
# LUI exec
36 1 0 0 0 0 1 0 0 0
# LSL
64 0 0 0 0 0 1 0 0 0
# LSL exec
64 1 0 0 0 0 1 0 0 0
# LSR
65 0 0 0 0 0 1 0 0 0
# LSR exec
65 1 0 0 0 0 1 0 0 0
# ASR
66 0 0 0 0 0 1 0 0 0
# ASR exec
66 1 0 0 0 0 1 0 0 0
# LW
96 0 0 0 0 0 2 0 0 0
# LW exec
96 1 0 0 0 0 2 0 0 0
# LB
97 0 0 0 0 0 2 0 0 0
# LB exec
97 1 0 0 0 0 2 0 0 0
# SW
104 0 0 0 0 0 2 0 0 0
# SW exec
104 1 0 0 0 0 2 0 0 0
# SB
105 0 0 0 0 0 2 0 0 0
# SB exec
105 1 0 0 0 0 2 0 0 0
# BEQ
128 0 1 0 0 0 1 0 0 0
# BEQ exec
128 1 1 0 0 0 1 0 0 0
# BNE
129 0 1 0 0 0 1 4 0 0
# BNE exec
129 1 1 0 0 0 1 4 0 0
# BLT
130 0 1 0 0 0 1 2 0 0
# BLT exec
130 1 1 0 0 0 1 2 0 0
# JMP
160 0 0 1 0 0 1 0 0 0
# JMP exec
160 1 0 1 0 0 1 0 0 0
# JAL
161 0 0 1 0 1 1 0 0 0
# JAL exec
161 1 0 1 0 1 1 0 0 0
# RET
162 0 0 1 2 0 1 0 0 0
# RET exec
162 1 0 1 2 0 1 0 0 0
# JR
163 0 0 1 2 0 1 0 0 0
# JR exec
163 1 0 1 2 0 1 0 0 0
# HALT
255 1 0 0 0 0 1 0 0 1
# HALT idle
255 0 0 0 0 0 1 0 0 0
*/
