// Digital circuit program-counter.dig as structural Verilog
module program_counter (
  input  [31:0] mem_din,
  input  [31:0] alu_in,
  input  [2:0] pc_src,
  input  [21:0] OFFSET,
  input  RESET,
  input  [1:0] cycles,
  input  [14:0] csr_flags,
  input  [3:0] pc_cond,
  input  jump_type,
  input  branch_en,
  input  INT_EN_IN,
  input  HALT_IN,
  input  INT_REQ,
  input  INT_VEC_0,
  input  INT_VEC_1,
  input  INT_VEC_2,
  input  link_in,
  input  clk,
  output [23:0] PC_OUT,
  output [23:0] PC_SAVE,
  output FETCH,
  output EXECUTE,
  output [23:0] PC_LINK
);

  wire and_1_out, and_2_out, and_3_out, and_5_out, and_7_out, and_8_out, COND_RESULT, HALT, INT_EN, INT_GATE,
       INT_GATE_prev, link_reg_en, match, MEM_WAIT, mux0, mux1, mux2, MUX_Y, nHALT, nor_4_out, not_1_out,
       not_3_out, not_4_out, nRESET, or_1_out, or_5_out, or_6_out, or_7_out, pc_load, pc_reg_en, seq0, seq1,
       seq_en, seq_rst, xnor_1_out, xnor_2_out;
  wire [23:0] multiplexer_1_out, multiplexer_2_out, pc_mux, pc_rel;
  wire [23:22] ir_abs_x;

  and and_1 (and_1_out, EXECUTE, link_in);
  and and_2 (and_2_out, FETCH, INT_GATE, INT_GATE_prev);
  D_FF d_ff_1 (.D(INT_GATE), .C(clk), .nQ(INT_GATE_prev));  // open: Q
  or or_1 (or_1_out, and_1_out, and_2_out);
  and and_3 (and_3_out, nHALT, or_1_out);
  or or_2 (link_reg_en, RESET, and_3_out);
  BitExtender #(.inputBits(1), .outputBits(2)) bitextender_1 (.in(OFFSET[21]), .out(ir_abs_x));
  Multiplexer #(.Bits(24)) multiplexer_1 (.sel(RESET), .in_0(PC_SAVE), .in_1({24{1'b0}}), .out(multiplexer_1_out));
  Register #(.Bits(24)) register_1 (.D(multiplexer_1_out), .C(clk), .en(link_reg_en), .Q(PC_LINK));
  or or_3 (mux0, INT_GATE, pc_src[0], FETCH);
  or or_4 (mux1, FETCH, INT_GATE, pc_src[1]);
  Multiplexer #(.Bits(24)) multiplexer_2 (.sel(RESET), .in_0(pc_mux), .in_1({24{1'b0}}), .out(multiplexer_2_out));
  or or_5 (or_5_out, jump_type, COND_RESULT);
  Add #(.Bits(24)) add_1 (.a({ir_abs_x, OFFSET}), .b(PC_OUT), .c_i(1'b0), .s(pc_rel));  // open: c_o
  Add #(.Bits(24)) add_2 (.a(24'h1), .b(PC_OUT), .c_i(1'b0), .s(PC_SAVE));  // open: c_o
  Register #(.Bits(24)) register_2 (.D(multiplexer_2_out), .C(clk), .en(pc_reg_en), .Q(PC_OUT));
  Multiplexer #(.Selector_Bits(3), .Bits(24)) multiplexer_3 (
    .sel({mux2, mux1, mux0}), .in_0({2'b00, OFFSET}), .in_1(pc_rel), .in_2(PC_LINK),
    .in_3({{18{1'b0}}, INT_VEC_2, INT_VEC_1, INT_VEC_0, 3'b000}), .in_4(alu_in[23:0]), .in_5(mem_din[23:0]),
    .in_6({24{1'b0}}), .in_7(PC_SAVE), .out(pc_mux));
  and and_4 (pc_load, EXECUTE, or_5_out);
  or or_6 (or_6_out, FETCH, INT_GATE, pc_load);
  or or_7 (or_7_out, FETCH, pc_src[2]);
  and and_5 (and_5_out, nHALT, or_6_out);
  and and_6 (mux2, or_7_out, not_1_out);
  not not_1 (not_1_out, INT_GATE);
  or or_8 (pc_reg_en, RESET, and_5_out);
  and and_7 (and_7_out, INT_EN_IN, nRESET);
  and and_8 (and_8_out, HALT_IN, nRESET);
  not not_2 (nRESET, RESET);
  D_FF d_ff_2 (.D(and_7_out), .C(clk), .Q(INT_EN));  // open: nQ
  D_FF d_ff_3 (.D(and_8_out), .C(clk), .Q(HALT));  // open: nQ
  Counter #(.Bits(2)) counter_1 (.en(1'b1), .C(seq_en), .clr(seq_rst), .out({seq1, seq0}));  // open: ovf
  not not_3 (not_3_out, seq0);
  not not_4 (not_4_out, seq1);
  nor nor_1 (FETCH, seq0, seq1);
  nor nor_2 (EXECUTE, not_3_out, seq1);
  nor nor_3 (MEM_WAIT, seq0, not_4_out);
  xnor xnor_1 (xnor_1_out, cycles[0], seq0);
  xnor xnor_2 (xnor_2_out, cycles[1], seq1);
  nor nor_4 (nor_4_out, match, RESET);
  and and_9 (INT_GATE, INT_REQ, INT_EN);
  and and_10 (seq_en, clk, nHALT);
  and and_11 (match, xnor_1_out, xnor_2_out);
  not not_5 (seq_rst, nor_4_out);
  not not_6 (nHALT, HALT);
  and and_12 (COND_RESULT, MUX_Y, branch_en);
  Multiplexer #(.Selector_Bits(4)) multiplexer_4 (
    .sel(pc_cond), .in_0(csr_flags[0]), .in_1(csr_flags[1]), .in_2(csr_flags[2]), .in_3(csr_flags[3]),
    .in_4(csr_flags[4]), .in_5(csr_flags[5]), .in_6(csr_flags[6]), .in_7(csr_flags[7]), .in_8(csr_flags[8]),
    .in_9(csr_flags[9]), .in_10(csr_flags[10]), .in_11(csr_flags[11]), .in_12(csr_flags[12]),
    .in_13(csr_flags[13]), .in_14(csr_flags[14]), .in_15(1'b0), .out(MUX_Y));

  // Other names for the same wires on the sheet: alu[23:0] = alu_in[23:0]; brch_en = branch_en; cyc0 = cycles[0];
  //   cyc1 = cycles[1]; int_vec[5:3] = {INT_VEC_2, INT_VEC_1, INT_VEC_0}; IR_ABS[21:0] = OFFSET;
  //   ir_abs_t[21:0] = OFFSET; ir_abs_x[21:0] = OFFSET; jmp_type = jump_type; mem_in[23:0] = mem_din[23:0];
  //   seq_out[1:0] = {seq1, seq0}

  // Notes on the sheet:
  //   OFFSET: default 1
  //   clk: default 1
  //   INPUTS
  //   OUTPUTS
  //   SEQUENCER
  //   BRANCH
endmodule

/* Test case pc-irq-jump:
clk cycles jump-type branch-en RESET pc-src OFFSET alu-in mem-din INT_EN_IN INT_REQ INT_VEC_0 INT_VEC_1 INT_VEC_2 PC-OUT PC-SAVE PC-LINK

# INT_GATE forces irq vector mux and pc-reg-en on FETCH
# PC-LINK must latch PC+1 (0x3) on first IRQ FETCH edge — irq_entry uses ~INT_GATE_prev

# RESET hold
0 0 0 0 1 0 0 0 0 0 0 0 0 0 x x x
C 0 0 0 1 0 0 0 0 0 0 0 0 0 0 1 0
0 0 0 0 1 0 0 0 0 0 0 0 0 0 0 1 0

# Release RESET, first FETCH
0 0 0 0 0 0 0 0 0 0 0 0 0 0 x x x
C 0 0 0 0 0 0 0 0 0 0 0 0 0 1 2 0
0 0 0 0 0 0 0 0 0 0 0 0 0 0 1 2 0

# Latch interrupt enable
0 0 0 0 0 0 0 0 0 1 0 0 0 0 x x x
C 0 0 0 0 0 0 0 0 1 0 0 0 0 2 3 0
0 0 0 0 0 0 0 0 0 1 0 0 0 0 2 3 0

# IRQ on FETCH with encoded vector — save return 0x3, jump 0x28
0 0 0 0 0 0 0 0 0 1 1 1 0 1 x x x
C 0 0 0 0 0 0 0 0 1 1 1 0 1 0x28 0x29 0x3
0 0 0 0 0 0 0 0 0 1 1 1 0 1 0x28 0x29 0x3

# INT_REQ still high: PC-LINK must NOT overwrite to 0x29
0 0 0 0 0 0 0 0 0 1 1 1 0 1 x x x
C 0 0 0 0 0 0 0 0 1 1 1 0 1 0x28 0x29 0x3
0 0 0 0 0 0 0 0 0 1 1 1 0 1 0x28 0x29 0x3

# FETCH with pc-src=0 OFFSET=max - IRQ override still loads vector
0 0 1 0 0 0 0xFFFFFF 0 0 1 1 1 0 1 x x x
C 0 1 0 0 0 0xFFFFFF 0 0 1 1 1 0 1 0x28 0x29 0x3
0 0 1 0 0 0 0xFFFFFF 0 0 1 1 1 0 1 0x28 0x29 0x3

# EXEC settle
0 1 0 0 0 0 0 0 0 1 0 0 0 0 x x x
C 1 0 0 0 0 0 0 0 1 0 0 0 0 0x29 0x2A 0x3
0 1 0 0 0 0 0 0 0 1 0 0 0 0 0x29 0x2A 0x3

# Abs jump to target address
0 1 1 0 0 0 0x50 0 0 1 0 0 0 0 x x x
C 1 1 0 0 0 0x50 0 0 1 0 0 0 0 0x50 0x51 0x3
0 1 1 0 0 0 0x50 0 0 1 0 0 0 0 0x50 0x51 0x3

# Clear INT_EN then INT_REQ ignored on FETCH
0 0 0 0 0 0 0 0 0 0 0 0 0 0 x x x
C 0 0 0 0 0 0 0 0 0 0 0 0 0 0x51 0x52 0x3
0 0 0 0 0 0 0 0 0 0 0 0 0 0 0x51 0x52 0x3
0 0 0 0 0 0 0 0 0 0 1 1 0 1 x x x
C 0 0 0 0 0 0 0 0 0 1 1 0 1 0x52 0x53 0x3
0 0 0 0 0 0 0 0 0 0 1 1 0 1 0x52 0x53 0x3
*/

/* Test case pc-fetch-override:
clk cycles jump-type branch-en RESET pc-src OFFSET alu-in mem-din csr_flags pc-cond PC-OUT PC-SAVE

# FETCH forces mux sel=7 (PC+1); jump-type/pc-src ignored in FETCH

# RESET hold
0 0 0 0 1 0 0 0 0 0 0 x x
C 0 0 0 1 0 0 0 0 0 0 0 1
0 0 0 0 1 0 0 0 0 0 0 0 1

# Release RESET, first FETCH
0 0 0 0 0 0 0 0 0 0 0 x x
C 0 0 0 0 0 0 0 0 0 0 1 2
0 0 0 0 0 0 0 0 0 0 0 1 2

# FETCH: pc-src=0 OFFSET=max jump-type=1 ignored (increment only)
0 0 1 0 0 0 0xFFFFFF 0 0 0 0 x x
C 0 1 0 0 0 0xFFFFFF 0 0 0 0 2 3
0 0 1 0 0 0 0xFFFFFF 0 0 0 0 2 3

# FETCH: pc-src=1 negative offset (bit21=1) increment only
0 0 1 0 0 1 0x200000 0 0 0 0 x x
C 0 1 0 0 1 0x200000 0 0 0 0 3 4
0 0 1 0 0 1 0x200000 0 0 0 0 3 4

# EXEC settle
0 1 0 0 0 0 0 0 0 0 0 x x
C 1 0 0 0 0 0 0 0 0 0 4 5
0 1 0 0 0 0 0 0 0 0 0 4 5

# EXEC: same pc-src=1 offset -4 - rel jump PC=0
0 1 1 0 0 1 0x3FFFFC 0 0 0 0 x x
C 1 1 0 0 1 0x3FFFFC 0 0 0 0 0 1
0 1 1 0 0 1 0x3FFFFC 0 0 0 0 0 1

# FETCH after jump: increment from 0
0 0 0 0 0 0 0 0 0 0 0 x x
C 0 0 0 0 0 0 0 0 0 0 1 2
0 0 0 0 0 0 0 0 0 0 0 1 2
*/

/* Test case pc-link-gate:
clk cycles link-in jump-type RESET pc-src OFFSET alu-in mem-din PC-OUT PC-SAVE PC-LINK

# Negative enable gating for link-in

# Setup: FETCH to PC=1
0 0 0 0 1 0 0 0 0 x x x
C 0 0 0 1 0 0 0 0 0 1 0
0 0 0 0 0 0 0 0 0 x x x
C 0 0 0 0 0 0 0 0 1 2 0
0 0 0 0 0 0 0 0 0 1 2 0

# FETCH only (cycles=0): link-in=1 must not latch
0 0 1 0 0 0 0 0 0 x x x
C 0 0 1 0 0 0 0 0 2 3 0
0 0 1 0 0 0 0 0 0 2 3 0

# EXEC, link-in=0: must not latch
0 1 0 0 0 0 0 0 0 x x x
C 1 0 0 0 0 0 0 0 3 4 0
0 1 0 0 0 0 0 0 0 3 4 0

# EXEC, link-in=1: sanity latch PC-SAVE=4
0 1 1 0 0 0 0 0 0 x x x
C 1 1 0 0 0 0 0 0 3 4 4
0 1 1 0 0 0 0 0 0 3 4 4
*/

/* Test case Exhaustive ISA Datapath Test:
clk cycles jump-type branch-en RESET pc-src OFFSET alu-in mem-din csr_flags pc-cond PC-OUT
0 0 0 0 1 0 0 0 0 3 0 x
C 0 0 0 1 0 0 0 0 3 0 x
0 0 0 0 0 0 0 0 0 3 0 x
C 0 0 0 0 0 0 0 0 3 0 x
0 1 0 0 0 0 5 128 64 3 0 x
C 1 0 0 0 0 5 128 64 3 0 0x2
0 0 0 0 1 0 0 0 0 3 0 x
C 0 0 0 1 0 0 0 0 3 0 x
0 0 0 0 0 0 0 0 0 3 0 x
C 0 0 0 0 0 0 0 0 3 0 x
0 1 0 0 0 0 5 128 64 3 0 x
C 1 0 0 0 0 5 128 64 3 0 0x2
0 0 0 0 1 0 0 0 0 3 0 x
C 0 0 0 1 0 0 0 0 3 0 x
0 0 0 0 0 0 0 0 0 3 0 x
C 0 0 0 0 0 0 0 0 3 0 x
0 1 0 0 0 0 5 128 64 3 0 x
C 1 0 0 0 0 5 128 64 3 0 0x2
0 0 0 0 1 0 0 0 0 3 0 x
C 0 0 0 1 0 0 0 0 3 0 x
0 0 0 0 0 0 0 0 0 3 0 x
C 0 0 0 0 0 0 0 0 3 0 x
0 1 0 0 0 0 5 128 64 3 0 x
C 1 0 0 0 0 5 128 64 3 0 0x2
0 0 0 0 1 0 0 0 0 3 0 x
C 0 0 0 1 0 0 0 0 3 0 x
0 0 0 0 0 0 0 0 0 3 0 x
C 0 0 0 0 0 0 0 0 3 0 x
0 1 0 0 0 0 5 128 64 3 0 x
C 1 0 0 0 0 5 128 64 3 0 0x2
0 0 0 0 1 0 0 0 0 3 0 x
C 0 0 0 1 0 0 0 0 3 0 x
0 0 0 0 0 0 0 0 0 3 0 x
C 0 0 0 0 0 0 0 0 3 0 x
0 1 0 0 0 0 5 128 64 3 0 x
C 1 0 0 0 0 5 128 64 3 0 0x2
0 0 0 0 1 0 0 0 0 3 0 x
C 0 0 0 1 0 0 0 0 3 0 x
0 0 0 0 0 0 0 0 0 3 0 x
C 0 0 0 0 0 0 0 0 3 0 x
0 1 0 0 0 0 5 128 64 3 0 x
C 1 0 0 0 0 5 128 64 3 0 0x2
0 0 0 0 1 0 0 0 0 3 0 x
C 0 0 0 1 0 0 0 0 3 0 x
0 0 0 0 0 0 0 0 0 3 0 x
C 0 0 0 0 0 0 0 0 3 0 x
0 1 0 0 0 0 5 128 64 3 0 x
C 1 0 0 0 0 5 128 64 3 0 0x2
0 0 0 0 1 0 0 0 0 3 0 x
C 0 0 0 1 0 0 0 0 3 0 x
0 0 0 0 0 0 0 0 0 3 0 x
C 0 0 0 0 0 0 0 0 3 0 x
0 1 0 0 0 0 5 128 64 3 0 x
C 1 0 0 0 0 5 128 64 3 0 0x2
0 0 0 0 1 0 0 0 0 3 0 x
C 0 0 0 1 0 0 0 0 3 0 x
0 0 0 0 0 0 0 0 0 3 0 x
C 0 0 0 0 0 0 0 0 3 0 x
0 1 0 0 0 0 5 128 64 3 0 x
C 1 0 0 0 0 5 128 64 3 0 0x2
0 0 0 0 1 0 0 0 0 3 0 x
C 0 0 0 1 0 0 0 0 3 0 x
0 0 0 0 0 0 0 0 0 3 0 x
C 0 0 0 0 0 0 0 0 3 0 x
0 1 0 0 0 0 5 128 64 3 0 x
C 1 0 0 0 0 5 128 64 3 0 0x2
0 0 0 0 1 0 0 0 0 3 0 x
C 0 0 0 1 0 0 0 0 3 0 x
0 0 0 0 0 0 0 0 0 3 0 x
C 0 0 0 0 0 0 0 0 3 0 x
0 1 0 0 0 0 5 128 64 3 0 x
C 1 0 0 0 0 5 128 64 3 0 0x2
0 0 0 0 1 0 0 0 0 3 0 x
C 0 0 0 1 0 0 0 0 3 0 x
0 0 0 0 0 0 0 0 0 3 0 x
C 0 0 0 0 0 0 0 0 3 0 x
0 1 0 0 0 0 5 128 64 3 0 x
C 1 0 0 0 0 5 128 64 3 0 0x2
0 0 0 0 1 0 0 0 0 3 0 x
C 0 0 0 1 0 0 0 0 3 0 x
0 0 0 0 0 0 0 0 0 3 0 x
C 0 0 0 0 0 0 0 0 3 0 x
0 1 0 0 0 0 5 128 64 3 0 x
C 1 0 0 0 0 5 128 64 3 0 0x2
0 0 0 0 1 0 0 0 0 3 0 x
C 0 0 0 1 0 0 0 0 3 0 x
0 0 0 0 0 0 0 0 0 3 0 x
C 0 0 0 0 0 0 0 0 3 0 x
0 1 0 0 0 0 5 128 64 3 0 x
C 1 0 0 0 0 5 128 64 3 0 0x2
0 0 0 0 1 0 0 0 0 3 0 x
C 0 0 0 1 0 0 0 0 3 0 x
0 0 0 0 0 0 0 0 0 3 0 x
C 0 0 0 0 0 0 0 0 3 0 x
0 1 0 0 0 0 5 128 64 3 0 x
C 1 0 0 0 0 5 128 64 3 0 0x2
0 0 0 0 1 0 0 0 0 3 0 x
C 0 0 0 1 0 0 0 0 3 0 x
0 0 0 0 0 0 0 0 0 3 0 x
C 0 0 0 0 0 0 0 0 3 0 x
0 1 0 0 0 0 5 128 64 3 0 x
C 1 0 0 0 0 5 128 64 3 0 0x2
0 0 0 0 1 0 0 0 0 3 0 x
C 0 0 0 1 0 0 0 0 3 0 x
0 0 0 0 0 0 0 0 0 3 0 x
C 0 0 0 0 0 0 0 0 3 0 x
0 1 0 0 0 0 5 128 64 3 0 x
C 1 0 0 0 0 5 128 64 3 0 0x2
0 0 0 0 1 0 0 0 0 3 0 x
C 0 0 0 1 0 0 0 0 3 0 x
0 0 0 0 0 0 0 0 0 3 0 x
C 0 0 0 0 0 0 0 0 3 0 x
0 1 0 0 0 0 5 128 64 3 0 x
C 1 0 0 0 0 5 128 64 3 0 0x2
0 0 0 0 1 0 0 0 0 3 0 x
C 0 0 0 1 0 0 0 0 3 0 x
0 0 0 0 0 0 0 0 0 3 0 x
C 0 0 0 0 0 0 0 0 3 0 x
0 1 0 0 0 0 5 128 64 3 0 x
C 1 0 0 0 0 5 128 64 3 0 0x2
0 0 0 0 1 0 0 0 0 3 0 x
C 0 0 0 1 0 0 0 0 3 0 x
0 0 0 0 0 0 0 0 0 3 0 x
C 0 0 0 0 0 0 0 0 3 0 x
0 1 0 0 0 0 5 128 64 3 0 x
C 1 0 0 0 0 5 128 64 3 0 0x2
0 0 0 0 1 0 0 0 0 3 0 x
C 0 0 0 1 0 0 0 0 3 0 x
0 0 0 0 0 0 0 0 0 3 0 x
C 0 0 0 0 0 0 0 0 3 0 x
0 1 0 0 0 0 5 128 64 3 0 x
C 1 0 0 0 0 5 128 64 3 0 0x2
0 0 0 0 1 0 0 0 0 3 0 x
C 0 0 0 1 0 0 0 0 3 0 x
0 0 0 0 0 0 0 0 0 3 0 x
C 0 0 0 0 0 0 0 0 3 0 x
0 1 0 0 0 0 5 128 64 3 0 x
C 1 0 0 0 0 5 128 64 3 0 0x2
0 0 0 0 1 0 0 0 0 3 0 x
C 0 0 0 1 0 0 0 0 3 0 x
0 0 0 0 0 0 0 0 0 3 0 x
C 0 0 0 0 0 0 0 0 3 0 x
0 1 0 0 0 0 5 128 64 3 0 x
C 1 0 0 0 0 5 128 64 3 0 0x2
0 0 0 0 1 0 0 0 0 3 0 x
C 0 0 0 1 0 0 0 0 3 0 x
0 0 0 0 0 0 0 0 0 3 0 x
C 0 0 0 0 0 0 0 0 3 0 x
0 1 0 0 0 0 5 128 64 3 0 x
C 1 0 0 0 0 5 128 64 3 0 0x2
0 0 0 0 1 0 0 0 0 3 0 x
C 0 0 0 1 0 0 0 0 3 0 x
0 0 0 0 0 0 0 0 0 3 0 x
C 0 0 0 0 0 0 0 0 3 0 x
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*/

/* Test case pc-irq-ret:
clk cycles jump-type branch-en RESET pc-src OFFSET alu-in mem-din INT_EN_IN INT_REQ INT_VEC_0 INT_VEC_1 INT_VEC_2 PC-OUT PC-SAVE PC-LINK

# Full keyboard IRQ: vector entry saves PC+1, IRET (pc-src=2) resumes

# RESET hold
0 0 0 0 1 0 0 0 0 0 0 0 0 0 x x x
C 0 0 0 1 0 0 0 0 0 0 0 0 0 0 1 0
0 0 0 0 1 0 0 0 0 0 0 0 0 0 0 1 0

# FETCH to PC=1
0 0 0 0 0 0 0 0 0 0 0 0 0 0 x x x
C 0 0 0 0 0 0 0 0 0 0 0 0 0 1 2 0
0 0 0 0 0 0 0 0 0 0 0 0 0 0 1 2 0

# SEI — INT_EN latched
0 0 0 0 0 0 0 0 0 1 0 0 0 0 x x x
C 0 0 0 0 0 0 0 0 1 0 0 0 0 2 3 0
0 0 0 0 0 0 0 0 0 1 0 0 0 0 2 3 0

# IRQ entry @ PC=2: PC-LINK=3, PC=0x28
0 0 0 0 0 0 0 0 0 1 1 1 0 1 x x x
C 0 0 0 0 0 0 0 0 1 1 1 0 1 0x28 0x29 0x3
0 0 0 0 0 0 0 0 0 1 1 1 0 1 0x28 0x29 0x3

# Clear INT_REQ (handler running)
0 0 0 0 0 0 0 0 0 1 0 0 0 0 x x x
C 0 0 0 0 0 0 0 0 1 0 0 0 0 0x29 0x2A 0x3
0 0 0 0 0 0 0 0 0 1 0 0 0 0 0x29 0x2A 0x3

# EXEC settle in handler
0 1 0 0 0 0 0 0 0 1 0 0 0 0 x x x
C 1 0 0 0 0 0 0 0 1 0 0 0 0 0x2A 0x2B 0x3
0 1 0 0 0 0 0 0 0 1 0 0 0 0 0x2A 0x2B 0x3

# IRET: pc-src=2 jump-type=1 restores PC-LINK (resume @ 0x3)
0 1 1 0 0 2 0 0 0 1 0 0 0 0 x x x
C 1 1 0 0 2 0 0 0 1 0 0 0 0 0x3 0x4 0x3
0 1 1 0 0 2 0 0 0 1 0 0 0 0 0x3 0x4 0x3

# Resume: FETCH increments from return point
0 0 0 0 0 0 0 0 0 1 0 0 0 0 x x x
C 0 0 0 0 0 0 0 0 1 0 0 0 0 0x4 0x5 0x3
0 0 0 0 0 0 0 0 0 1 0 0 0 0 0x4 0x5 0x3
*/

/* Test case pc-halt-frozen:
clk cycles HALT_IN jump-type RESET pc-src OFFSET alu-in mem-din PC-OUT PC-SAVE PC-LINK link-in

# HALT freezes PC and link via CLK_GATED=0

# RESET hold
0 0 0 0 1 0 0 0 0 x x x 0
C 0 0 0 1 0 0 0 0 0 1 0 0
0 0 0 0 1 0 0 0 0 0 1 0 0

# Release RESET, FETCH increments
0 0 0 0 0 0 0 0 0 x x x 0
C 0 0 0 0 0 0 0 0 1 2 0 0
0 0 0 0 0 0 0 0 0 1 2 0 0
0 0 0 0 0 0 0 0 0 x x x 0
C 0 0 0 0 0 0 0 0 2 3 0 0
0 0 0 0 0 0 0 0 0 2 3 0 0

# EXEC settle (PC=3)
0 1 0 0 0 0 0 0 0 x x x 0
C 1 0 0 0 0 0 0 0 3 4 0 0
0 1 0 0 0 0 0 0 0 3 4 0 0

# Latch HALT=1 on clock edge
0 1 1 0 0 0 0 0 0 x x x 0
C 1 1 0 0 0 0 0 0 3 4 0 0
0 1 1 0 0 0 0 0 0 3 4 0 0

# Halted: abs jump must not change PC
0 1 1 1 0 0 0x50 0 0 x x x 0
C 1 1 1 0 0 0x50 0 0 3 4 0 0
0 1 1 1 0 0 0x50 0 0 3 4 0 0

# Halted + link-in=1 in EXEC: PC-LINK unchanged
0 1 1 0 0 0 0 0 0 x x x 1
C 1 1 0 0 0 0 0 0 3 4 0 1
0 1 1 0 0 0 0 0 0 3 4 0 1

# RESET while halted clears PC and link
0 1 1 0 1 0 0 0 0 x x x 1
C 1 1 0 1 0 0 0 0 0 1 0 0
0 1 1 0 1 0 0 0 0 0 1 0 0

# Release RESET, clear HALT (two clocks)
0 1 0 0 0 0 0 0 0 x x x 0
C 1 0 0 0 0 0 0 0 1 2 0 0
0 1 0 0 0 0 0 0 0 1 2 0 0
C 1 0 0 0 0 0 0 0 1 2 0 0
0 1 0 0 0 0 0 0 0 1 2 0 0

# EXEC settle then jump works after de-halt
0 1 0 0 0 0 0 0 0 x x x 0
C 1 0 0 0 0 0 0 0 2 3 0 0
0 1 0 0 0 0 0 0 0 2 3 0 0
0 1 0 1 0 0 0x40 0 0 x x x 0
C 1 0 1 0 0 0x40 0 0 0x40 0x41 0 0
0 1 0 1 0 0 0x40 0 0 0x40 0x41 0 0
*/

/* Test case pc-mux-sources:
clk cycles jump-type branch-en RESET pc-src OFFSET alu-in mem-din csr_flags pc-cond INT_VEC_0 INT_VEC_1 INT_VEC_2 PC-OUT PC-SAVE PC-LINK

# Untested mux sources: pc-src 5 (mem), 6 (glue/0), 3 (int-vec), 2 (RET miss)

# RESET hold
0 0 0 0 1 0 0 0 0 0 0 0 0 0 x x x
C 0 0 0 1 0 0 0 0 0 0 0 0 0 0 1 0
0 0 0 0 1 0 0 0 0 0 0 0 0 0 0 1 0

# Release RESET, FETCH
0 0 0 0 0 0 0 0 0 0 0 0 0 0 x x x
C 0 0 0 0 0 0 0 0 0 0 0 0 0 1 2 0
0 0 0 0 0 0 0 0 0 0 0 0 0 0 1 2 0

# EXEC settle
0 1 0 0 0 0 0 0 0 0 0 0 0 0 x x x
C 1 0 0 0 0 0 0 0 0 0 0 0 0 2 3 0
0 1 0 0 0 0 0 0 0 0 0 0 0 0 2 3 0

# 1. mem jump (pc-src=5): mem-din lower 24b = 0xBBCCDD
0 1 1 0 0 5 0 0 0xBBCCDD 0 0 0 0 0 x x x
C 1 1 0 0 5 0 0 0xBBCCDD 0 0 0 0 0 0xBBCCDD 0xBBCCDE 0
0 1 1 0 0 5 0 0 0xBBCCDD 0 0 0 0 0 0xBBCCDD 0xBBCCDE 0

# FETCH->EXEC setup
0 1 0 0 0 0 0 0 0 0 0 0 0 0 x x x
C 1 0 0 0 0 0 0 0 0 0 0 0 0 0xBBCCDE 0xBBCCDF 0
0 1 0 0 0 0 0 0 0 0 0 0 0 0 0xBBCCDE 0xBBCCDF 0

# 2. glue jump (pc-src=6): loads 0
0 1 1 0 0 6 0 0 0 0 0 0 0 0 x x x
C 1 1 0 0 6 0 0 0 0 0 0 0 0 0 1 0
0 1 1 0 0 6 0 0 0 0 0 0 0 0 0 1 0

# FETCH->EXEC setup
0 1 0 0 0 0 0 0 0 0 0 0 0 0 x x x
C 1 0 0 0 0 0 0 0 0 0 0 0 0 1 2 0
0 1 0 0 0 0 0 0 0 0 0 0 0 0 1 2 0

# 3. int-vec jump (pc-src=3): vector 0x28 (VEC_0=1 VEC_1=0 VEC_2=1)
0 1 1 0 0 3 0 0 0 0 0 1 0 1 x x x
C 1 1 0 0 3 0 0 0 0 0 1 0 1 0x28 0x29 0
0 1 1 0 0 3 0 0 0 0 0 1 0 1 0x28 0x29 0

# FETCH->EXEC setup
0 1 0 0 0 0 0 0 0 0 0 0 0 0 x x x
C 1 0 0 0 0 0 0 0 0 0 0 0 0 0x29 0x2A 0
0 1 0 0 0 0 0 0 0 0 0 0 0 0 0x29 0x2A 0

# 4. RET miss (pc-src=2, PC-LINK=0)
0 1 1 0 0 2 0 0 0 0 0 0 0 0 x x x
C 1 1 0 0 2 0 0 0 0 0 0 0 0 0 1 0
0 1 1 0 0 2 0 0 0 0 0 0 0 0 0 1 0
*/

/* Test case pc-link-latch:
clk cycles link-in jump-type RESET pc-src OFFSET alu-in mem-din PC-OUT PC-SAVE PC-LINK

# Latch PC-SAVE into pc_link on EXEC when link-in=1 (RESET=1 hold / RESET=0 run)

# 1. RESET hold
0 0 0 0 1 0 0 0 0 x x x
C 0 0 0 1 0 0 0 0 0 1 0

# 2. Release RESET, FETCH (PC 0->1)
0 0 0 0 0 0 0 0 0 x x x
C 0 0 0 0 0 0 0 0 1 2 0
0 0 0 0 0 0 0 0 0 1 2 0

# 3. EXEC (no link-in) — advance to PC=2
0 1 0 0 0 0 0 0 0 x x x
C 1 0 0 0 0 0 0 0 2 3 0
0 1 0 0 0 0 0 0 0 2 3 0

# 4. EXEC + link-in: latch PC-SAVE=3 into pc_link
0 1 1 0 0 0 0 0 0 x x x
C 1 1 0 0 0 0 0 0 2 3 3
0 1 1 0 0 0 0 0 0 2 3 3

# 5. Hold — pc_link unchanged
0 1 1 0 0 0 0 0 0 2 3 3
*/

/* Test case pc-link-ret:
clk cycles link-in jump-type RESET pc-src OFFSET alu-in mem-din PC-OUT PC-SAVE PC-LINK

# RET via mux in_2 (pc-src=2)

# Latch PC-LINK=2
0 0 0 0 1 0 0 0 0 x x x
C 0 0 0 1 0 0 0 0 0 1 0
0 0 0 0 0 0 0 0 0 x x x
C 0 0 0 0 0 0 0 0 1 2 0
0 0 0 0 0 0 0 0 0 1 2 0
0 1 0 0 0 0 0 0 0 x x x
C 1 0 0 0 0 0 0 0 2 3 0
0 1 0 0 0 0 0 0 0 2 3 0
0 1 1 0 0 0 0 0 0 x x x
C 1 1 0 0 0 0 0 0 2 3 3
0 1 1 0 0 0 0 0 0 2 3 3

# EXEC settle before jump
0 1 0 0 0 0 0 0 0 x x x
C 1 0 0 0 0 0 0 0 3 4 3
0 1 0 0 0 0 0 0 0 3 4 3

# Jump away to 0x100
0 1 0 1 0 0 0x100 0 0 x x x
C 1 0 1 0 0 0x100 0 0 0x100 0x101 3
0 1 0 1 0 0 0x100 0 0 0x100 0x101 3

# FETCH — PC increments
0 0 0 0 0 0 0 0 0 x x x
C 0 0 0 0 0 0 0 0 0x101 0x102 3
0 0 0 0 0 0 0 0 0 0x101 0x102 3

# EXEC settle before RET (avoid FETCH mux override)
0 1 0 0 0 0 0 0 0 x x x
C 1 0 0 0 0 0 0 0 0x102 0x103 3
0 1 0 0 0 0 0 0 0 0x102 0x103 3

# RET: pc-src=2 restores PC-LINK
0 1 0 1 0 2 0 0 0 x x x
C 1 0 1 0 2 0 0 0 3 4 3
0 1 0 1 0 2 0 0 0 3 4 3
*/

/* Test case pc-link-reset:
clk cycles link-in jump-type RESET pc-src OFFSET alu-in mem-din PC-OUT PC-SAVE PC-LINK

# RESET clears pc_link flop

# Latch PC-LINK=2
0 0 0 0 1 0 0 0 0 x x x
C 0 0 0 1 0 0 0 0 0 1 0
0 0 0 0 0 0 0 0 0 x x x
C 0 0 0 0 0 0 0 0 1 2 0
0 0 0 0 0 0 0 0 0 1 2 0
0 1 0 0 0 0 0 0 0 x x x
C 1 0 0 0 0 0 0 0 2 3 0
0 1 0 0 0 0 0 0 0 2 3 0
0 1 1 0 0 0 0 0 0 x x x
C 1 1 0 0 0 0 0 0 2 3 3
0 1 1 0 0 0 0 0 0 2 3 3

# RESET=1 clocks link to 0
0 1 1 0 1 0 0 0 0 2 3 3
C 1 1 0 1 0 0 0 0 0 1 0
0 1 1 0 1 0 0 0 0 0 1 0

# Release RESET — pc_link stays 0
0 1 1 0 0 0 0 0 0 0 1 0
*/

/* Test case pc-link-edge:
clk cycles link-in jump-type RESET HALT_IN pc-src OFFSET alu-in mem-din PC-OUT PC-SAVE PC-LINK

# Link register edge cases: overwrite, RESET priority, halt block, post-RET latch

# RESET hold
0 0 0 0 1 0 0 0 0 0 x x x
C 0 0 0 1 0 0 0 0 0 0 1 0
0 0 0 0 1 0 0 0 0 0 0 1 0

# Release RESET, FETCH
0 0 0 0 0 0 0 0 0 0 x x x
C 0 0 0 0 0 0 0 0 0 1 2 0
0 0 0 0 0 0 0 0 0 0 1 2 0

# EXEC settle
0 1 0 0 0 0 0 0 0 0 x x x
C 1 0 0 0 0 0 0 0 0 2 3 0
0 1 0 0 0 0 0 0 0 0 2 3 0

# Jump to 0xAABB
0 1 0 1 0 0 0 0xAABB 0 0 x x x
C 1 0 1 0 0 0 0xAABB 0 0 0xAABB 0xAABC 0
0 1 0 1 0 0 0 0xAABB 0 0 0xAABB 0xAABC 0

# EXEC settle, latch PC-SAVE=0xAABC
0 1 0 0 0 0 0 0 0 0 x x x
C 1 0 0 0 0 0 0 0 0 0xAABC 0xAABD 0
0 1 0 0 0 0 0 0 0 0 0xAABC 0xAABD 0
0 1 1 0 0 0 0 0 0 0 x x x
C 1 1 0 0 0 0 0 0 0 0xAABC 0xAABD 0xAABD
0 1 1 0 0 0 0 0 0 0 0xAABC 0xAABD 0xAABD

# Second latch overwrites link
0 1 0 0 0 0 0 0 0 0 x x x
C 1 0 0 0 0 0 0 0 0 0xAABD 0xAABE 0xAABD
0 1 0 0 0 0 0 0 0 0 0xAABD 0xAABE 0xAABD
0 1 1 0 0 0 0 0 0 0 x x x
C 1 1 0 0 0 0 0 0 0 0xAABD 0xAABE 0xAABE
0 1 1 0 0 0 0 0 0 0 0xAABD 0xAABE 0xAABE

# RESET during EXEC with link-in=1 clears link
0 1 1 0 1 0 0 0 0 0 x x x
C 1 1 0 1 0 0 0 0 0 0 1 0
0 1 1 0 1 0 0 0 0 0 0 1 0
*/

/* Test case pc-boundary-arith:
clk cycles jump-type branch-en RESET pc-src OFFSET alu-in mem-din csr_flags pc-cond PC-OUT PC-SAVE

# 24-bit wrap and sign-ext relative adder edge cases

# RESET hold
0 0 0 0 1 0 0 0 0 0 0 x x
C 0 0 0 1 0 0 0 0 0 0 0 1
0 0 0 0 1 0 0 0 0 0 0 0 1

# Release RESET, FETCH
0 0 0 0 0 0 0 0 0 0 0 x x
C 0 0 0 0 0 0 0 0 0 0 1 2
0 0 0 0 0 0 0 0 0 0 0 1 2

# EXEC settle
0 1 0 0 0 0 0 0 0 0 0 x x
C 1 0 0 0 0 0 0 0 0 0 2 3
0 1 0 0 0 0 0 0 0 0 0 2 3

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*/

/* Test case program-counter:
clk cycles jump-type branch-en RESET pc-src OFFSET alu-in mem-din csr_flags pc-cond PC-OUT PC-SAVE

# PC smoke (cycles=0 FETCH / cycles=1 EXEC). RESET=1 hold / RESET=0 run.
# Jumps: jump-type=1 in EXEC. Branches: branch-en=1, jump-type=0, flags+pc-cond.

# 1. Idle
0 0 0 0 0 0 0 0 0 0 0 0 1

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*/
