// Digital circuit register.dig as structural Verilog
module register (
  input  WE,
  input  [31:0] DATA_W,
  input  [5:0] ADDR_A,
  input  [5:0] ADDR_B,
  input  [5:0] ADDR_W,
  input  EXEC,
  input  clk,
  input  [3:0] BANK_SEL,
  input  Bank_en,
  output [31:0] DATA_A,
  output [31:0] DATA_B,
  output [31:0] DATA_C
);

  wire ram_and;
  wire [9:6] ADDR_A_6;

  RAMDualAccess #(.AddrBits(10), .Bits(32)) U1 (
    .str(ram_and), .C(clk), .ld(1'b1), .A1({ADDR_A_6, ADDR_W}), .Din1(DATA_W), .A2({ADDR_A_6, ADDR_A}),
    .D2(DATA_A));  // open: D1
  and and_1 (ram_and, EXEC, WE);
  D_FF #(.Bits(4)) d_ff_1 (.D(BANK_SEL), .C(Bank_en), .Q(ADDR_A_6));  // open: nQ
  RAMDualAccess #(.AddrBits(10), .Bits(32)) U2 (
    .str(ram_and), .C(clk), .ld(1'b1), .A1({ADDR_A_6, ADDR_W}), .Din1(DATA_W), .A2({ADDR_A_6, ADDR_B}),
    .D2(DATA_B));  // open: D1
  RAMDualAccess #(.AddrBits(10), .Bits(32)) U3 (
    .str(ram_and), .C(clk), .ld(1'b1), .A1({ADDR_A_6, ADDR_W}), .Din1(DATA_W), .A2({ADDR_A_6, ADDR_W}),
    .D2(DATA_C));  // open: D1

  // Other names for the same wires on the sheet: ADDR_A_6[5:0] = ADDR_A; ADDR_B_6[9:0] = {ADDR_A_6, ADDR_B};
  //   ADDR_W_6[9:0] = {ADDR_A_6, ADDR_W}; bank[3:0] = ADDR_A_6

  // Notes on the sheet:
  //   DATA_W: default 43981
endmodule

/* Test case regfile-exhaustive:
clk WE EXEC DATA_W ADDR_A ADDR_B ADDR_W BANK_SEL Bank_en addr_c_sel DATA_A DATA_B DATA_C
# 6-bit reg indices; phys={bank[3:0],reg[5:0]}; port C reads ADDR_W (bool3)
# 1. Unwritten memory reads as zero (combinational)
0 0 0 0x00000000 0 0 0 0 0 0 0x00000000 0x00000000 0x00000000
0 0 0 0x00000000 1 2 0 0 0 0 0x00000000 0x00000000 0x00000000
0 0 0 0x00000000 0x3F 0x20 0 0 0 0 0x00000000 0x00000000 0x00000000
# 2. WRITE_REG — EXEC=1 WE=1 on clk posedge
0 1 1 0x0000ABCD 0 0 1 0 0 0 x x x
C 1 1 0x0000ABCD 0 0 1 0 0 0 x x x
0 1 1 0x0000ABCD 0 0 1 0 0 0 x x x
0 0 0 0x00000000 1 1 1 0 0 0 0x0000ABCD 0x0000ABCD 0x0000ABCD
0 1 1 0xDEADBEEF 0 0 7 0 0 0 x x x
C 1 1 0xDEADBEEF 0 0 7 0 0 0 x x x
0 1 1 0xDEADBEEF 0 0 7 0 0 0 x x x
0 0 0 0x00000000 7 7 7 0 0 0 0xDEADBEEF 0xDEADBEEF 0xDEADBEEF
# 3. WE=0 — no write on posedge
0 0 1 0x11111111 0 0 10 0 0 0 x x x
C 0 1 0x11111111 0 0 10 0 0 0 x x x
0 0 1 0x11111111 0 0 10 0 0 0 x x x
0 0 0 0x00000000 10 10 0 0 0 0 0x00000000 0x00000000 0x00000000
0 1 1 0x22222222 0 0 10 0 0 0 x x x
C 1 1 0x22222222 0 0 10 0 0 0 x x x
0 1 1 0x22222222 0 0 10 0 0 0 x x x
0 0 0 0x00000000 10 10 10 0 0 0 0x22222222 0x22222222 0x22222222
# 4. EXEC=0 — no write on posedge
0 1 0 0x33333333 0 0 11 0 0 0 x x x
C 1 0 0x33333333 0 0 11 0 0 0 x x x
0 1 0 0x33333333 0 0 11 0 0 0 x x x
0 0 0 0x00000000 11 11 0 0 0 0 0x00000000 0x00000000 0x00000000
0 1 1 0x44444444 0 0 11 0 0 0 x x x
C 1 1 0x44444444 0 0 11 0 0 0 x x x
0 1 1 0x44444444 0 0 11 0 0 0 x x x
0 0 0 0x00000000 11 11 11 0 0 0 0x44444444 0x44444444 0x44444444
# 5. Write gating matrix (fixed DATA_W on C)
0 0 0 0xA0000000 0x14 0x14 0x14 0 0 0 x x x
C 0 0 0xA0000000 0x14 0x14 0x14 0 0 0 x x x
0 0 0 0xA0000000 0x14 0x14 0x14 0 0 0 0x00000000 0x00000000 0x00000000
0 0 1 0xA0000001 0x15 0x15 0x15 0 0 0 x x x
C 0 1 0xA0000001 0x15 0x15 0x15 0 0 0 x x x
0 0 0 0xA0000001 0x15 0x15 0x15 0 0 0 0x00000000 0x00000000 0x00000000
0 1 0 0xA0000002 0x16 0x16 0x16 0 0 0 x x x
C 1 0 0xA0000002 0x16 0x16 0x16 0 0 0 x x x
0 0 0 0xA0000002 0x16 0x16 0x16 0 0 0 0x00000000 0x00000000 0x00000000
0 1 1 0xA0000003 0x17 0x17 0x17 0 0 0 x x x
C 1 1 0xA0000003 0x17 0x17 0x17 0 0 0 x x x
0 0 0 0xA0000003 0x17 0x17 0x17 0 0 0 0xA0000003 0xA0000003 0xA0000003
# 6. Port C follows ADDR_W — read write-target (old value before overwrite)
0 1 1 0xCAFEBABE 0 0 0x2A 0 0 0 x x x
C 1 1 0xCAFEBABE 0 0 0x2A 0 0 0 x x x
0 1 1 0xCAFEBABE 0 0 0x2A 0 0 0 x x x
0 0 0 0x00000000 1 2 0x2A 0 0 0 0x0000ABCD 0x00000000 0xCAFEBABE
# 7. Triple-port simultaneous read (A, B, C via ADDR_W)
0 1 1 0x00000001 0 0 1 0 0 0 x x x
C 1 1 0x00000001 0 0 1 0 0 0 x x x
0 1 1 0x00000001 0 0 1 0 0 0 x x x
0 1 1 0x00000002 0 0 2 0 0 0 x x x
C 1 1 0x00000002 0 0 2 0 0 0 x x x
0 1 1 0x00000002 0 0 2 0 0 0 x x x
0 1 1 0x00000003 0 0 3 0 0 0 x x x
C 1 1 0x00000003 0 0 3 0 0 0 x x x
0 1 1 0x00000003 0 0 3 0 0 0 x x x
0 0 0 0x00000000 1 2 3 0 0 0 0x00000001 0x00000002 0x00000003
# 8. Overwrite same address
0 1 1 0xAAAAAAAA 0 0 5 0 0 0 x x x
C 1 1 0xAAAAAAAA 0 0 5 0 0 0 x x x
0 1 1 0xAAAAAAAA 0 0 5 0 0 0 x x x
0 0 0 0x00000000 5 5 5 0 0 0 0xAAAAAAAA 0xAAAAAAAA 0xAAAAAAAA
0 1 1 0x55555555 0 0 5 0 0 0 x x x
C 1 1 0x55555555 0 0 5 0 0 0 x x x
0 1 1 0x55555555 0 0 5 0 0 0 x x x
0 0 0 0x00000000 5 5 5 0 0 0 0x55555555 0x55555555 0x55555555
# 9. R0 and max index r63
0 1 1 0x00000001 0 0 0 0 0 0 x x x
C 1 1 0x00000001 0 0 0 0 0 0 x x x
0 1 1 0x00000001 0 0 0 0 0 0 x x x
0 0 0 0x00000000 0 0 0 0 0 0 0x00000001 0x00000001 0x00000001
0 1 1 0xFFFFFFFF 0 0 0x3F 0 0 0 x x x
C 1 1 0xFFFFFFFF 0 0 0x3F 0 0 0 x x x
0 1 1 0xFFFFFFFF 0 0 0x3F 0 0 0 x x x
0 0 0 0x00000000 0x3F 0x3F 0x3F 0 0 0 0xFFFFFFFF 0xFFFFFFFF 0xFFFFFFFF
# 10. Read does not require EXEC or WE
0 0 0 0x00000000 3 3 3 0 0 0 0x00000003 0x00000003 0x00000003
# 11. Write ADDR_W independent of read addresses
0 1 1 0x0BADF00D 0 0 0x23 0 0 0 x x x
C 1 1 0x0BADF00D 0 0 0x23 0 0 0 x x x
0 1 1 0x0BADF00D 0 0 0x23 0 0 0 x x x
0 0 0 0x00000000 1 2 0x23 0 0 0 0x00000001 0x00000002 0x0BADF00D
*/

/* Test case regfile-bank:
clk WE EXEC DATA_W ADDR_A ADDR_B ADDR_W BANK_SEL Bank_en addr_c_sel DATA_A DATA_B DATA_C
# Bank latch: BANK_SEL on D, Bank_en posedge; phys addr = {bank,reg}
# bank 0: write r5
0 1 1 0xAAAAA000 0 0 5 0 0 0 x x x
C 1 1 0xAAAAA000 0 0 5 0 0 0 x x x
0 0 0 0 5 5 5 0 0 0 0xAAAAA000 0xAAAAA000 0xAAAAA000
# latch bank=1 (pulse Bank_en)
0 0 0 0 0 0 0 1 0 0 x x x
0 0 0 0 0 0 0 1 1 0 x x x
0 0 0 0 0 0 0 1 0 0 x x x
# bank 1: write r5
0 1 1 0xBBBBB001 0 0 5 0 0 0 x x x
C 1 1 0xBBBBB001 0 0 5 0 0 0 x x x
0 0 0 0 5 5 5 0 0 0 0xBBBBB001 0xBBBBB001 0xBBBBB001
# latch bank=0
0 0 0 0 0 0 0 0 0 0 x x x
0 0 0 0 0 0 0 0 1 0 x x x
0 0 0 0 0 0 0 0 0 0 x x x
# bank 0 r5 still 0xAAAAA000
0 0 0 0 5 5 5 0 0 0 0xAAAAA000 0xAAAAA000 0xAAAAA000
# BANK_SEL=2 with Bank_en=0 — latch stays 0, write r6 in bank 0
0 0 0 0 0 0 0 2 0 0 x x x
0 1 1 0xCCCC0002 0 0 6 0 0 0 x x x
C 1 1 0xCCCC0002 0 0 6 0 0 0 x x x
0 0 0 0 6 6 6 0 0 0 0xCCCC0002 0xCCCC0002 0xCCCC0002
*/
