// Digital circuit shift-mul-control.dig as structural Verilog
module shift_mul_control (
  input  [9:0] op,
  output [1:0] shift_op,
  output mul_div_en,
  output pc_enc
);

  wire [7:4] shift_mul_control_d;

  ROM #(.bigEndian("true"), .AddrBits(10), .Bits(8)) shift_mul_control (
    .A(op), .sel(1'b1), .D({shift_mul_control_d, pc_enc, mul_div_en, shift_op}));

  // Other names for the same wires on the sheet: ir_opcode[9:0] = op

  // Notes on the sheet:
  //   op: default 48
  //   shift_mul_control loads pc_control.hex
endmodule
