// Digital circuit store-mux.dig as structural Verilog
module store_mux (
  input  [31:0] reg_a,
  input  [31:0] alu_out,
  input  [23:0] pc_save,
  input  [31:0] reg_b,
  input  [1:0] mem_sel,
  output [31:0] mem_mux
);

  Multiplexer #(.Selector_Bits(2), .Bits(32)) multiplexer_1 (
    .sel(mem_sel), .in_0(reg_a), .in_1(reg_b), .in_2({{8{1'b0}}, pc_save}), .in_3(alu_out), .out(mem_mux));

  // Other names for the same wires on the sheet: pc_save_24[23:0] = pc_save; pc_save_32[23:0] = pc_save
endmodule
